// Logisim project 658_Computer.circ as structural Verilog
module Motherboard (
  input  in_1,
  input  in_2,
  input  in_3,
  input  in_4,
  input  in_5
);

  wire and_3_out, and_4_out, and_5_out, and_6_out, and_7_out, and_8_out, and_9_out, and_10_out,
       BLIT_0_DONE_IRQ_B, BLIT_2_DONE_IRQ_B, CH_0_RWB, CH_0_RWB_B, CH_1_RWB, CH_1_RWB_B, CH_2_RWB,
       CH_2_RWB_B, CH_3_RWB, CH_3_RWB_B, CLEAR_IRQ_BLIT_0, CLEAR_IRQ_BLIT_2, clock_1_out,
       clock_generator_1_clock_out, device_strobe_1_channel_0_b, device_strobe_1_channel_1_b,
       device_strobe_1_channel_2_b, device_strobe_1_channel_3_b, DONE_IRQ_ENABLE_BLIT_0,
       DONE_IRQ_ENABLE_BLIT_2, DONE_RASTERISING_MPU0_BLIT_0_B, DONE_RASTERISING_MPU0_BLIT_2_B,
       DONE_RASTERISING_MPU1_BLIT_0_B, DONE_RASTERISING_MPU1_BLIT_2_B, DONE_RASTERISING_MPU2_BLIT_0_B,
       DONE_RASTERISING_MPU2_BLIT_2_B, DONE_RASTERISING_MPU3_BLIT_0_B, DONE_RASTERISING_MPU3_BLIT_2_B,
       EIGHT_BIT_MODE_BLIT_0, EIGHT_BIT_MODE_BLIT_2, FST, graphics_board_1_main_memory_valid_b,
       graphics_board_2_main_memory_valid_b, LINE_WIDTH_HIGH_OE_BLIT_0_B, LINE_WIDTH_HIGH_OE_BLIT_2_B,
       LINE_WIDTH_LE_BLIT_0, LINE_WIDTH_LE_BLIT_2, LINE_WIDTH_LOW_OE_BLIT_0_B, LINE_WIDTH_LOW_OE_BLIT_2_B,
       main_memory_gateway_1_memory_oeb_out, main_memory_gateway_1_memory_web_out,
       memory_lockout_and_generator_3_oe_b, memory_lockout_and_generator_3_we_b,
       memory_lockout_and_generator_4_oe_b, memory_lockout_and_generator_4_we_b, MEMORY_LOCKOUT_CHANNEL_0,
       MEMORY_LOCKOUT_CHANNEL_1, MEMORY_LOCKOUT_CHANNEL_2,
       microcontroller_board_kernal_and_user_1_clock_enable_b,
       microcontroller_board_kernal_and_user_1_main_memory_oeb,
       microcontroller_board_kernal_and_user_1_main_memory_valid_b,
       microcontroller_board_kernal_and_user_1_main_memory_web,
       microcontroller_board_kernal_and_user_1_reset, microcontroller_board_kernal_only_1_clock_enable_b,
       microcontroller_board_kernal_only_1_main_memory_oeb,
       microcontroller_board_kernal_only_1_main_memory_valid_b,
       microcontroller_board_kernal_only_1_main_memory_web, microcontroller_board_kernal_only_1_reset,
       MPU0_IRQ_B, MPU0_NMI_B, MPU0_RES_B, MPU1_IRQ_B, MPU1_NMI_B, MPU1_RES_B, MPU2_IRQ_B, MPU2_NMI_B,
       MPU2_RES_B, MPU_0_DEVICE_RWB, MPU_0_DEVICE_VALID_B, MPU_1_DEVICE_RWB, MPU_1_DEVICE_VALID_B,
       NMIB_LOCKOUT_CHANNEL_0, NMIB_LOCKOUT_CHANNEL_1, or_1_out, or_2_out, or_3_out, or_4_out,
       pull_resistor_1_node, pull_resistor_2_node, pull_resistor_3_node, pull_resistor_4_node,
       pull_resistor_23_node, pull_resistor_24_node, pull_resistor_25_node, pull_resistor_26_node,
       pull_resistor_29_node, pull_resistor_30_node, pull_resistor_31_node, pull_resistor_32_node,
       pull_resistor_33_node, pull_resistor_34_node, quick_timing_circuit_1_reset_0_b, RESET, SEL0, SEL2,
       SEL4, SEL6, SLW, START_RASTERISING_BLIT_0, START_RASTERISING_BLIT_2, TRANSPARENCY_TESTING_BLIT_0_B,
       TRANSPARENCY_TESTING_BLIT_2_B;
  wire [1:0] device_null_gateway_1_channel_out, device_null_gateway_2_channel_out,
       device_null_gateway_3_channel_out, MPU_0_DEVICE_CHANNEL, MPU_1_DEVICE_CHANNEL;
  wire [3:0] CH_0_DEVICE_ADDRESS, CH_1_DEVICE_ADDRESS, CH_2_DEVICE_ADDRESS, CH_3_DEVICE_ADDRESS,
       FOUR_BIT_HIGH_NYBBLE_BLIT_0, FOUR_BIT_HIGH_NYBBLE_BLIT_2, MPU_0_DEVICE_ADDRESS, MPU_1_DEVICE_ADDRESS;
  wire [3:2] pull_resistor_12_node, pull_resistor_21_node;
  wire [5:0] CH_0_DEVICE_IDENTIFIER, CH_1_DEVICE_IDENTIFIER, CH_2_DEVICE_IDENTIFIER, CH_3_DEVICE_IDENTIFIER,
       MPU_0_DEVICE_IDENTIFIER, MPU_1_DEVICE_IDENTIFIER;
  wire [7:0] BLIT_0_REMAINING_WIDTH_W0_7, BLIT_2_REMAINING_WIDTH_W0_7, CH_0_D, CH_1_D, CH_2_D, CH_3_D,
       main_memory_gateway_1_d_out_right, microcontroller_board_kernal_and_user_1_main_memory_d_out,
       microcontroller_board_kernal_only_1_main_memory_d_out, MPU_0_ABILITY, MPU_0_DEVICE_D, MPU_1_ABILITY,
       MPU_1_DEVICE_D, MPU_2_ABILITY, n3_to_8_decoder_lvc138_1_p5, n3_to_8_decoder_lvc138_2_p5,
       n3_to_8_decoder_lvc138_3_p5, pull_resistor_27_node, pull_resistor_28_node, TRANSPARENCU_INDEX_BLIT_0,
       TRANSPARENCU_INDEX_BLIT_2;
  wire [7:1] SELECTOR;
  wire [8:1] and_1_out, and_2_out;
  wire [11:0] LINE_WIDTH_BLIT_0, LINE_WIDTH_BLIT_2;
  wire [23:0] DESTINATION_ADDRESS_BLIT_0, DESTINATION_ADDRESS_BLIT_2,
       main_memory_gateway_1_maddress_out_a0_23, memory_lockout_and_generator_3_address_out_a0_23,
       memory_lockout_and_generator_4_address_out_a0_23,
       microcontroller_board_kernal_and_user_1_main_memory_address,
       microcontroller_board_kernal_only_1_main_memory_address, SOURCE_ADDRESS_BLIT_0, SOURCE_ADDRESS_BLIT_2;
  wire [39:0] T1, T2;

  Clock clock_1 (.out(clock_1_out));
  Pull_Resistor #(.pull(1)) pull_resistor_1 (.node(pull_resistor_1_node));
  Pull_Resistor #(.pull(1)) pull_resistor_2 (.node(pull_resistor_2_node));
  Pull_Resistor #(.pull(1)) pull_resistor_3 (.node(pull_resistor_3_node));
  Pull_Resistor #(.pull(1)) pull_resistor_4 (.node(pull_resistor_4_node));
  and and_1 (and_1_out[1], DONE_RASTERISING_MPU0_BLIT_0_B, pull_resistor_1_node, DONE_RASTERISING_MPU0_BLIT_2_B, pull_resistor_2_node);
  and and_2 (and_2_out[1], DONE_RASTERISING_MPU0_BLIT_0_B, pull_resistor_3_node, DONE_RASTERISING_MPU0_BLIT_2_B, pull_resistor_4_node);
  Clock_Generator clock_generator_1 (
    .CLOCK_IN(clock_1_out), .CLOCK_OUT(clock_generator_1_clock_out), .SELECT_HIGH_SPEED_S0_3(4'b0000),
    .RESET(quick_timing_circuit_1_reset_0_b), .SELECT_LOW_SPEED_S0_3(4'b0000));
  Quick_Timing_Circuit quick_timing_circuit_1 (
    .SELECTOR_B({SELECTOR[7], SEL6, SELECTOR[5], SEL4, SELECTOR[3], SEL2, SELECTOR[1], SEL0}), .CLK(FST),
    .RESET_1_B(RESET), .SLOW_SELECTOR(SLW), .CLOCK_IN(clock_generator_1_clock_out),
    .RESET_0_B(quick_timing_circuit_1_reset_0_b), .RESET(in_5));  // open: MULTIPLEXER, COUNTER, CLK_B, HCLK, HCLK_B
  and and_3 (and_3_out, RESET, MPU0_RES_B);
  Pull_Resistor #(.pull(1)) pull_resistor_5 (.node(and_1_out[2]));
  Pull_Resistor #(.pull(1)) pull_resistor_6 (.node(and_1_out[3]));
  Pull_Resistor #(.pull(1)) pull_resistor_7 (.node(and_1_out[4]));
  Pull_Resistor #(.pull(1)) pull_resistor_8 (.node(and_1_out[5]));
  Pull_Resistor #(.pull(1)) pull_resistor_9 (.node(and_1_out[6]));
  Pull_Resistor #(.pull(1)) pull_resistor_10 (.node(and_1_out[7]));
  Pull_Resistor #(.pull(1)) pull_resistor_11 (.node(and_1_out[8]));
  Pull_Resistor #(.pull(1)) pull_resistor_12 (.node(pull_resistor_12_node[2]));
  Pull_Resistor #(.pull(1)) pull_resistor_13 (.node(pull_resistor_12_node[3]));
  and and_4 (and_4_out, RESET, MPU1_RES_B);
  Pull_Resistor #(.pull(1)) pull_resistor_14 (.node(and_2_out[2]));
  Pull_Resistor #(.pull(1)) pull_resistor_15 (.node(and_2_out[3]));
  Pull_Resistor #(.pull(1)) pull_resistor_16 (.node(and_2_out[4]));
  Pull_Resistor #(.pull(1)) pull_resistor_17 (.node(and_2_out[5]));
  Pull_Resistor #(.pull(1)) pull_resistor_18 (.node(and_2_out[6]));
  Pull_Resistor #(.pull(1)) pull_resistor_19 (.node(and_2_out[7]));
  Pull_Resistor #(.pull(1)) pull_resistor_20 (.node(and_2_out[8]));
  Pull_Resistor #(.pull(1)) pull_resistor_21 (.node(pull_resistor_21_node[2]));
  Pull_Resistor #(.pull(1)) pull_resistor_22 (.node(pull_resistor_21_node[3]));
  LED led_1 (.in(microcontroller_board_kernal_only_1_reset));
  LED led_2 (.in(microcontroller_board_kernal_and_user_1_reset));
  Microcontroller_Board_Kernal_Only microcontroller_board_kernal_only_1 (
    .CLOCK_ENABLE_B(microcontroller_board_kernal_only_1_clock_enable_b),
    .DEVICE_CHANNEL(MPU_0_DEVICE_CHANNEL), .IRQ_IN({and_1_out, MPU0_IRQ_B}), .T1(T1),
    .MAIN_MEMORY_ADDRESS(microcontroller_board_kernal_only_1_main_memory_address),
    .MAIN_MEMORY_WEB(microcontroller_board_kernal_only_1_main_memory_web),
    .MAIN_MEMORY_D_IN(microcontroller_board_kernal_only_1_main_memory_d_out),
    .DEVICE_IDENTIFIER(MPU_0_DEVICE_IDENTIFIER),
    .NMI_B_IN({pull_resistor_12_node, NMIB_LOCKOUT_CHANNEL_0, MPU0_NMI_B}), .DEVICE_RWB(MPU_0_DEVICE_RWB),
    .MAIN_MEMORY_LOCKOUT(MEMORY_LOCKOUT_CHANNEL_0), .RESET_1(and_3_out), .MPU_ABILITY(MPU_0_ABILITY),
    .DEVICE_D_IN(MPU_0_DEVICE_D),
    .MAIN_MEMORY_VALID_B(microcontroller_board_kernal_only_1_main_memory_valid_b),
    .DEVICE_ADDRESS(MPU_0_DEVICE_ADDRESS), .DEVICE_D_OUT(MPU_0_DEVICE_D), .FST(FST),
    .MAIN_MEMORY_D_OUT(microcontroller_board_kernal_only_1_main_memory_d_out),
    .RESET(microcontroller_board_kernal_only_1_reset), .DEVICE_VALID_B(MPU_0_DEVICE_VALID_B),
    .SELECTOR({SELECTOR[7], SEL6, SELECTOR[5], SEL4, SELECTOR[3], SEL2, SELECTOR[1], SEL0}), .T2(T2),
    .MAIN_MEMORY_OEB(microcontroller_board_kernal_only_1_main_memory_oeb));
  Microcontroller_Board_Kernal_And_User microcontroller_board_kernal_and_user_1 (
    .DEVICE_RWB(MPU_1_DEVICE_RWB), .DEVICE_ADDRESS(MPU_1_DEVICE_ADDRESS),
    .DEVICE_VALID_B(MPU_1_DEVICE_VALID_B), .DEVICE_D_IN(MPU_1_DEVICE_D),
    .MAIN_MEMORY_VALID_B(microcontroller_board_kernal_and_user_1_main_memory_valid_b),
    .IRQ_B_IN({and_2_out, MPU1_IRQ_B}), .T2(T2),
    .SELECTOR({SELECTOR[1], SEL0, SELECTOR[7], SEL6, SELECTOR[5], SEL4, SELECTOR[3], SEL2}),
    .RESET(microcontroller_board_kernal_and_user_1_reset), .T1(T1), .DEVICE_CHANNEL(MPU_1_DEVICE_CHANNEL),
    .MAIN_MEMORY_ADDRESS(microcontroller_board_kernal_and_user_1_main_memory_address),
    .DEVICE_IDENTIFIER(MPU_1_DEVICE_IDENTIFIER),
    .MAIN_MEMORY_D_IN(microcontroller_board_kernal_and_user_1_main_memory_d_out),
    .DEVICE_D_OUT(MPU_1_DEVICE_D),
    .MAIN_MEMORY_D_OUT(microcontroller_board_kernal_and_user_1_main_memory_d_out),
    .MPU_ABILITY(MPU_1_ABILITY), .FST(FST),
    .CLOCK_ENABLE_B(microcontroller_board_kernal_and_user_1_clock_enable_b),
    .NMI_B_IN({pull_resistor_21_node, NMIB_LOCKOUT_CHANNEL_1, MPU1_NMI_B}),
    .MAIN_MEMORY_OEB(microcontroller_board_kernal_and_user_1_main_memory_oeb),
    .MAIN_MEMORY_LOCKOUT(MEMORY_LOCKOUT_CHANNEL_1),
    .MAIN_MEMORY_WEB(microcontroller_board_kernal_and_user_1_main_memory_web), .RESET_1(and_4_out));
  LED led_3 (.in(microcontroller_board_kernal_only_1_clock_enable_b));
  LED led_4 (.in(microcontroller_board_kernal_and_user_1_clock_enable_b));
  Device_NULL_Gateway device_null_gateway_1 (
    .CHANNEL_DEVICE_VALID_B(MPU_0_DEVICE_VALID_B), .CHANNEL_RWB(MPU_0_DEVICE_RWB),
    .CHANNEL_OUT(device_null_gateway_1_channel_out), .CHANNEL_DEVICE_ADDRESS(MPU_0_DEVICE_ADDRESS),
    .SELECTOR_B(SEL6), .CHANNEL_DEVICE_IDENTIFIER(MPU_0_DEVICE_IDENTIFIER), .CHANNEL_IN(2'b01),
    .CHANNEL_D_IN(MPU_0_DEVICE_D));
  Device_NULL_Gateway device_null_gateway_2 (
    .CHANNEL_DEVICE_VALID_B(MPU_0_DEVICE_VALID_B), .CHANNEL_RWB(MPU_0_DEVICE_RWB),
    .CHANNEL_OUT(device_null_gateway_2_channel_out), .CHANNEL_DEVICE_ADDRESS(MPU_0_DEVICE_ADDRESS),
    .SELECTOR_B(SEL0), .CHANNEL_DEVICE_IDENTIFIER(MPU_0_DEVICE_IDENTIFIER), .CHANNEL_IN(2'b10),
    .CHANNEL_D_IN(MPU_0_DEVICE_D));
  Device_NULL_Gateway device_null_gateway_3 (
    .CHANNEL_DEVICE_VALID_B(MPU_0_DEVICE_VALID_B), .CHANNEL_RWB(MPU_0_DEVICE_RWB),
    .CHANNEL_OUT(device_null_gateway_3_channel_out), .CHANNEL_DEVICE_ADDRESS(MPU_0_DEVICE_ADDRESS),
    .SELECTOR_B(SEL2), .CHANNEL_DEVICE_IDENTIFIER(MPU_0_DEVICE_IDENTIFIER), .CHANNEL_IN(2'b11),
    .CHANNEL_D_IN(MPU_0_DEVICE_D));
  Pull_Resistor #(.pull(1)) pull_resistor_23 (.node(pull_resistor_23_node));
  Pull_Resistor #(.pull(1)) pull_resistor_24 (.node(pull_resistor_24_node));
  Pull_Resistor #(.pull(1)) pull_resistor_25 (.node(pull_resistor_25_node));
  Pull_Resistor #(.pull(1)) pull_resistor_26 (.node(pull_resistor_26_node));
  Graphics_Board graphics_board_1 (
    .D_IN(microcontroller_board_kernal_only_1_main_memory_d_out), .MEMORY_LOCKOUT(MEMORY_LOCKOUT_CHANNEL_0),
    .RESET_B(RESET), .D_OUT(microcontroller_board_kernal_only_1_main_memory_d_out),
    .EIGHT_BIT(EIGHT_BIT_MODE_BLIT_0), .REMAINING_WIDTH_HIGH_OEB(LINE_WIDTH_HIGH_OE_BLIT_0_B),
    .WEB(microcontroller_board_kernal_only_1_main_memory_web), .IRQ_ENABLE(DONE_IRQ_ENABLE_BLIT_0),
    .SOURCE_ADDRESS(SOURCE_ADDRESS_BLIT_0), .DONE_IRQB(BLIT_0_DONE_IRQ_B),
    .ADDRESS_A0_23(microcontroller_board_kernal_only_1_main_memory_address),
    .DESTINATION_ADDRESS(DESTINATION_ADDRESS_BLIT_0), .LINE_WIDTH_0_11(LINE_WIDTH_BLIT_0),
    .LINE_WIDTH_REMAINING_W0_7(BLIT_0_REMAINING_WIDTH_W0_7), .START_RASTERISING(START_RASTERISING_BLIT_0),
    .OEB(microcontroller_board_kernal_only_1_main_memory_oeb),
    .TRANSPARENCY_B(TRANSPARENCY_TESTING_BLIT_0_B), .IRQ_CLEAR(CLEAR_IRQ_BLIT_0),
    .REMAINING_WIDTH_LOW_OEB(LINE_WIDTH_LOW_OE_BLIT_0_B), .HIGH_NYBBLE(FOUR_BIT_HIGH_NYBBLE_BLIT_0),
    .SELECTOR({SELECTOR[7], SEL6, SELECTOR[5], SEL4, SELECTOR[3], SEL2, SELECTOR[1], SEL0}),
    .MAIN_MEMORY_VALID_B(graphics_board_1_main_memory_valid_b),
    .TRANSPARENCY_COLOUR_INDEX(TRANSPARENCU_INDEX_BLIT_0), .REMAINING_WIDTH_LE(LINE_WIDTH_LE_BLIT_0));
  Memory_Lockout_And_Generator memory_lockout_and_generator_1 (
    .SLOW_SELECTOR(SLW), .LOCKOUT(MEMORY_LOCKOUT_CHANNEL_0), .NMI_B(NMIB_LOCKOUT_CHANNEL_0),
    .WE_B(microcontroller_board_kernal_only_1_main_memory_oeb),
    .MAIN_MEMORY_VALID_3_B(pull_resistor_23_node), .GATEWAY_ENABLE_B(SEL6),
    .MAIN_MEMORY_VALID_2_B(graphics_board_1_main_memory_valid_b),
    .ADDRESS_OUT_A0_23(microcontroller_board_kernal_only_1_main_memory_address),
    .MAIN_MEMORY_VALID_1_B(microcontroller_board_kernal_only_1_main_memory_valid_b),
    .OE_B(microcontroller_board_kernal_only_1_main_memory_web), .ADDRESS_IN_A0_23(24'h4aaaaa), .RESET(RESET));
  Graphics_Board graphics_board_2 (
    .D_IN(microcontroller_board_kernal_and_user_1_main_memory_d_out),
    .MEMORY_LOCKOUT(MEMORY_LOCKOUT_CHANNEL_2), .RESET_B(RESET),
    .D_OUT(microcontroller_board_kernal_and_user_1_main_memory_d_out), .EIGHT_BIT(EIGHT_BIT_MODE_BLIT_2),
    .REMAINING_WIDTH_HIGH_OEB(LINE_WIDTH_HIGH_OE_BLIT_2_B),
    .WEB(microcontroller_board_kernal_and_user_1_main_memory_web), .IRQ_ENABLE(DONE_IRQ_ENABLE_BLIT_2),
    .SOURCE_ADDRESS(SOURCE_ADDRESS_BLIT_2), .DONE_IRQB(BLIT_2_DONE_IRQ_B),
    .ADDRESS_A0_23(microcontroller_board_kernal_and_user_1_main_memory_address),
    .DESTINATION_ADDRESS(DESTINATION_ADDRESS_BLIT_2), .LINE_WIDTH_0_11(LINE_WIDTH_BLIT_2),
    .LINE_WIDTH_REMAINING_W0_7(BLIT_2_REMAINING_WIDTH_W0_7), .START_RASTERISING(START_RASTERISING_BLIT_2),
    .OEB(microcontroller_board_kernal_and_user_1_main_memory_oeb),
    .TRANSPARENCY_B(TRANSPARENCY_TESTING_BLIT_2_B), .IRQ_CLEAR(CLEAR_IRQ_BLIT_2),
    .REMAINING_WIDTH_LOW_OEB(LINE_WIDTH_LOW_OE_BLIT_2_B), .HIGH_NYBBLE(FOUR_BIT_HIGH_NYBBLE_BLIT_2),
    .SELECTOR({SELECTOR[3], SEL2, SELECTOR[1], SEL0, SELECTOR[7], SEL6, SELECTOR[5], SEL4}),
    .MAIN_MEMORY_VALID_B(graphics_board_2_main_memory_valid_b),
    .TRANSPARENCY_COLOUR_INDEX(TRANSPARENCU_INDEX_BLIT_2), .REMAINING_WIDTH_LE(LINE_WIDTH_LE_BLIT_2));
  Memory_Lockout_And_Generator memory_lockout_and_generator_2 (
    .SLOW_SELECTOR(SLW), .LOCKOUT(MEMORY_LOCKOUT_CHANNEL_1), .NMI_B(NMIB_LOCKOUT_CHANNEL_1),
    .WE_B(microcontroller_board_kernal_and_user_1_main_memory_oeb),
    .MAIN_MEMORY_VALID_3_B(pull_resistor_24_node), .GATEWAY_ENABLE_B(SEL0),
    .MAIN_MEMORY_VALID_2_B(graphics_board_2_main_memory_valid_b),
    .ADDRESS_OUT_A0_23(microcontroller_board_kernal_and_user_1_main_memory_address),
    .MAIN_MEMORY_VALID_1_B(microcontroller_board_kernal_and_user_1_main_memory_valid_b),
    .OE_B(microcontroller_board_kernal_and_user_1_main_memory_web), .ADDRESS_IN_A0_23(24'h6bbbbb),
    .RESET(RESET));
  Memory_Lockout_And_Generator memory_lockout_and_generator_3 (
    .SLOW_SELECTOR(SLW), .WE_B(memory_lockout_and_generator_3_we_b),
    .MAIN_MEMORY_VALID_3_B(pull_resistor_25_node), .GATEWAY_ENABLE_B(SEL2),
    .MAIN_MEMORY_VALID_2_B(pull_resistor_25_node),
    .ADDRESS_OUT_A0_23(memory_lockout_and_generator_3_address_out_a0_23),
    .MAIN_MEMORY_VALID_1_B(pull_resistor_25_node), .OE_B(memory_lockout_and_generator_3_oe_b),
    .ADDRESS_IN_A0_23(24'h8ccccc), .RESET(RESET));  // open: LOCKOUT, NMI_B
  Memory_Lockout_And_Generator memory_lockout_and_generator_4 (
    .SLOW_SELECTOR(SLW), .WE_B(memory_lockout_and_generator_4_we_b),
    .MAIN_MEMORY_VALID_3_B(pull_resistor_26_node), .GATEWAY_ENABLE_B(SEL4),
    .MAIN_MEMORY_VALID_2_B(pull_resistor_26_node),
    .ADDRESS_OUT_A0_23(memory_lockout_and_generator_4_address_out_a0_23),
    .MAIN_MEMORY_VALID_1_B(pull_resistor_26_node), .OE_B(memory_lockout_and_generator_4_oe_b),
    .ADDRESS_IN_A0_23(24'haddddd), .RESET(RESET));  // open: LOCKOUT, NMI_B
  Device_Strobe device_strobe_1 (
    .Channel_2_B(device_strobe_1_channel_2_b), .DEVICE_0_VALID_B(MPU_0_DEVICE_VALID_B),
    .Channel_3_B(device_strobe_1_channel_3_b), .CHANNEL_1_NUMBER(device_null_gateway_1_channel_out),
    .Channel_0_B(device_strobe_1_channel_0_b), .CHANNEL_0_NUMBER(MPU_0_DEVICE_CHANNEL),
    .DEVICE_1_VALID_B(MPU_0_DEVICE_VALID_B), .SELECTOR_0_B(SEL4), .Channel_1_B(device_strobe_1_channel_1_b),
    .RESET(RESET), .SELECTOR_1_B(SEL6));
  Device_Strobe device_strobe_2 (
    .Channel_2_B(device_strobe_1_channel_2_b), .DEVICE_0_VALID_B(MPU_0_DEVICE_VALID_B),
    .Channel_3_B(device_strobe_1_channel_3_b), .CHANNEL_1_NUMBER(device_null_gateway_3_channel_out),
    .Channel_0_B(device_strobe_1_channel_0_b), .CHANNEL_0_NUMBER(device_null_gateway_2_channel_out),
    .DEVICE_1_VALID_B(MPU_0_DEVICE_VALID_B), .SELECTOR_0_B(SEL0), .Channel_1_B(device_strobe_1_channel_1_b),
    .RESET(RESET), .SELECTOR_1_B(SEL2));
  // Probe on MPU_0_DEVICE_D
  // Probe on MPU_0_DEVICE_D
  // Probe on MPU_0_DEVICE_D
  // Probe on MPU_0_DEVICE_D
  // Probe on BLIT_0_REMAINING_WIDTH_W0_7
  // Probe on BLIT_2_REMAINING_WIDTH_W0_7
  Pull_Resistor #(.pull(1)) pull_resistor_27 (.node(pull_resistor_27_node));
  Pull_Resistor #(.pull(1)) pull_resistor_28 (.node(pull_resistor_28_node));
  Main_Memory_Gateway main_memory_gateway_1 (
    .MEMORY_OEB_IN(microcontroller_board_kernal_only_1_main_memory_oeb),
    .MEMORY_OEB_OUT(main_memory_gateway_1_memory_oeb_out),
    .D_IN_LEFT(microcontroller_board_kernal_only_1_main_memory_d_out),
    .MEMORY_WEB_IN(microcontroller_board_kernal_only_1_main_memory_web), .GATEWAY_ENABLE_B(SEL6),
    .D_IN_RIGHT(main_memory_gateway_1_d_out_right),
    .MADDRESS_OUT_A0_23(main_memory_gateway_1_maddress_out_a0_23),
    .D_OUT_RIGHT(main_memory_gateway_1_d_out_right),
    .ADDRESS_IN_A0_23(microcontroller_board_kernal_only_1_main_memory_address),
    .D_OUT_LEFT(microcontroller_board_kernal_only_1_main_memory_d_out),
    .MEMORY_WEB_OUT(main_memory_gateway_1_memory_web_out));
  Main_Memory_Gateway main_memory_gateway_2 (
    .MEMORY_OEB_IN(microcontroller_board_kernal_and_user_1_main_memory_oeb),
    .MEMORY_OEB_OUT(main_memory_gateway_1_memory_oeb_out),
    .D_IN_LEFT(microcontroller_board_kernal_and_user_1_main_memory_d_out),
    .MEMORY_WEB_IN(microcontroller_board_kernal_and_user_1_main_memory_web), .GATEWAY_ENABLE_B(SEL0),
    .D_IN_RIGHT(main_memory_gateway_1_d_out_right),
    .MADDRESS_OUT_A0_23(main_memory_gateway_1_maddress_out_a0_23),
    .D_OUT_RIGHT(main_memory_gateway_1_d_out_right),
    .ADDRESS_IN_A0_23(microcontroller_board_kernal_and_user_1_main_memory_address),
    .D_OUT_LEFT(microcontroller_board_kernal_and_user_1_main_memory_d_out),
    .MEMORY_WEB_OUT(main_memory_gateway_1_memory_web_out));
  Main_Memory_Gateway main_memory_gateway_3 (
    .MEMORY_OEB_IN(memory_lockout_and_generator_3_we_b),
    .MEMORY_OEB_OUT(main_memory_gateway_1_memory_oeb_out), .D_IN_LEFT(pull_resistor_27_node),
    .MEMORY_WEB_IN(memory_lockout_and_generator_3_oe_b), .GATEWAY_ENABLE_B(SEL2),
    .D_IN_RIGHT(main_memory_gateway_1_d_out_right),
    .MADDRESS_OUT_A0_23(main_memory_gateway_1_maddress_out_a0_23),
    .D_OUT_RIGHT(main_memory_gateway_1_d_out_right),
    .ADDRESS_IN_A0_23(memory_lockout_and_generator_3_address_out_a0_23), .D_OUT_LEFT(pull_resistor_27_node),
    .MEMORY_WEB_OUT(main_memory_gateway_1_memory_web_out));
  Main_Memory_Gateway main_memory_gateway_4 (
    .MEMORY_OEB_IN(memory_lockout_and_generator_4_we_b),
    .MEMORY_OEB_OUT(main_memory_gateway_1_memory_oeb_out), .D_IN_LEFT(pull_resistor_28_node),
    .MEMORY_WEB_IN(memory_lockout_and_generator_4_oe_b), .GATEWAY_ENABLE_B(SEL4),
    .D_IN_RIGHT(main_memory_gateway_1_d_out_right),
    .MADDRESS_OUT_A0_23(main_memory_gateway_1_maddress_out_a0_23),
    .D_OUT_RIGHT(main_memory_gateway_1_d_out_right),
    .ADDRESS_IN_A0_23(memory_lockout_and_generator_4_address_out_a0_23), .D_OUT_LEFT(pull_resistor_28_node),
    .MEMORY_WEB_OUT(main_memory_gateway_1_memory_web_out));
  Device_Channel_Gateway device_channel_gateway_1 (
    .MPU_DEVICE_ADDRESS(MPU_0_DEVICE_ADDRESS), .CHANNEL_RWB(CH_0_RWB), .CHANNEL_RWB_B(CH_0_RWB_B),
    .MPU_DEVICE_IDENTIFIER(MPU_0_DEVICE_IDENTIFIER), .CHANNEL_DEVICE_ADDRESS(CH_0_DEVICE_ADDRESS), .FST(FST),
    .CHANNEL_D_OUT(CH_0_D), .MPU_RWB(MPU_0_DEVICE_RWB), .CHANNEL_DEVICE_IDENTIFIER(CH_0_DEVICE_IDENTIFIER),
    .MPU_D_IN(MPU_0_DEVICE_D), .SELECTOR_B(device_strobe_1_channel_0_b),
    .MPU_DEVICE_VALID_B(MPU_0_DEVICE_VALID_B), .CHANNEL_D_IN(CH_0_D), .MPU_D_OUT(MPU_0_DEVICE_D));
  Device_Channel_Gateway device_channel_gateway_2 (
    .MPU_DEVICE_ADDRESS(MPU_0_DEVICE_ADDRESS), .CHANNEL_RWB(CH_1_RWB), .CHANNEL_RWB_B(CH_1_RWB_B),
    .MPU_DEVICE_IDENTIFIER(MPU_0_DEVICE_IDENTIFIER), .CHANNEL_DEVICE_ADDRESS(CH_1_DEVICE_ADDRESS), .FST(FST),
    .CHANNEL_D_OUT(CH_1_D), .MPU_RWB(MPU_0_DEVICE_RWB), .CHANNEL_DEVICE_IDENTIFIER(CH_1_DEVICE_IDENTIFIER),
    .MPU_D_IN(MPU_0_DEVICE_D), .SELECTOR_B(device_strobe_1_channel_1_b),
    .MPU_DEVICE_VALID_B(MPU_0_DEVICE_VALID_B), .CHANNEL_D_IN(CH_1_D), .MPU_D_OUT(MPU_0_DEVICE_D));
  Device_Channel_Gateway device_channel_gateway_3 (
    .MPU_DEVICE_ADDRESS(MPU_0_DEVICE_ADDRESS), .CHANNEL_RWB(CH_2_RWB), .CHANNEL_RWB_B(CH_2_RWB_B),
    .MPU_DEVICE_IDENTIFIER(MPU_0_DEVICE_IDENTIFIER), .CHANNEL_DEVICE_ADDRESS(CH_2_DEVICE_ADDRESS), .FST(FST),
    .CHANNEL_D_OUT(CH_2_D), .MPU_RWB(MPU_0_DEVICE_RWB), .CHANNEL_DEVICE_IDENTIFIER(CH_2_DEVICE_IDENTIFIER),
    .MPU_D_IN(MPU_0_DEVICE_D), .SELECTOR_B(device_strobe_1_channel_2_b),
    .MPU_DEVICE_VALID_B(MPU_0_DEVICE_VALID_B), .CHANNEL_D_IN(CH_2_D), .MPU_D_OUT(MPU_0_DEVICE_D));
  Device_Channel_Gateway device_channel_gateway_4 (
    .MPU_DEVICE_ADDRESS(MPU_0_DEVICE_ADDRESS), .CHANNEL_RWB(CH_3_RWB), .CHANNEL_RWB_B(CH_3_RWB_B),
    .MPU_DEVICE_IDENTIFIER(MPU_0_DEVICE_IDENTIFIER), .CHANNEL_DEVICE_ADDRESS(CH_3_DEVICE_ADDRESS), .FST(FST),
    .CHANNEL_D_OUT(CH_3_D), .MPU_RWB(MPU_0_DEVICE_RWB), .CHANNEL_DEVICE_IDENTIFIER(CH_3_DEVICE_IDENTIFIER),
    .MPU_D_IN(MPU_0_DEVICE_D), .SELECTOR_B(device_strobe_1_channel_3_b),
    .MPU_DEVICE_VALID_B(MPU_0_DEVICE_VALID_B), .CHANNEL_D_IN(CH_3_D), .MPU_D_OUT(MPU_0_DEVICE_D));
  // Probe on CH_0_D
  // Probe on CH_1_D
  // Probe on CH_2_D
  Pull_Resistor pull_resistor_29 (.node(pull_resistor_29_node));
  Pull_Resistor #(.pull(1)) pull_resistor_30 (.node(pull_resistor_30_node));
  // _3_to_8_Decoder__LVC138 3_to_8_decoder_lvc138_1: pin names not known; wires that end beside it: pull_resistor_29_node, pull_resistor_29_node, main_memory_gateway_1_maddress_out_a0_23[23:21], pull_resistor_30_node, n3_to_8_decoder_lvc138_1_p5
  Pull_Resistor pull_resistor_31 (.node(pull_resistor_31_node));
  Pull_Resistor #(.pull(1)) pull_resistor_32 (.node(pull_resistor_32_node));
  Pull_Resistor pull_resistor_33 (.node(pull_resistor_33_node));
  Pull_Resistor #(.pull(1)) pull_resistor_34 (.node(pull_resistor_34_node));
  // Probe on CH_0_D
  // Probe on CH_1_D
  // Probe on CH_2_D
  // Probe on main_memory_gateway_1_maddress_out_a0_23[20:0]
  // _3_to_8_Decoder__LVC138 3_to_8_decoder_lvc138_2: pin names not known; wires that end beside it: n3_to_8_decoder_lvc138_1_p5[0], pull_resistor_31_node, main_memory_gateway_1_maddress_out_a0_23[20:18], pull_resistor_32_node, n3_to_8_decoder_lvc138_2_p5, n3_to_8_decoder_lvc138_2_p5[0], n3_to_8_decoder_lvc138_2_p5[1]
  // _3_to_8_Decoder__LVC138 3_to_8_decoder_lvc138_3: pin names not known; wires that end beside it: n3_to_8_decoder_lvc138_1_p5[1], pull_resistor_33_node, main_memory_gateway_1_maddress_out_a0_23[20:18], pull_resistor_34_node, n3_to_8_decoder_lvc138_3_p5, n3_to_8_decoder_lvc138_3_p5[7]
  Microcontroller_Device microcontroller_device_1 (
    .CHANNEL_RWB_B(CH_0_RWB_B), .CHANNEL_DEVICE_ADDRESS(CH_0_DEVICE_ADDRESS), .RESET(RESET),
    .MPU_CHANNEL(4'b0000), .NMI_B(MPU0_NMI_B), .RES_B(MPU0_RES_B), .SLOW_SELECTOR(SLW),
    .CHANNEL_DEVICE_IDENTIFIER(CH_0_DEVICE_IDENTIFIER), .CHANNEL_RWB(CH_0_RWB), .MPU_ABILITY(MPU_0_ABILITY),
    .IRQ_B(MPU0_IRQ_B), .D_OUT(CH_0_D), .D_IN(CH_0_D));
  Microcontroller_Device microcontroller_device_2 (
    .CHANNEL_RWB_B(CH_1_RWB_B), .CHANNEL_DEVICE_ADDRESS(CH_1_DEVICE_ADDRESS), .RESET(RESET),
    .MPU_CHANNEL(4'b0001), .NMI_B(MPU1_NMI_B), .RES_B(MPU1_RES_B), .SLOW_SELECTOR(SLW),
    .CHANNEL_DEVICE_IDENTIFIER(CH_1_DEVICE_IDENTIFIER), .CHANNEL_RWB(CH_1_RWB), .MPU_ABILITY(MPU_1_ABILITY),
    .IRQ_B(MPU1_IRQ_B), .D_OUT(CH_1_D), .D_IN(CH_1_D));
  Microcontroller_Device microcontroller_device_3 (
    .CHANNEL_RWB_B(CH_2_RWB_B), .CHANNEL_DEVICE_ADDRESS(CH_2_DEVICE_ADDRESS), .RESET(RESET),
    .MPU_CHANNEL(4'b0010), .NMI_B(MPU2_NMI_B), .RES_B(MPU2_RES_B), .SLOW_SELECTOR(SLW),
    .CHANNEL_DEVICE_IDENTIFIER(CH_2_DEVICE_IDENTIFIER), .CHANNEL_RWB(CH_1_RWB), .MPU_ABILITY(MPU_2_ABILITY),
    .IRQ_B(MPU2_IRQ_B), .D_OUT(CH_2_D), .D_IN(CH_2_D));
  RAM #(.addrWidth(21), .trigger("high"), .databus("bidir"), .\type ("nonvolatile"), .enables("line")) ram_1 (
    .addr(main_memory_gateway_1_maddress_out_a0_23[20:0]), .data(main_memory_gateway_1_d_out_right));  // open: we, oe, clk
  SRAM_Chipifier sram_chipifier_1 (
    .CEB(n3_to_8_decoder_lvc138_1_p5[2]), .OEB(main_memory_gateway_1_memory_oeb_out),
    .WEB(main_memory_gateway_1_memory_web_out));  // open: E, OE, WE
  RAM #(.trigger("high"), .addrWidth(21), .enables("line"), .databus("bidir"), .\type ("nonvolatile")) ram_2 (
    .addr(main_memory_gateway_1_maddress_out_a0_23[20:0]), .data(main_memory_gateway_1_d_out_right));  // open: we, oe, clk
  SRAM_Chipifier sram_chipifier_2 (
    .CEB(n3_to_8_decoder_lvc138_1_p5[3]), .OEB(main_memory_gateway_1_memory_oeb_out),
    .WEB(main_memory_gateway_1_memory_web_out));  // open: E, OE, WE
  RAM #(.trigger("high"), .databus("bidir"), .addrWidth(21), .\type ("nonvolatile"), .enables("line")) ram_3 (
    .addr(main_memory_gateway_1_maddress_out_a0_23[20:0]), .data(main_memory_gateway_1_d_out_right));  // open: we, oe, clk
  SRAM_Chipifier sram_chipifier_3 (
    .CEB(n3_to_8_decoder_lvc138_1_p5[4]), .OEB(main_memory_gateway_1_memory_oeb_out),
    .WEB(main_memory_gateway_1_memory_web_out));  // open: E, OE, WE
  RAM #(.trigger("high"), .addrWidth(21), .enables("line"), .databus("bidir"), .\type ("nonvolatile")) ram_4 (
    .addr(main_memory_gateway_1_maddress_out_a0_23[20:0]), .data(main_memory_gateway_1_d_out_right));  // open: we, oe, clk
  SRAM_Chipifier sram_chipifier_4 (
    .CEB(n3_to_8_decoder_lvc138_1_p5[5]), .OEB(main_memory_gateway_1_memory_oeb_out),
    .WEB(main_memory_gateway_1_memory_web_out));  // open: E, OE, WE
  RAM #(.trigger("high"), .addrWidth(21), .\type ("nonvolatile"), .databus("bidir"), .enables("line")) ram_5 (
    .addr(main_memory_gateway_1_maddress_out_a0_23[20:0]), .data(main_memory_gateway_1_d_out_right));  // open: we, oe, clk
  SRAM_Chipifier sram_chipifier_5 (
    .CEB(n3_to_8_decoder_lvc138_1_p5[6]), .OEB(main_memory_gateway_1_memory_oeb_out),
    .WEB(main_memory_gateway_1_memory_web_out));  // open: E, OE, WE
  RAM #(.databus("bidir"), .enables("line"), .addrWidth(21), .\type ("nonvolatile"), .trigger("high")) ram_6 (
    .addr(main_memory_gateway_1_maddress_out_a0_23[20:0]), .data(main_memory_gateway_1_d_out_right));  // open: we, oe, clk
  SRAM_Chipifier sram_chipifier_6 (
    .CEB(n3_to_8_decoder_lvc138_1_p5[7]), .OEB(main_memory_gateway_1_memory_oeb_out),
    .WEB(main_memory_gateway_1_memory_web_out));  // open: E, OE, WE
  // Probe on main_memory_gateway_1_d_out_right
  // Probe on CH_0_D
  Echo_Device echo_device_1 (
    .CHANNEL_DEVICE_ADDRESS(CH_0_DEVICE_ADDRESS), .D_IN(CH_0_D), .D_OUT(CH_0_D),
    .CHANNEL_DEVICE_IDENTIFIER(CH_0_DEVICE_IDENTIFIER), .CHANNEL_RWB(CH_0_RWB));
  Echo_Device echo_device_2 (
    .CHANNEL_DEVICE_ADDRESS(CH_1_DEVICE_ADDRESS), .D_IN(CH_1_D), .D_OUT(CH_1_D),
    .CHANNEL_DEVICE_IDENTIFIER(CH_1_DEVICE_IDENTIFIER), .CHANNEL_RWB(CH_1_RWB));
  Echo_Device echo_device_3 (
    .CHANNEL_DEVICE_ADDRESS(CH_2_DEVICE_ADDRESS), .D_IN(CH_2_D), .D_OUT(CH_2_D),
    .CHANNEL_DEVICE_IDENTIFIER(CH_2_DEVICE_IDENTIFIER), .CHANNEL_RWB(CH_2_RWB));
  // Helper__W65C816_Timing helper_w65c816_timing_1: pin names not known; wires that end beside it: 4'b0110, 4'b0001, 4'b0110, 4'b0100, 4'b0001, 4'b0101, 4'b0001, 4'b0110, 4'b0010, 4'b0110, T1, 4'b0100, 4'b0000, 4'b0111, 4'b0000, 4'b0011, 4'b0111, 4'b0111, 4'b0000, 4'b0011, 4'b0000, T2
  and and_5 (and_5_out, in_1, in_2);
  and and_6 (and_6_out, in_1, in_3);
  and and_7 (and_7_out, in_1, in_4);
  and and_8 (and_8_out, in_2, in_3);
  and and_9 (and_9_out, in_2, in_4);
  and and_10 (and_10_out, in_3, in_4);
  or or_1 (or_1_out, and_5_out, and_6_out);
  or or_2 (or_2_out, or_1_out, or_3_out, or_4_out);
  or or_3 (or_3_out, and_7_out, and_8_out);
  or or_4 (or_4_out, and_9_out, and_10_out);
  // Probe on CH_0_D
  Graphics_Device graphics_device_1 (
    .START_RASTERISING(START_RASTERISING_BLIT_0), .CHANNEL_RWB_B(CH_0_RWB_B), .CHANNEL_RWB(CH_0_RWB),
    .DONE_IRQB_MPU_0_1_2_3({DONE_RASTERISING_MPU3_BLIT_0_B, DONE_RASTERISING_MPU2_BLIT_0_B, DONE_RASTERISING_MPU1_BLIT_0_B, DONE_RASTERISING_MPU0_BLIT_0_B}),
    .EIGHT_BIT(EIGHT_BIT_MODE_BLIT_0), .REMAINING_WIDTH_LE(LINE_WIDTH_LE_BLIT_0),
    .REMAINING_WIDTH_HIGH_OEB(LINE_WIDTH_HIGH_OE_BLIT_0_B), .D_OUT(CH_0_D),
    .REMAINING_WIDTH_LOW_OEB(LINE_WIDTH_LOW_OE_BLIT_0_B), .PIXEL_HIGH_NYBBLE(FOUR_BIT_HIGH_NYBBLE_BLIT_0),
    .TRANSPARENCY_COLOUR(TRANSPARENCU_INDEX_BLIT_0), .CLEAR_IRQ(CLEAR_IRQ_BLIT_0),
    .DEST_ADDRESS(DESTINATION_ADDRESS_BLIT_0), .DONE_IRQB(BLIT_0_DONE_IRQ_B), .D_IN(CH_0_D),
    .LINE_WIDTH_REMAINING_IN_W0_7(BLIT_0_REMAINING_WIDTH_W0_7), .LINE_WIDTH_W0_11(LINE_WIDTH_BLIT_0),
    .TRANSPARENCY_B(TRANSPARENCY_TESTING_BLIT_0_B), .CHANNEL_DEVICE_ADDRESS(CH_0_DEVICE_ADDRESS),
    .SOURCE_ADDRESS(SOURCE_ADDRESS_BLIT_0), .CHANNEL_DEVICE_IDENTIFIER(CH_0_DEVICE_IDENTIFIER),
    .IRQ_ENABLE(DONE_IRQ_ENABLE_BLIT_0));
  Graphics_Device graphics_device_2 (
    .START_RASTERISING(START_RASTERISING_BLIT_2), .CHANNEL_RWB_B(CH_2_RWB_B), .CHANNEL_RWB(CH_2_RWB),
    .DONE_IRQB_MPU_0_1_2_3({DONE_RASTERISING_MPU3_BLIT_2_B, DONE_RASTERISING_MPU2_BLIT_2_B, DONE_RASTERISING_MPU1_BLIT_2_B, DONE_RASTERISING_MPU0_BLIT_2_B}),
    .EIGHT_BIT(EIGHT_BIT_MODE_BLIT_2), .REMAINING_WIDTH_LE(LINE_WIDTH_LE_BLIT_2),
    .REMAINING_WIDTH_HIGH_OEB(LINE_WIDTH_HIGH_OE_BLIT_2_B), .D_OUT(CH_2_D),
    .REMAINING_WIDTH_LOW_OEB(LINE_WIDTH_LOW_OE_BLIT_2_B), .PIXEL_HIGH_NYBBLE(FOUR_BIT_HIGH_NYBBLE_BLIT_2),
    .TRANSPARENCY_COLOUR(TRANSPARENCU_INDEX_BLIT_2), .CLEAR_IRQ(CLEAR_IRQ_BLIT_2),
    .DEST_ADDRESS(DESTINATION_ADDRESS_BLIT_2), .D_IN(CH_2_D), .LINE_WIDTH_W0_11(LINE_WIDTH_BLIT_2),
    .TRANSPARENCY_B(TRANSPARENCY_TESTING_BLIT_2_B), .CHANNEL_DEVICE_ADDRESS(CH_2_DEVICE_ADDRESS),
    .SOURCE_ADDRESS(SOURCE_ADDRESS_BLIT_2), .CHANNEL_DEVICE_IDENTIFIER(CH_2_DEVICE_IDENTIFIER),
    .IRQ_ENABLE(DONE_IRQ_ENABLE_BLIT_2));  // open: DONE_IRQB, LINE_WIDTH_REMAINING_IN_W0_7

  // Other names for the same wires on the sheet: SELECTOR (some bits) = {SEL6, SEL4, SEL2, SEL0};
  //   SELECTOR_OFFSET_0[7:0] = {SELECTOR[7], SEL6, SELECTOR[5], SEL4, SELECTOR[3], SEL2, SELECTOR[1], SEL0};
  //   SELECTOR_OFFSET_2[7:0] = {SELECTOR[1], SEL0, SELECTOR[7], SEL6, SELECTOR[5], SEL4, SELECTOR[3], SEL2};
  //   SELECTOR_OFFSET_4[7:0] = {SELECTOR[3], SEL2, SELECTOR[1], SEL0, SELECTOR[7], SEL6, SELECTOR[5], SEL4};
  //   SELECTOR_OFFSET_6[7:0] = {SELECTOR[5], SEL4, SELECTOR[3], SEL2, SELECTOR[1], SEL0, SELECTOR[7], SEL6}
endmodule

module Microcontroller_Board_Kernal_Only (
  input  RESET_1,
  input  [7:0] SELECTOR,
  input  FST,
  input  [39:0] T1,
  input  [39:0] T2,
  input  MAIN_MEMORY_LOCKOUT,
  input  [8:0] IRQ_IN,
  input  [3:0] NMI_B_IN,
  input  [7:0] MAIN_MEMORY_D_IN,
  input  [7:0] DEVICE_D_IN,
  output RESET,
  output CLOCK_ENABLE_B,
  output [7:0] MPU_ABILITY,
  output [23:0] MAIN_MEMORY_ADDRESS,
  output MAIN_MEMORY_OEB,
  output MAIN_MEMORY_WEB,
  output [7:0] MAIN_MEMORY_D_OUT,
  output MAIN_MEMORY_VALID_B,
  output [1:0] DEVICE_CHANNEL,
  output DEVICE_VALID_B,
  output [5:0] DEVICE_IDENTIFIER,
  output [3:0] DEVICE_ADDRESS,
  output DEVICE_RWB,
  output [7:0] DEVICE_D_OUT
);

  wire BANK_LATCH, DATA_TRANSMIT_B, DEVICE_STROBE_B, DEVICE_VALID_B_t, FST_t, INTERNAL_MEMORY_VALID, IRQ_B,
       KERNAL_ROM_B, microprocessor_w65c816_1_p6, microprocessor_w65c816_1_p13, microprocessor_w65c816_1_p14,
       microprocessor_w65c816_1_p15, MPU_LOCK_IN, nand_1_out, nand_2_out, NATIVE_MODE, NMI_B, not_1_out,
       not_2_out, not_3_out, OPCODE_ADDRESS, or_1_out, PHI2, pull_resistor_1_node, pull_resistor_2_node,
       pull_resistor_3_node, pull_resistor_6_node, RDY, READ_ENABLE, READ_ENABLE_B, READ_SELECTOR,
       ROM_ADDRESS_VALID, RWB, RWB_B, SA_FLAG_REGISTER_B, SA_INSTRUCTION_COUNTER_0, SA_INSTRUCTION_COUNTER_1,
       SA_INSTRUCTION_COUNTER_2, SA_INSTRUCTION_COUNTER_3, SA_INTERRUPTS_IN_DEPTH_B, SA_USER_PROGRAM_ID_B,
       selector_state_1_sel0, selector_state_1_sel1, selector_state_1_sel2, selector_state_1_sel3,
       selector_state_1_sel4, selector_state_1_sel5, selector_state_1_sel6, selector_state_1_sel7,
       SPECIAL_ADDRESS_VALID_B, STOP_SELECTOR, VPB, WRITE_ENABLE, WRITE_SELECTOR;
  wire [3:0] DEVICE_ADDRESS_t;
  wire [5:0] DEVICE_IDENTIFIER_t;
  wire [7:0] A0_7, A8_15, D, IRAM_A0_7, KERNAL_ROM_data, microprocessor_w65c816_1_p10;
  wire [7:2] flags_register_1_flag_register;
  wire [11:3] address_decode_1_special_memory_selector_b;
  wire [23:16] ADDRESS;

  Pull_Resistor #(.pull(1)) pull_resistor_1 (.node(pull_resistor_1_node));
  Pull_Resistor pull_resistor_2 (.node(pull_resistor_2_node));
  // Probe on {ADDRESS, A8_15, A0_7}
  LED led_1 (.in(selector_state_1_sel0));
  LED led_2 (.in(selector_state_1_sel1));
  LED led_3 (.in(selector_state_1_sel4));
  LED led_4 (.in(selector_state_1_sel2));
  LED led_5 (.in(selector_state_1_sel3));
  Selector_State selector_state_1 (
    .RESET(RESET_1), .PHI2(PHI2), .SEL1(selector_state_1_sel1), .SEL0(selector_state_1_sel0),
    .BOARD_RESET(RESET), .WRITE_SELECTOR(WRITE_SELECTOR), .DEVICE_STROBE_B(DEVICE_STROBE_B),
    .SEL3(selector_state_1_sel3), .BANK_LATCH(BANK_LATCH), .READ_SELECTOR(READ_SELECTOR),
    .CLOCK_ENABLE_B(CLOCK_ENABLE_B), .SEL2(selector_state_1_sel2), .DATA_TRANSMIT_B(DATA_TRANSMIT_B),
    .SEL7(selector_state_1_sel7), .SEL4(selector_state_1_sel4), .SELECTOR(SELECTOR),
    .SEL6(selector_state_1_sel6), .STOP_SELECTOR_B(STOP_SELECTOR), .SEL5(selector_state_1_sel5));  // open: READ_BANK_REMAP_B, MPU_LOCK_IN
  not not_1 (not_1_out, CLOCK_ENABLE_B);
  and and_1 (FST_t, not_1_out, FST);
  Clock_Control clock_control_1 (
    .CLOCK_ENABLE_B(CLOCK_ENABLE_B), .RESET(RESET), .ROM_ADDRESS_VALID(ROM_ADDRESS_VALID), .RWB_B(RWB_B),
    .DEVICE_ADDRESS_VALID_B(DEVICE_VALID_B_t), .UNSTOPPABLE_CLOCK(STOP_SELECTOR));
  Flags_Register flags_register_1 (
    .SA_FLAG_REGISTER_B(SA_FLAG_REGISTER_B), .RESET(RESET), .WRITE_ENABLE_B(READ_ENABLE_B), .D_OUT(D),
    .FLAG_REGISTER({flags_register_1_flag_register, KERNAL_ROM_B, MPU_LOCK_IN}),
    .READ_ENABLE_B(READ_ENABLE_B), .D_IN(D));
  LED led_6 (.in(selector_state_1_sel6));
  LED led_7 (.in(selector_state_1_sel7));
  LED led_8 (.in(selector_state_1_sel5));
  Counter #(.width(32), .max('hffffffff)) counter_1 (.clk(FST_t));  // open: load, D, count, Q, carry, up, clr
  Address_Decode address_decode_1 (
    .SPECIAL_VALID_B(SPECIAL_ADDRESS_VALID_B), .MAIN_MEMORY_VALID_B(MAIN_MEMORY_VALID_B),
    .DEVICE_VALID_B(DEVICE_VALID_B_t), .INTERNAL_MEMORY_VALID(INTERNAL_MEMORY_VALID),
    .DEVICE_CHANNEL(DEVICE_CHANNEL), .KERNAL_ROM_B(KERNAL_ROM_B), .ADDRESS_IN_A0_24({ADDRESS, A8_15, A0_7}),
    .DEVICE_ADDRESS(DEVICE_ADDRESS_t), .RWB(RWB),
    .SPECIAL_MEMORY_SELECTOR_B({SA_INSTRUCTION_COUNTER_3, SA_INSTRUCTION_COUNTER_2, SA_INSTRUCTION_COUNTER_1, SA_INSTRUCTION_COUNTER_0, address_decode_1_special_memory_selector_b, SA_FLAG_REGISTER_B, SA_INTERRUPTS_IN_DEPTH_B, SA_USER_PROGRAM_ID_B}),
    .MPU_LOCK_IN(MPU_LOCK_IN), .ROM_VALID(ROM_ADDRESS_VALID), .KERNAL_MODE(pull_resistor_1_node),
    .KERNAL_MODE_B(pull_resistor_2_node), .DEVICE_IDENTIFIER(DEVICE_IDENTIFIER_t));
  Pull_Resistor #(.pull(1)) pull_resistor_3 (.node(pull_resistor_3_node));
  LED led_9 (.in(INTERNAL_MEMORY_VALID));
  LED led_10 (.in(SPECIAL_ADDRESS_VALID_B));
  LED led_11 (.in(DEVICE_VALID_B_t));
  LED led_12 (.in(ROM_ADDRESS_VALID));
  LED led_13 (.in(MAIN_MEMORY_VALID_B));
  // Microprocessor__W65C816 microprocessor_w65c816_1: pin names not known; wires that end beside it: pull_resistor_3_node, IRQ_B, NMI_B, RESET, PHI2, microprocessor_w65c816_1_p6, T1, T2, {A8_15, A0_7}, microprocessor_w65c816_1_p10, RWB, RDY, microprocessor_w65c816_1_p13, microprocessor_w65c816_1_p14, microprocessor_w65c816_1_p15, FST_t, VPB
  Interrupt_Vectoring interrupt_vectoring_1 (
    .ADDRESS_OUT_A0_7(IRAM_A0_7), .IRQ_4_B(IRQ_IN[4]), .IRQ_1_B(IRQ_IN[1]), .IRQ_B(IRQ_B),
    .NMI_2_B(NMI_B_IN[2]), .ADDRESS_IN_A0_7(A0_7), .NMI_0_B(NMI_B_IN[0]), .NMI_1_B(NMI_B_IN[1]),
    .IRQ_7_B(IRQ_IN[7]), .IRQ_0_B(IRQ_IN[0]), .IRQ_8_B(IRQ_IN[8]), .NMI_3_B(NMI_B_IN[3]),
    .IRQ_5_B(IRQ_IN[5]), .IRQ_6_B(IRQ_IN[6]), .VPB(VPB), .IRQ_3_B(IRQ_IN[3]), .NMI_B(NMI_B),
    .IRQ_2_B(IRQ_IN[2]));
  // Probe on {A8_15, A0_7}
  Pull_Resistor #(.pull(1)) pull_resistor_4 (.node(microprocessor_w65c816_1_p15));
  // Probe on microprocessor_w65c816_1_p10
  Signals signals_1 (
    .BA0_7(ADDRESS), .VPA(microprocessor_w65c816_1_p14), .READ_SELECTOR(READ_SELECTOR),
    .CLOCK_ENABLE_B(CLOCK_ENABLE_B), .BANK_LATCH(BANK_LATCH), .OPCODE_ADDRESS(OPCODE_ADDRESS),
    .D(microprocessor_w65c816_1_p10), .RWB(RWB), .READ_ENABLE_B(READ_ENABLE_B), .NATIVE_MODE(NATIVE_MODE),
    .READ_ENABLE(READ_ENABLE), .WRITE_SELECTOR(WRITE_SELECTOR), .RWB_B(RWB_B),
    .VDA(microprocessor_w65c816_1_p13), .E(microprocessor_w65c816_1_p6), .WRITE_ENABLE(WRITE_ENABLE));  // open: WRITE_ENABLE_B
  // _8_bit_Bus_Transceiver__LVC4245 8_bit_bus_transceiver_lvc4245_1: pin names not known; wires that end beside it: DATA_TRANSMIT_B, microprocessor_w65c816_1_p10, RWB, D
  // Probe on {ADDRESS[16], A8_15, IRAM_A0_7}
  nand nand_1 (nand_1_out, INTERNAL_MEMORY_VALID, READ_ENABLE);
  nand nand_2 (nand_2_out, INTERNAL_MEMORY_VALID, WRITE_ENABLE);
  not not_2 (not_2_out, ROM_ADDRESS_VALID);
  or or_1 (or_1_out, not_2_out, READ_ENABLE_B);
  Pull_Resistor pull_resistor_5 (.node({A8_15, A0_7}));
  RAM #(.addrWidth(17), .databus("bidir"), .trigger("high"), .enables("line"), .\type ("nonvolatile")) INTERNAL_MEMORY (
    .addr({ADDRESS[16], A8_15, IRAM_A0_7}), .data(D));  // open: we, oe, clk
  LED led_14 (.in(nand_1_out));
  SRAM_Chipifier sram_chipifier_1 (.CEB(pull_resistor_6_node), .OEB(nand_1_out), .WEB(nand_2_out));  // open: E, OE, WE
  LED led_15 (.in(nand_2_out));
  Pull_Resistor pull_resistor_6 (.node(pull_resistor_6_node));
  // Probe on {A8_15[6:0], IRAM_A0_7}
  ROM #(.addrWidth(16)) KERNAL_ROM (.addr({1'b1, A8_15[6:0], IRAM_A0_7}), .data(KERNAL_ROM_data));
  LED led_16 (.in(or_1_out));
  not not_3 (not_3_out, or_1_out);
  Pull_Resistor pull_resistor_7 (.node(D));
  // Probe on {ADDRESS, A8_15, A0_7}
  // Probe on D
  // Probe on D
  // Probe on D
  assign D = not_3_out ? KERNAL_ROM_data : 8'bz;  // Controlled_Buffer controlled_buffer_1
  Pull_Resistor pull_resistor_8 (.node(MPU_ABILITY[0]));
  Pull_Resistor pull_resistor_9 (.node(MPU_ABILITY[7]));
  Device_MPU_Gateway device_mpu_gateway_1 (
    .MPU_DEVICE_VALID_B(DEVICE_VALID_B_t), .CHANNEL_RWB(DEVICE_RWB), .MPU_D_OUT(D), .MPU_D_IN(D),
    .CHANNEL_D_IN(DEVICE_D_IN), .CHANNEL_DEVICE_VALID_B(DEVICE_VALID_B),
    .CHANNEL_DEVICE_IDENTIFIER(DEVICE_IDENTIFIER), .MPU_0_DEVICE_IDENTIFIER(DEVICE_IDENTIFIER_t),
    .CHANNEL_DEVICE_ADDRESS(DEVICE_ADDRESS), .SELECTOR_B(DEVICE_STROBE_B),
    .MPU_0_DEVICE_ADDRESS(DEVICE_ADDRESS_t), .MPU_RWB(RWB), .CHANNEL_D_OUT(DEVICE_D_OUT));
  Memory_Transceiver memory_transceiver_1 (
    .MPU_D_IN(D), .WE_B(MAIN_MEMORY_WEB), .MAIN_MEMORY_D_OUT(MAIN_MEMORY_D_OUT), .RWB(RWB),
    .MEMORY_LOCKOUT(MAIN_MEMORY_LOCKOUT), .RWB_B(RWB_B), .ADDRESS_OUT_A0_23(MAIN_MEMORY_ADDRESS),
    .ADDRESS_IN_A0_23({ADDRESS, A8_15, A0_7}), .MAIN_MEMORY_VALID_B(MAIN_MEMORY_VALID_B),
    .MAIN_MEMORY_D_IN(MAIN_MEMORY_D_IN), .OE_B(MAIN_MEMORY_OEB), .MPU_D_OUT(D));

  assign MPU_ABILITY[6:1] = {6{MPU_ABILITY[7]}};

  // Other names for the same wires on the sheet: ADDRESS[15:0] = {A8_15, A0_7}; BA0_7[7:0] = ADDRESS;
  //   ABILITY_USER_MODE = MPU_ABILITY[0]; WRITE_ENABLE_B = READ_ENABLE_B

  // Notes on the sheet:
  //   contents of KERNAL_ROM (hex, n*v repeats v):
  //   16384*0 ad fc ff c9 2b e1 f0 2 0 0 e2 20 a9 a4 8d 12 70 a9 cc ad 12 70 1a 8d 12 70 a9 cc ad 12 70 c9
  //   a5 f0 2 0 0 a2 ef cd 9b ae c 6f ac e 6f a9 ff 8d 0 6f a9 42 8f 0 ff 1 a9 43 8f 1 ff 1 a9 0 48 a9 4
  //   48 a9 1c 48 8 40 41184*ff 18 fb c2 30 a9 ff 1 1b e2 20 a9 0 48 ab c2 20 5c 0 40 0 8b b c2 30 48 da
  //   5a 80 39 8b b c2 30 48 da 5a 80 30 8b b c2 30 48 da 5a 80 27 8b b c2 30 48 da 5a e2 20 a9 0 48 ab ae
  //   c 6f ac e 6f 80 12 8b b c2 30 48 da 5a 80 9 8b b c2 30 48 da 5a 80 0 c2 30 7a fa 68 2b ab 40 7771*ff
  //   5a e1 6f e1 51 e1 48 e1 0 0 3f e1 4*ff 78 e1 0 0 78 e1 78 e1 2b e1 78 e1
  //   32KB_ROM
endmodule

module Microcontroller_Board_Kernal_And_User (
  input  RESET_1,
  input  [7:0] SELECTOR,
  input  FST,
  input  [39:0] T1,
  input  [39:0] T2,
  input  MAIN_MEMORY_LOCKOUT,
  input  [8:0] IRQ_B_IN,
  input  [3:0] NMI_B_IN,
  input  [7:0] MAIN_MEMORY_D_IN,
  input  [7:0] DEVICE_D_IN,
  output [7:0] MPU_ABILITY,
  output RESET,
  output CLOCK_ENABLE_B,
  output [23:0] MAIN_MEMORY_ADDRESS,
  output MAIN_MEMORY_OEB,
  output MAIN_MEMORY_WEB,
  output [7:0] MAIN_MEMORY_D_OUT,
  output MAIN_MEMORY_VALID_B,
  output [1:0] DEVICE_CHANNEL,
  output DEVICE_VALID_B,
  output [5:0] DEVICE_IDENTIFIER,
  output [3:0] DEVICE_ADDRESS,
  output DEVICE_RWB,
  output [7:0] DEVICE_D_OUT
);

  wire BANK_LATCH, DATA_TRANSMIT_B, DEVICE_STROBE_B, DEVICE_VALID_B_t, ENTER_INTERRUPT, EXIT_INTERRUPT,
       FST_t, INTERNAL_MEMORY_VALID, IRQ_B, KERNAL_MODE, KERNAL_MODE_B, KERNAL_ROM_B, LOCK_IN_B,
       microprocessor_w65c816_1_p6, microprocessor_w65c816_1_p13, microprocessor_w65c816_1_p14,
       microprocessor_w65c816_1_p15, MPU_LOCK_IN, NATIVE_MODE, NMI_B, not_1_out, not_2_out, not_3_out,
       not_4_out, not_5_out, OPCODE_ADDRESS, or_1_out, PHI2, pull_resistor_1_node, RDY, READ_BANK_REMAP_B,
       READ_ENABLE, READ_ENABLE_B, READ_SELECTOR, ROM_ADDRESS_VALID, RWB, RWB_B, SA_FLAG_REGISTER_B,
       SA_INSTRUCTION_COUNTER_0, SA_INSTRUCTION_COUNTER_1, SA_INSTRUCTION_COUNTER_2,
       SA_INSTRUCTION_COUNTER_3, SA_INTERRUPTS_IN_DEPTH_B, SA_USER_PROGRAM_ID_B, selector_state_1_sel0,
       selector_state_1_sel1, selector_state_1_sel2, selector_state_1_sel3, selector_state_1_sel4,
       selector_state_1_sel5, selector_state_1_sel6, selector_state_1_sel7, SPECIAL_ADDRESS_VALID_B,
       STOP_SELECTOR, user_mode_memory_glue_1_ceb, user_mode_memory_glue_1_oeb, user_mode_memory_glue_1_web,
       VPB, WRITE_ENABLE, WRITE_SELECTOR;
  wire [3:0] DEVICE_ADDRESS_t;
  wire [5:0] DEVICE_IDENTIFIER_t;
  wire [7:0] A0_7, A8_15, D, interrupt_detection_1_opcode, IRAM_A0_7, KERNAL_ROM_data,
       kernal_user_mode_1_interrupt_depth, microprocessor_w65c816_1_p10, MRAM_A16_23, USER_PROGRAM_ID;
  wire [7:2] flags_register_1_flag_register;
  wire [11:3] address_decode_1_special_memory_selector_b;
  wire [16:0] user_mode_memory_glue_1_address_out_a0_16;
  wire [23:16] ADDRESS;
  wire [31:0] instruction_counter_1_count;

  // Probe on {ADDRESS, A8_15, A0_7}
  LED led_1 (.in(selector_state_1_sel0));
  LED led_2 (.in(selector_state_1_sel1));
  LED led_3 (.in(selector_state_1_sel3));
  LED led_4 (.in(selector_state_1_sel4));
  LED led_5 (.in(selector_state_1_sel2));
  Selector_State selector_state_1 (
    .RESET(RESET_1), .PHI2(PHI2), .SEL1(selector_state_1_sel1), .SEL0(selector_state_1_sel0),
    .BOARD_RESET(RESET), .WRITE_SELECTOR(WRITE_SELECTOR), .DEVICE_STROBE_B(DEVICE_STROBE_B),
    .SEL3(selector_state_1_sel3), .BANK_LATCH(BANK_LATCH), .READ_SELECTOR(READ_SELECTOR),
    .CLOCK_ENABLE_B(CLOCK_ENABLE_B), .SEL2(selector_state_1_sel2), .READ_BANK_REMAP_B(READ_BANK_REMAP_B),
    .DATA_TRANSMIT_B(DATA_TRANSMIT_B), .SEL7(selector_state_1_sel7), .SEL4(selector_state_1_sel4),
    .SELECTOR(SELECTOR), .SEL6(selector_state_1_sel6), .STOP_SELECTOR_B(STOP_SELECTOR),
    .SEL5(selector_state_1_sel5));  // open: MPU_LOCK_IN
  not not_1 (not_1_out, CLOCK_ENABLE_B);
  and and_1 (FST_t, not_1_out, FST);
  Interrupt_Vectoring interrupt_vectoring_1 (
    .ADDRESS_OUT_A0_7(IRAM_A0_7), .IRQ_4_B(IRQ_B_IN[4]), .IRQ_1_B(IRQ_B_IN[1]), .IRQ_B(IRQ_B),
    .NMI_2_B(NMI_B_IN[2]), .ADDRESS_IN_A0_7(A0_7), .NMI_0_B(NMI_B_IN[0]), .NMI_1_B(NMI_B_IN[1]),
    .IRQ_7_B(IRQ_B_IN[7]), .IRQ_0_B(IRQ_B_IN[0]), .IRQ_8_B(IRQ_B_IN[8]), .NMI_3_B(NMI_B_IN[3]),
    .IRQ_5_B(IRQ_B_IN[5]), .IRQ_6_B(IRQ_B_IN[6]), .VPB(VPB), .IRQ_3_B(IRQ_B_IN[3]), .NMI_B(NMI_B),
    .IRQ_2_B(IRQ_B_IN[2]));
  Flags_Register flags_register_1 (
    .SA_FLAG_REGISTER_B(SA_FLAG_REGISTER_B), .RESET(RESET), .WRITE_ENABLE_B(READ_ENABLE_B), .D_OUT(D),
    .FLAG_REGISTER({flags_register_1_flag_register, KERNAL_ROM_B, LOCK_IN_B}), .READ_ENABLE_B(READ_ENABLE_B),
    .D_IN(D));
  Address_Decode address_decode_1 (
    .SPECIAL_VALID_B(SPECIAL_ADDRESS_VALID_B), .MAIN_MEMORY_VALID_B(MAIN_MEMORY_VALID_B),
    .DEVICE_VALID_B(DEVICE_VALID_B_t), .INTERNAL_MEMORY_VALID(INTERNAL_MEMORY_VALID),
    .DEVICE_CHANNEL(DEVICE_CHANNEL), .KERNAL_ROM_B(KERNAL_ROM_B), .ADDRESS_IN_A0_24({ADDRESS, A8_15, A0_7}),
    .DEVICE_ADDRESS(DEVICE_ADDRESS_t), .RWB(RWB),
    .SPECIAL_MEMORY_SELECTOR_B({SA_INSTRUCTION_COUNTER_3, SA_INSTRUCTION_COUNTER_2, SA_INSTRUCTION_COUNTER_1, SA_INSTRUCTION_COUNTER_0, address_decode_1_special_memory_selector_b, SA_FLAG_REGISTER_B, SA_INTERRUPTS_IN_DEPTH_B, SA_USER_PROGRAM_ID_B}),
    .MPU_LOCK_IN(MPU_LOCK_IN), .ROM_VALID(ROM_ADDRESS_VALID), .KERNAL_MODE(KERNAL_MODE),
    .KERNAL_MODE_B(KERNAL_MODE_B), .DEVICE_IDENTIFIER(DEVICE_IDENTIFIER_t));
  LED led_6 (.in(selector_state_1_sel5));
  LED led_7 (.in(selector_state_1_sel6));
  LED led_8 (.in(selector_state_1_sel7));
  Counter #(.max('hffffffff), .width(32)) counter_1 (.clk(FST_t));  // open: load, D, count, Q, carry, up, clr
  Pull_Resistor #(.pull(1)) pull_resistor_1 (.node(pull_resistor_1_node));
  LED led_9 (.in(INTERNAL_MEMORY_VALID));
  LED led_10 (.in(SPECIAL_ADDRESS_VALID_B));
  LED led_11 (.in(DEVICE_VALID_B_t));
  LED led_12 (.in(ROM_ADDRESS_VALID));
  LED led_13 (.in(MAIN_MEMORY_VALID_B));
  // Microprocessor__W65C816 microprocessor_w65c816_1: pin names not known; wires that end beside it: pull_resistor_1_node, IRQ_B, NMI_B, RESET, PHI2, microprocessor_w65c816_1_p6, T1, T2, {A8_15, A0_7}, microprocessor_w65c816_1_p10, RWB, RDY, microprocessor_w65c816_1_p13, microprocessor_w65c816_1_p14, microprocessor_w65c816_1_p15, FST_t, VPB
  // Probe on {ADDRESS, A8_15, IRAM_A0_7}
  Clock_Control clock_control_1 (
    .CLOCK_ENABLE_B(CLOCK_ENABLE_B), .RESET(RESET), .ROM_ADDRESS_VALID(ROM_ADDRESS_VALID), .RWB_B(RWB_B),
    .DEVICE_ADDRESS_VALID_B(DEVICE_VALID_B_t), .UNSTOPPABLE_CLOCK(STOP_SELECTOR));
  // Probe on {A8_15, A0_7}
  Pull_Resistor #(.pull(1)) pull_resistor_2 (.node(microprocessor_w65c816_1_p15));
  User_Mode_Memory_Glue user_mode_memory_glue_1 (
    .WRITE_ENABLE(WRITE_ENABLE), .OEB(user_mode_memory_glue_1_oeb), .READ_BANK_REMAP_B(READ_BANK_REMAP_B),
    .ADDRESS_OUT_A0_16(user_mode_memory_glue_1_address_out_a0_16), .USER_BANK(USER_PROGRAM_ID),
    .READ_ENABLE(READ_ENABLE), .ADDRESS_IN_A0_23({ADDRESS, A8_15, IRAM_A0_7}),
    .WEB(user_mode_memory_glue_1_web), .CEB(user_mode_memory_glue_1_ceb),
    .INTERNAL_MEMORY_VALID(INTERNAL_MEMORY_VALID));
  not not_2 (not_2_out, PHI2);
  // Probe on microprocessor_w65c816_1_p10
  not not_3 (not_3_out, PHI2);
  // Probe on D
  // Probe on user_mode_memory_glue_1_address_out_a0_16
  RAM #(.databus("bidir"), .addrWidth(17), .trigger("high"), .\type ("nonvolatile"), .enables("line")) INTERNAL_MEMORY (
    .addr(user_mode_memory_glue_1_address_out_a0_16), .data(D));  // open: we, oe, clk
  LED led_14 (.in(user_mode_memory_glue_1_oeb));
  SRAM_Chipifier sram_chipifier_1 (
    .CEB(user_mode_memory_glue_1_ceb), .OEB(user_mode_memory_glue_1_oeb), .WEB(user_mode_memory_glue_1_web));  // open: E, OE, WE
  LED led_15 (.in(user_mode_memory_glue_1_web));
  LED led_16 (.in(user_mode_memory_glue_1_ceb));
  Interrupt_Detection interrupt_detection_1 (
    .RESET_B(RESET), .LATCH_D(WRITE_SELECTOR), .RETURN_FROM_INTERRUPT(EXIT_INTERRUPT),
    .OPCODE(interrupt_detection_1_opcode), .ENTER_INTERRUPT(ENTER_INTERRUPT), .D(D),
    .OPCODE_ADDRESS(OPCODE_ADDRESS), .NATIVE_MODE(NATIVE_MODE), .ADDRESS_IN_A0(A0_7[0]), .PHI2_B(not_2_out));
  Signals signals_1 (
    .BA0_7(ADDRESS), .VPA(microprocessor_w65c816_1_p14), .READ_SELECTOR(READ_SELECTOR),
    .CLOCK_ENABLE_B(CLOCK_ENABLE_B), .BANK_LATCH(BANK_LATCH), .OPCODE_ADDRESS(OPCODE_ADDRESS),
    .D(microprocessor_w65c816_1_p10), .RWB(RWB), .READ_ENABLE_B(READ_ENABLE_B), .NATIVE_MODE(NATIVE_MODE),
    .READ_ENABLE(READ_ENABLE), .WRITE_SELECTOR(WRITE_SELECTOR), .RWB_B(RWB_B),
    .VDA(microprocessor_w65c816_1_p13), .E(microprocessor_w65c816_1_p6), .WRITE_ENABLE(WRITE_ENABLE));  // open: WRITE_ENABLE_B
  not not_4 (not_4_out, ROM_ADDRESS_VALID);
  Instruction_Counter instruction_counter_1 (
    .RESET(RESET), .READ_ENABLE_B(READ_ENABLE_B), .A0(A0_7[0]), .OEB_C8_15(SA_INSTRUCTION_COUNTER_1),
    .PHI2_B(not_3_out), .D_OUT(D), .OEB_C0_7(SA_INSTRUCTION_COUNTER_0),
    .OEB_C24_31(SA_INSTRUCTION_COUNTER_3), .OEB_C16_23(SA_INSTRUCTION_COUNTER_2),
    .COUNT(instruction_counter_1_count), .OPCODE_ADDRESS(OPCODE_ADDRESS));
  // _8_bit_Bus_Transceiver__LVC4245 8_bit_bus_transceiver_lvc4245_1: pin names not known; wires that end beside it: DATA_TRANSMIT_B, microprocessor_w65c816_1_p10, RWB, D
  // Probe on {A8_15[6:0], IRAM_A0_7}
  LED led_17 (.in(or_1_out));
  or or_1 (or_1_out, not_4_out, READ_ENABLE_B);
  // Probe on interrupt_detection_1_opcode
  Pull_Resistor pull_resistor_3 (.node({A8_15, A0_7}));
  ROM #(.addrWidth(16)) KERNAL_ROM (.addr({1'b1, A8_15[6:0], IRAM_A0_7}), .data(KERNAL_ROM_data));
  not not_5 (not_5_out, or_1_out);
  // Probe on instruction_counter_1_count
  Pull_Resistor pull_resistor_4 (.node(D));
  // Probe on D
  // Probe on {ADDRESS, A8_15, A0_7}
  // Probe on D
  assign D = not_5_out ? KERNAL_ROM_data : 8'bz;  // Controlled_Buffer controlled_buffer_1
  // Probe on D
  Kernal_User_Mode kernal_user_mode_1 (
    .D_IN(D), .USER_MODE_ABILITY(MPU_ABILITY[0]), .D_OUT(D), .RESET(RESET),
    .INTERRUPT_DEPTH(kernal_user_mode_1_interrupt_depth), .ENTER_INTERRUPT(ENTER_INTERRUPT),
    .KERNAL_MODE(KERNAL_MODE), .SA_INTERRUPTS_IN_DEPTH_B(SA_INTERRUPTS_IN_DEPTH_B), .USER(USER_PROGRAM_ID),
    .READ_ENABLE_B(READ_ENABLE_B), .KERNAL_MODE_B(KERNAL_MODE_B), .MAIN_MEMORY_BA0_7(MRAM_A16_23),
    .EXIT_INTERRUPT(EXIT_INTERRUPT), .BA0_7(ADDRESS), .WRITE_ENABLE_B(READ_ENABLE_B),
    .SA_USER_PROGRAM_ID_B(SA_USER_PROGRAM_ID_B), .READ_BANK_REMAP_B(READ_BANK_REMAP_B));
  Pull_Resistor pull_resistor_5 (.node(MPU_ABILITY[7]));
  Device_MPU_Gateway device_mpu_gateway_1 (
    .MPU_DEVICE_VALID_B(DEVICE_VALID_B_t), .CHANNEL_RWB(DEVICE_RWB), .MPU_D_OUT(D), .MPU_D_IN(D),
    .CHANNEL_D_IN(DEVICE_D_IN), .CHANNEL_DEVICE_VALID_B(DEVICE_VALID_B),
    .CHANNEL_DEVICE_IDENTIFIER(DEVICE_IDENTIFIER), .MPU_0_DEVICE_IDENTIFIER(DEVICE_IDENTIFIER_t),
    .CHANNEL_DEVICE_ADDRESS(DEVICE_ADDRESS), .SELECTOR_B(DEVICE_STROBE_B),
    .MPU_0_DEVICE_ADDRESS(DEVICE_ADDRESS_t), .MPU_RWB(RWB), .CHANNEL_D_OUT(DEVICE_D_OUT));
  Memory_Transceiver memory_transceiver_1 (
    .MPU_D_IN(D), .WE_B(MAIN_MEMORY_WEB), .MAIN_MEMORY_D_OUT(MAIN_MEMORY_D_OUT), .RWB(RWB),
    .MEMORY_LOCKOUT(MAIN_MEMORY_LOCKOUT), .RWB_B(RWB_B), .ADDRESS_OUT_A0_23(MAIN_MEMORY_ADDRESS),
    .ADDRESS_IN_A0_23({ADDRESS, A8_15, A0_7}), .MAIN_MEMORY_VALID_B(MAIN_MEMORY_VALID_B),
    .MAIN_MEMORY_D_IN(MAIN_MEMORY_D_IN), .OE_B(MAIN_MEMORY_OEB), .MPU_D_OUT(D));
  // Probe on USER_PROGRAM_ID
  // Probe on MRAM_A16_23
  // Probe on kernal_user_mode_1_interrupt_depth

  assign MPU_ABILITY[6:1] = {6{MPU_ABILITY[7]}};

  // Other names for the same wires on the sheet: ADDRESS[15:0] = {A8_15, A0_7}; BA0_7[7:0] = ADDRESS;
  //   ABILITY_USER_MODE = MPU_ABILITY[0]; WRITE_ENABLE_B = READ_ENABLE_B

  // Notes on the sheet:
  //   contents of KERNAL_ROM (hex, n*v repeats v):
  //   16384*0 ad fc ff c9 2b e1 f0 2 0 0 e2 20 a9 a4 8d 12 70 a9 cc ad 12 70 1a 8d 12 70 a9 cc ad 12 70 c9
  //   a5 f0 2 0 0 a2 ef cd 9b ae c 6f ac e 6f a9 ff 8d 0 6f a9 42 8f 0 ff 1 a9 43 8f 1 ff 1 a9 0 48 a9 4
  //   48 a9 1c 48 8 40 41184*ff 18 fb c2 30 a9 ff 1 1b e2 20 a9 0 48 ab c2 20 5c 0 40 0 8b b c2 30 48 da
  //   5a 80 39 8b b c2 30 48 da 5a 80 30 8b b c2 30 48 da 5a 80 27 8b b c2 30 48 da 5a e2 20 a9 0 48 ab ae
  //   c 6f ac e 6f 80 12 8b b c2 30 48 da 5a 80 9 8b b c2 30 48 da 5a 80 0 c2 30 7a fa 68 2b ab 40 7771*ff
  //   5a e1 6f e1 51 e1 48 e1 0 0 3f e1 4*ff 78 e1 0 0 78 e1 78 e1 2b e1 78 e1
  //   32KB_ROM
endmodule

module Video_Board (
  input  [7:0] PALETTE_INDEX,
  input  MAIN_MEMORY_0_B,
  input  MAIN_MEMORY_1_B,
  input  MAIN_MEMORY_2_B,
  input  [17:0] ADDRESS,
  input  OEB,
  input  WEB,
  input  RESET_B,
  input  [1:0] PIXEL_DOUBLING_X,
  input  FRAME_BUFFER,
  input  IRQ_ENABLE,
  input  [7:0] HACTIVE_D4_11,
  input  [7:0] H_FRONT_PORCH_D4_11,
  input  [7:0] H_SYNC_D4_11,
  input  [7:0] H_BACK_PORCH_D4_11,
  input  [7:0] V_ACTIVE_D4_11,
  input  [7:0] V_FRONT_PORCH_D0_7,
  input  [7:0] V_SYNC_D0_7,
  input  [7:0] V_BACK_PORCH_D0_7,
  input  VERTICAL_RASTER_LE,
  input  VERTICAL_RASTER_HIGH_OEB,
  input  VERTICAL_RASTER_LOW_OEB,
  input  [7:0] CLOCK_D8_15,
  input  [7:0] CLOCK_D0_7,
  input  CLEAR_IRQ,
  output [7:0] RED,
  output [7:0] GREEN,
  output [7:0] BLUE,
  output H_SYNC,
  output VSYNC,
  output IRQ_B,
  output [7:0] V_D0_7
);

  wire not_1_out, or_1_out, or_2_out, pull_resistor_1_node, undriven, video_address_1_frame_memory_0_b,
       video_address_1_frame_memory_1_b, video_address_1_frame_memory_2_b,
       video_horizontal_signal_1_h_pixel_valid, video_horizontal_signal_1_h_pixel_valid_b,
       video_horizontal_signal_1_h_sync_pulse, video_horizontal_signal_1_v_clock,
       video_vertical_signal_1_v_pixel_valid, video_vertical_signal_1_v_pixel_valid_b,
       video_vertical_signal_1_v_sync_pulse;
  wire [7:0] video_memory_1_d_out, video_memory_1_palette_d0_7, video_memory_1_pixel_d0_7,
       video_palette_1_d_out;
  wire [17:0] video_address_1_frame_buffer_a0_17;

  Video_Address video_address_1 (
    .START_FRAME_B(or_1_out), .FRAME_MEMORY_0_B(video_address_1_frame_memory_0_b),
    .PIXEL_DOUBLING_X(PIXEL_DOUBLING_X), .FRAME_MEMORY_1_B(video_address_1_frame_memory_1_b),
    .CLOCK(undriven), .FRAME_MEMORY_2_B(video_address_1_frame_memory_2_b), .RESET_B(RESET_B),
    .FRAME_BUFFER_A0_17(video_address_1_frame_buffer_a0_17));
  Video_Horizontal_Signal video_horizontal_signal_1 (
    .H_BACK_PORCH_D4_11(H_BACK_PORCH_D4_11), .H_FRONT_PORCH_D4_11(H_FRONT_PORCH_D4_11),
    .HACTIVE_D4_11(HACTIVE_D4_11), .H_PIXEL_VALID(video_horizontal_signal_1_h_pixel_valid),
    .RESET_B(RESET_B), .H_PIXEL_VALID_B(video_horizontal_signal_1_h_pixel_valid_b),
    .V_CLOCK(video_horizontal_signal_1_v_clock), .H_SYNC_D4_11(H_SYNC_D4_11),
    .H_SYNC_PULSE(video_horizontal_signal_1_h_sync_pulse), .CLOCK(undriven));
  Video_Vertical_Signal video_vertical_signal_1 (
    .V_SYNC_D0_7(V_SYNC_D0_7), .V_LOW_OEB(VERTICAL_RASTER_HIGH_OEB), .CLEAR_IRQ(CLEAR_IRQ),
    .RESET_B(RESET_B), .V_SYNC_PULSE(video_vertical_signal_1_v_sync_pulse), .V_ACTIVE_D4_11(V_ACTIVE_D4_11),
    .V_BACK_PORCH_D0_7(V_BACK_PORCH_D0_7), .V_PIXEL_VALID_B(video_vertical_signal_1_v_pixel_valid_b),
    .V_PULSE_LE(VERTICAL_RASTER_LE), .V_FRONT_PORCH_D0_7(V_FRONT_PORCH_D0_7), .V_D0_7(V_D0_7),
    .V_PIXEL_VALID(video_vertical_signal_1_v_pixel_valid), .V_HIGH_OEB(VERTICAL_RASTER_LOW_OEB),
    .V_CLOCK(video_horizontal_signal_1_v_clock), .IRQ_ENABLE(IRQ_ENABLE), .IRQ_B(IRQ_B));
  or or_1 (or_1_out, video_horizontal_signal_1_h_pixel_valid, video_vertical_signal_1_v_pixel_valid);
  or or_2 (or_2_out, video_horizontal_signal_1_h_pixel_valid_b, video_vertical_signal_1_v_pixel_valid_b);
  not not_1 (not_1_out, FRAME_BUFFER);
  Video_Memory video_memory_1 (
    .FRAME_MEMORY_1_B(video_address_1_frame_memory_1_b), .PIXEL_D0_7(video_memory_1_pixel_d0_7),
    .FRAME_BUFFER_A0_17(video_address_1_frame_buffer_a0_17),
    .FRAME_MEMORY_0_B(video_address_1_frame_memory_0_b), .FRAME_MEMORY_2_B(video_address_1_frame_memory_2_b),
    .PALETTE_D0_7(video_memory_1_palette_d0_7), .FRAME_BUFFER_0(FRAME_BUFFER), .ADDRESS_A0_17(ADDRESS),
    .OEB(OEB), .D_OUT(video_memory_1_d_out), .MAIN_MEMORY_0_B(MAIN_MEMORY_0_B), .WEB(WEB),
    .FRAME_BUFFER_1(not_1_out), .PALETTE_INDEX(PALETTE_INDEX), .MAIN_MEMORY_2_B(MAIN_MEMORY_2_B),
    .MAIN_MEMORY_1_B(MAIN_MEMORY_1_B), .D_IN(video_palette_1_d_out));
  Pull_Resistor pull_resistor_1 (.node(pull_resistor_1_node));
  Video_Palette video_palette_1 (
    .VIDEO_PALETTE_INDEX(video_memory_1_palette_d0_7), .GREEN(GREEN),
    .VIDEO_PIXEL_INDEX(video_memory_1_pixel_d0_7), .WEB(WEB), .PIXEL_VALID_B(or_2_out),
    .D_OUT(video_palette_1_d_out), .RGB_LE(undriven), .RED(RED), .MPU_VALID_B(MAIN_MEMORY_0_B), .OEB(OEB),
    .BLUE(BLUE), .D_IN(video_memory_1_d_out), .Address_A0_17(ADDRESS), .RGB_OEB(pull_resistor_1_node));
  Signal_Dragger_2Bit signal_dragger_2bit_1 (
    .INPUT1(video_horizontal_signal_1_h_sync_pulse), .INPUT2(video_vertical_signal_1_v_sync_pulse),
    .RESET_B(RESET_B), .CLK(undriven), .OUTPUT2(VSYNC), .OUTPUT1(H_SYNC));
endmodule

module Video_Memory (
  input  [7:0] PALETTE_INDEX,
  input  MAIN_MEMORY_0_B,
  input  MAIN_MEMORY_1_B,
  input  MAIN_MEMORY_2_B,
  input  OEB,
  input  [7:0] D_IN,
  input  WEB,
  input  FRAME_MEMORY_0_B,
  input  FRAME_MEMORY_1_B,
  input  FRAME_MEMORY_2_B,
  input  FRAME_BUFFER_0,
  input  FRAME_BUFFER_1,
  input  [17:0] ADDRESS_A0_17,
  input  [17:0] FRAME_BUFFER_A0_17,
  output [7:0] PIXEL_D0_7,
  output [7:0] PALETTE_D0_7,
  output [7:0] D_OUT
);

  wire and_1_out, or_1_out, or_2_out, pull_resistor_4_node, pull_resistor_11_node;
  wire [4:0] pull_resistor_6_node, pull_resistor_9_node, pull_resistor_13_node, pull_resistor_16_node;
  wire [7:0] selecting_8bit_data_multiplexer_1_d_out, selecting_8bit_data_multiplexer_2_d_out;
  wire [23:0] enabling_24bit_address_multiplexer_1_address_a0_23,
       enabling_24bit_address_multiplexer_2_address_a0_23;
  wire [23:18] undriven, undriven_2, undriven_3, undriven_4;

  Pull_Resistor pull_resistor_1 (.node(pull_resistor_9_node[3]));
  Pull_Resistor #(.pull(1)) pull_resistor_2 (.node(pull_resistor_9_node[2]));
  and and_1 (and_1_out, MAIN_MEMORY_0_B, MAIN_MEMORY_1_B, MAIN_MEMORY_2_B);
  Pull_Resistor #(.pull(1)) pull_resistor_3 (.node(pull_resistor_6_node[4]));
  Pull_Resistor pull_resistor_4 (.node(pull_resistor_4_node));
  Pull_Resistor #(.pull(1)) pull_resistor_5 (.node(pull_resistor_6_node[1]));
  Pull_Resistor #(.pull(1)) pull_resistor_6 (.node(pull_resistor_6_node[0]));
  Pull_Resistor #(.pull(1)) pull_resistor_7 (.node(pull_resistor_9_node[4]));
  Pull_Resistor #(.pull(1)) pull_resistor_8 (.node(pull_resistor_9_node[1]));
  Pull_Resistor #(.pull(1)) pull_resistor_9 (.node(pull_resistor_9_node[0]));
  Pull_Resistor #(.pull(1)) pull_resistor_10 (.node(pull_resistor_13_node[4]));
  Pull_Resistor pull_resistor_11 (.node(pull_resistor_11_node));
  Pull_Resistor #(.pull(1)) pull_resistor_12 (.node(pull_resistor_13_node[1]));
  Pull_Resistor #(.pull(1)) pull_resistor_13 (.node(pull_resistor_13_node[0]));
  Pull_Resistor #(.pull(1)) pull_resistor_14 (.node(pull_resistor_16_node[4]));
  Pull_Resistor #(.pull(1)) pull_resistor_15 (.node(pull_resistor_16_node[1]));
  Pull_Resistor #(.pull(1)) pull_resistor_16 (.node(pull_resistor_16_node[0]));
  or or_1 (or_1_out, FRAME_BUFFER_0, and_1_out);
  or or_2 (or_2_out, and_1_out, FRAME_BUFFER_1);
  Selecting_8Bit_Data_Multiplexer selecting_8bit_data_multiplexer_1 (
    .OE(pull_resistor_4_node),
    .DATA_1_D0_8({FRAME_MEMORY_0_B, FRAME_MEMORY_1_B, FRAME_MEMORY_2_B, pull_resistor_9_node}),
    .S(FRAME_BUFFER_0),
    .DATA_0_D0_7({MAIN_MEMORY_0_B, MAIN_MEMORY_1_B, MAIN_MEMORY_2_B, pull_resistor_6_node[4], OEB, WEB, pull_resistor_6_node[1:0]}),
    .D_OUT(selecting_8bit_data_multiplexer_1_d_out));
  Enabling_24Bit_Address_Multiplexer enabling_24bit_address_multiplexer_1 (
    .ADDRESS_0_A0_23({undriven, ADDRESS_A0_17}), .ADDRESS_1_A0_23({undriven_2, FRAME_BUFFER_A0_17}),
    .ADDRESS_A0_23(enabling_24bit_address_multiplexer_1_address_a0_23), .OEB_1(FRAME_BUFFER_0),
    .OEB_0(FRAME_BUFFER_1));
  Selecting_8Bit_Data_Multiplexer selecting_8bit_data_multiplexer_2 (
    .OE(pull_resistor_11_node),
    .DATA_1_D0_8({FRAME_MEMORY_0_B, FRAME_MEMORY_1_B, FRAME_MEMORY_2_B, pull_resistor_16_node[4], pull_resistor_9_node[3:2], pull_resistor_16_node[1:0]}),
    .S(FRAME_BUFFER_1),
    .DATA_0_D0_7({MAIN_MEMORY_0_B, MAIN_MEMORY_1_B, MAIN_MEMORY_2_B, pull_resistor_13_node[4], OEB, WEB, pull_resistor_13_node[1:0]}),
    .D_OUT(selecting_8bit_data_multiplexer_2_d_out));
  Enabling_24Bit_Address_Multiplexer enabling_24bit_address_multiplexer_2 (
    .ADDRESS_0_A0_23({undriven_3, ADDRESS_A0_17}), .ADDRESS_1_A0_23({undriven_4, FRAME_BUFFER_A0_17}),
    .ADDRESS_A0_23(enabling_24bit_address_multiplexer_2_address_a0_23), .OEB_1(FRAME_BUFFER_1),
    .OEB_0(FRAME_BUFFER_0));
  Video_Frame_Buffer video_frame_buffer_1 (
    .Address_A0_17(enabling_24bit_address_multiplexer_1_address_a0_23[17:0]),
    .CEB_2(selecting_8bit_data_multiplexer_1_d_out[5]), .CEB_0(selecting_8bit_data_multiplexer_1_d_out[7]),
    .OEB(selecting_8bit_data_multiplexer_1_d_out[3]), .CEB_1(selecting_8bit_data_multiplexer_1_d_out[6]),
    .VIDEO_BUFFER_ENABLE_B(FRAME_BUFFER_1), .WEB(selecting_8bit_data_multiplexer_1_d_out[2]),
    .PALETTE_OUT_D0_7(PALETTE_D0_7), .MPU_ENABLE_B(or_1_out), .D_IN(D_IN), .D_OUT(D_OUT),
    .PIXEL_OUT_D0_7(PIXEL_D0_7), .PALETTE_INDEX_IN(PALETTE_INDEX));
  Video_Frame_Buffer video_frame_buffer_2 (
    .Address_A0_17(enabling_24bit_address_multiplexer_2_address_a0_23[17:0]),
    .CEB_2(selecting_8bit_data_multiplexer_2_d_out[5]), .CEB_0(selecting_8bit_data_multiplexer_2_d_out[7]),
    .OEB(selecting_8bit_data_multiplexer_2_d_out[3]), .CEB_1(selecting_8bit_data_multiplexer_2_d_out[6]),
    .VIDEO_BUFFER_ENABLE_B(FRAME_BUFFER_0), .WEB(selecting_8bit_data_multiplexer_2_d_out[2]),
    .PALETTE_OUT_D0_7(PALETTE_D0_7), .MPU_ENABLE_B(or_2_out), .D_IN(D_IN), .D_OUT(D_OUT),
    .PIXEL_OUT_D0_7(PIXEL_D0_7), .PALETTE_INDEX_IN(PALETTE_INDEX));
endmodule

module Video_Horizontal_Signal (
  input  RESET_B,
  input  CLOCK,
  input  [7:0] HACTIVE_D4_11,
  input  [7:0] H_FRONT_PORCH_D4_11,
  input  [7:0] H_SYNC_D4_11,
  input  [7:0] H_BACK_PORCH_D4_11,
  output H_PIXEL_VALID,
  output H_PIXEL_VALID_B,
  output H_SYNC_PULSE,
  output V_CLOCK
);

  wire and_2_out, and_3_out, n4_bit_up_counter_lvc163_1_p1, n4_bit_up_counter_lvc163_1_p7,
       n4_bit_up_counter_lvc163_2_p7, n8_bit_comparator_f521_1_p3, n8_bit_comparator_f521_2_p3,
       n8_bit_comparator_f521_3_p3, n8_bit_comparator_f521_4_p3, nand_1_out, or_1_out, pull_resistor_2_node,
       pull_resistor_3_node, pull_resistor_5_node, pull_resistor_7_node;
  wire [3:0] n4_bit_up_counter_lvc163_3_p6;
  wire [7:0] n4_bit_up_counter_lvc163_1_p6;

  Pull_Resistor #(.pull(1)) pull_resistor_1 ();  // open: node
  Pull_Resistor #(.pull(1)) pull_resistor_2 (.node(pull_resistor_2_node));
  Pull_Resistor #(.pull(1)) pull_resistor_3 (.node(pull_resistor_3_node));
  // _4_bit_Up_Counter__LVC163 4_bit_up_counter_lvc163_1: pin names not known; wires that end beside it: n4_bit_up_counter_lvc163_1_p1, pull_resistor_2_node, CLOCK, pull_resistor_3_node, pull_resistor_3_node, n4_bit_up_counter_lvc163_1_p6[3:0], n4_bit_up_counter_lvc163_1_p7
  Pull_Resistor #(.pull(1)) pull_resistor_4 ();  // open: node
  Pull_Resistor #(.pull(1)) pull_resistor_5 (.node(pull_resistor_5_node));
  // _4_bit_Up_Counter__LVC163 4_bit_up_counter_lvc163_2: pin names not known; wires that end beside it: n4_bit_up_counter_lvc163_1_p1, pull_resistor_5_node, CLOCK, n4_bit_up_counter_lvc163_1_p7, pull_resistor_3_node, n4_bit_up_counter_lvc163_1_p6[7:4], n4_bit_up_counter_lvc163_2_p7
  nand nand_1 (nand_1_out, n4_bit_up_counter_lvc163_1_p6[3], n4_bit_up_counter_lvc163_1_p6[2], n4_bit_up_counter_lvc163_1_p6[1], n4_bit_up_counter_lvc163_1_p6[0]);
  Pull_Resistor #(.pull(1)) pull_resistor_6 ();  // open: node
  Pull_Resistor #(.pull(1)) pull_resistor_7 (.node(pull_resistor_7_node));
  // _4_bit_Up_Counter__LVC163 4_bit_up_counter_lvc163_3: pin names not known; wires that end beside it: n4_bit_up_counter_lvc163_1_p1, pull_resistor_7_node, CLOCK, n4_bit_up_counter_lvc163_2_p7, pull_resistor_3_node, n4_bit_up_counter_lvc163_3_p6
  // Probe on {n4_bit_up_counter_lvc163_3_p6, n4_bit_up_counter_lvc163_1_p6}
  // Probe on {HACTIVE_D4_11, 4'b0000}
  // Probe on {H_FRONT_PORCH_D4_11, 4'b0000}
  // Probe on {H_SYNC_D4_11, 4'b0000}
  // Probe on {H_BACK_PORCH_D4_11, 4'b0000}
  Pull_Resistor pull_resistor_8 ();  // open: node
  Pull_Resistor pull_resistor_9 ();  // open: node
  Pull_Resistor pull_resistor_10 ();  // open: node
  Pull_Resistor pull_resistor_11 ();  // open: node
  and and_1 (n4_bit_up_counter_lvc163_1_p1, RESET_B, or_1_out);
  // _8_bit_Comparator__F521 8_bit_comparator_f521_1: pin names not known; wires that end beside it: {n4_bit_up_counter_lvc163_3_p6, n4_bit_up_counter_lvc163_1_p6[7:4]}, HACTIVE_D4_11, n8_bit_comparator_f521_1_p3
  // _8_bit_Comparator__F521 8_bit_comparator_f521_2: pin names not known; wires that end beside it: {n4_bit_up_counter_lvc163_3_p6, n4_bit_up_counter_lvc163_1_p6[7:4]}, H_FRONT_PORCH_D4_11, n8_bit_comparator_f521_2_p3
  // _8_bit_Comparator__F521 8_bit_comparator_f521_3: pin names not known; wires that end beside it: {n4_bit_up_counter_lvc163_3_p6, n4_bit_up_counter_lvc163_1_p6[7:4]}, H_SYNC_D4_11, n8_bit_comparator_f521_3_p3
  // _8_bit_Comparator__F521 8_bit_comparator_f521_4: pin names not known; wires that end beside it: {n4_bit_up_counter_lvc163_3_p6, n4_bit_up_counter_lvc163_1_p6[7:4]}, H_BACK_PORCH_D4_11, n8_bit_comparator_f521_4_p3
  and and_2 (and_2_out, RESET_B, n8_bit_comparator_f521_1_p3);
  and and_3 (and_3_out, RESET_B, n8_bit_comparator_f521_2_p3);
  or or_1 (or_1_out, n8_bit_comparator_f521_4_p3, nand_1_out);
  Pull_Resistor pull_resistor_12 ();  // open: node
  Pull_Resistor #(.pull(1)) pull_resistor_13 ();  // open: node
  Pull_Resistor pull_resistor_14 ();  // open: node
  Pull_Resistor #(.pull(1)) pull_resistor_15 ();  // open: node
  // D_type_Flip_Flop__LVC74 d_type_flip_flop_lvc74_1: pin names not known; wires that end beside it: and_2_out, or_1_out, and_3_out, n8_bit_comparator_f521_3_p3, H_PIXEL_VALID, H_SYNC_PULSE, H_PIXEL_VALID_B
  not not_1 (V_CLOCK, or_1_out);

  // Notes on the sheet:
  //   640x480x60 = $28 $29 $2d $31
endmodule

module Video_Vertical_Signal (
  input  RESET_B,
  input  V_CLOCK,
  input  [7:0] V_ACTIVE_D4_11,
  input  [7:0] V_FRONT_PORCH_D0_7,
  input  [7:0] V_SYNC_D0_7,
  input  [7:0] V_BACK_PORCH_D0_7,
  input  CLEAR_IRQ,
  input  IRQ_ENABLE,
  input  V_PULSE_LE,
  input  V_LOW_OEB,
  input  V_HIGH_OEB,
  output V_PIXEL_VALID,
  output V_PIXEL_VALID_B,
  output V_SYNC_PULSE,
  output IRQ_B,
  output [7:0] V_D0_7
);

  wire and_1_out, and_2_out, and_3_out, d_type_flip_flop_lvc74_1_p8, n4_bit_up_counter_lvc161_1_p7,
       n8_bit_comparator_f521_1_p3, n8_bit_comparator_f521_2_p3, n8_bit_comparator_f521_3_p3,
       n8_bit_comparator_f521_4_p3, nand_1_out, not_1_out, not_2_out, not_3_out, not_4_out, not_5_out,
       not_6_out, not_7_out, or_1_out, pull_resistor_2_node, pull_resistor_3_node, pull_resistor_6_node,
       pull_resistor_8_node;
  wire [3:0] n4_bit_up_counter_lvc161_1_p6, n4_bit_up_counter_lvc161_2_p6, n12_bit_up_counter_hc4040_1_p3_2,
       pull_resistor_12_node;
  wire [7:0] n12_bit_up_counter_hc4040_1_p3;

  and and_1 (and_1_out, n8_bit_comparator_f521_4_p3, RESET_B);
  not not_1 (not_1_out, and_1_out);
  // _12_bit_Up_Counter__HC4040 12_bit_up_counter_hc4040_1: pin names not known; wires that end beside it: not_1_out, V_CLOCK, {n12_bit_up_counter_hc4040_1_p3_2, n12_bit_up_counter_hc4040_1_p3}
  // Probe on {V_ACTIVE_D4_11, 4'b0000}
  // Probe on {n12_bit_up_counter_hc4040_1_p3_2, n12_bit_up_counter_hc4040_1_p3[7:4]}
  Pull_Resistor pull_resistor_1 ();  // open: node
  not not_2 (not_2_out, n12_bit_up_counter_hc4040_1_p3[3]);
  not not_3 (not_3_out, n12_bit_up_counter_hc4040_1_p3[2]);
  nand nand_1 (nand_1_out, not_2_out, not_3_out, not_4_out, not_5_out);
  not not_4 (not_4_out, n12_bit_up_counter_hc4040_1_p3[1]);
  not not_5 (not_5_out, n12_bit_up_counter_hc4040_1_p3[0]);
  // _8_bit_Comparator__F521 8_bit_comparator_f521_1: pin names not known; wires that end beside it: {n12_bit_up_counter_hc4040_1_p3_2, n12_bit_up_counter_hc4040_1_p3[7:4]}, V_ACTIVE_D4_11, n8_bit_comparator_f521_1_p3
  and and_2 (and_2_out, RESET_B, or_1_out);
  or or_1 (or_1_out, n8_bit_comparator_f521_1_p3, nand_1_out);
  and and_3 (and_3_out, RESET_B, not_6_out);
  not not_6 (not_6_out, CLEAR_IRQ);
  Pull_Resistor pull_resistor_2 (.node(pull_resistor_2_node));
  Pull_Resistor #(.pull(1)) pull_resistor_3 (.node(pull_resistor_3_node));
  not not_7 (not_7_out, and_2_out);
  Pull_Resistor #(.pull(1)) pull_resistor_4 ();  // open: node
  Pull_Resistor #(.pull(1)) pull_resistor_5 ();  // open: node
  Pull_Resistor #(.pull(1)) pull_resistor_6 (.node(pull_resistor_6_node));
  // D_type_Flip_Flop__LVC74 d_type_flip_flop_lvc74_1: pin names not known; wires that end beside it: and_1_out, and_2_out, and_3_out, pull_resistor_2_node, pull_resistor_3_node, not_7_out, IRQ_ENABLE, d_type_flip_flop_lvc74_1_p8, IRQ_B
  // _4_bit_Up_Counter__LVC161 4_bit_up_counter_lvc161_1: pin names not known; wires that end beside it: and_2_out, pull_resistor_6_node, V_CLOCK, d_type_flip_flop_lvc74_1_p8, d_type_flip_flop_lvc74_1_p8, n4_bit_up_counter_lvc161_1_p6, n4_bit_up_counter_lvc161_1_p7
  Pull_Resistor #(.pull(1)) pull_resistor_7 ();  // open: node
  Pull_Resistor #(.pull(1)) pull_resistor_8 (.node(pull_resistor_8_node));
  // _4_bit_Up_Counter__LVC161 4_bit_up_counter_lvc161_2: pin names not known; wires that end beside it: and_2_out, pull_resistor_8_node, V_CLOCK, n4_bit_up_counter_lvc161_1_p7, d_type_flip_flop_lvc74_1_p8, n4_bit_up_counter_lvc161_2_p6
  // Probe on {n4_bit_up_counter_lvc161_2_p6, n4_bit_up_counter_lvc161_1_p6}
  Pull_Resistor pull_resistor_9 ();  // open: node
  Pull_Resistor pull_resistor_10 ();  // open: node
  Pull_Resistor pull_resistor_11 ();  // open: node
  // _8_bit_Comparator__F521 8_bit_comparator_f521_2: pin names not known; wires that end beside it: {n4_bit_up_counter_lvc161_2_p6, n4_bit_up_counter_lvc161_1_p6}, V_FRONT_PORCH_D0_7, n8_bit_comparator_f521_2_p3
  // _8_bit_Comparator__F521 8_bit_comparator_f521_3: pin names not known; wires that end beside it: {n4_bit_up_counter_lvc161_2_p6, n4_bit_up_counter_lvc161_1_p6}, V_SYNC_D0_7, n8_bit_comparator_f521_3_p3
  // _8_bit_Comparator__F521 8_bit_comparator_f521_4: pin names not known; wires that end beside it: {n4_bit_up_counter_lvc161_2_p6, n4_bit_up_counter_lvc161_1_p6}, V_BACK_PORCH_D0_7, n8_bit_comparator_f521_4_p3
  Pull_Resistor pull_resistor_12 (.node(pull_resistor_12_node));
  Pull_Resistor pull_resistor_13 ();  // open: node
  Pull_Resistor #(.pull(1)) pull_resistor_14 ();  // open: node
  Pull_Resistor pull_resistor_15 ();  // open: node
  Pull_Resistor #(.pull(1)) pull_resistor_16 ();  // open: node
  // D_type_Flip_Flop__LVC74 d_type_flip_flop_lvc74_2: pin names not known; wires that end beside it: and_2_out, n8_bit_comparator_f521_4_p3, n8_bit_comparator_f521_2_p3, n8_bit_comparator_f521_3_p3, V_PIXEL_VALID, V_PIXEL_VALID_B, V_SYNC_PULSE
  // _8_bit_Latch__LVC574 8_bit_latch_lvc574_1: pin names not known; wires that end beside it: V_HIGH_OEB, {pull_resistor_12_node, n12_bit_up_counter_hc4040_1_p3_2}, V_PULSE_LE, V_D0_7
  // _8_bit_Latch__LVC574 8_bit_latch_lvc574_2: pin names not known; wires that end beside it: V_LOW_OEB, n12_bit_up_counter_hc4040_1_p3, V_PULSE_LE, V_D0_7

  // Notes on the sheet:
  //   640x480x60 = $1d $03 $07 $14
endmodule

module Video_Address (
  input  START_FRAME_B,
  input  RESET_B,
  input  CLOCK,
  input  [1:0] PIXEL_DOUBLING_X,
  output FRAME_MEMORY_0_B,
  output FRAME_MEMORY_1_B,
  output FRAME_MEMORY_2_B,
  output [17:0] FRAME_BUFFER_A0_17
);

  wire and_1_out, d_ff_1_qn, d_ff_2_qn, n4_bit_up_counter_lvc163_1_p3, n4_bit_up_counter_lvc163_1_p7,
       n4_bit_up_counter_lvc163_2_p7, n4_bit_up_counter_lvc163_3_p7, n4_bit_up_counter_lvc163_4_p7,
       not_1_out, not_2_out, pull_resistor_2_node, pull_resistor_3_node, pull_resistor_4_node,
       pull_resistor_6_node, pull_resistor_7_node, pull_resistor_8_node, pull_resistor_10_node,
       pull_resistor_11_node, pull_resistor_13_node, pull_resistor_14_node, pull_resistor_16_node,
       pull_resistor_17_node, pull_resistor_19_node, pull_resistor_20_node, pull_resistor_23_node;
  wire [3:1] d_ff_1_q;
  wire [3:2] n4_bit_up_counter_lvc163_5_p6;
  wire [3:3] n2_to_4_decoder_lvc139_1_p3;

  and and_1 (and_1_out, START_FRAME_B, RESET_B);
  Pull_Resistor #(.pull(1)) pull_resistor_1 ();  // open: node
  Pull_Resistor #(.pull(1)) pull_resistor_2 (.node(pull_resistor_2_node));
  Pull_Resistor #(.pull(1)) pull_resistor_3 (.node(pull_resistor_3_node));
  Pull_Resistor #(.pull(1)) pull_resistor_4 (.node(pull_resistor_4_node));
  D_Flip_Flop d_ff_1 (.clk(CLOCK), .D(d_ff_1_qn), .Q(d_ff_1_q[1]), .Qn(d_ff_1_qn), .reset(not_1_out));  // open: preset
  Pull_Resistor pull_resistor_5 (.node(d_ff_1_q[3]));
  not not_1 (not_1_out, RESET_B);
  D_Flip_Flop d_ff_2 (
    .clk(d_ff_1_qn), .D(d_ff_2_qn), .Q(d_ff_1_q[2]), .Qn(d_ff_2_qn), .reset(not_2_out));  // open: preset
  Pull_Resistor #(.pull(1)) pull_resistor_6 (.node(pull_resistor_6_node));
  not not_2 (not_2_out, RESET_B);
  // _4_bit_Up_Counter__LVC163 4_bit_up_counter_lvc163_1: pin names not known; wires that end beside it: and_1_out, pull_resistor_2_node, n4_bit_up_counter_lvc163_1_p3, pull_resistor_3_node, pull_resistor_4_node, FRAME_BUFFER_A0_17[3:0], n4_bit_up_counter_lvc163_1_p7
  Pull_Resistor pull_resistor_7 (.node(pull_resistor_7_node));
  Pull_Resistor #(.pull(1)) pull_resistor_8 (.node(pull_resistor_8_node));
  // _4_to_1_Multiplexer__QS3253 4_to_1_multiplexer_qs3253_1: pin names not known; wires that end beside it: pull_resistor_7_node, pull_resistor_8_node, PIXEL_DOUBLING_X, {d_ff_1_q, CLOCK}, pull_resistor_6_node, n4_bit_up_counter_lvc163_1_p3
  Pull_Resistor #(.pull(1)) pull_resistor_9 ();  // open: node
  Pull_Resistor #(.pull(1)) pull_resistor_10 (.node(pull_resistor_10_node));
  Pull_Resistor #(.pull(1)) pull_resistor_11 (.node(pull_resistor_11_node));
  // _4_bit_Up_Counter__LVC163 4_bit_up_counter_lvc163_2: pin names not known; wires that end beside it: and_1_out, pull_resistor_10_node, n4_bit_up_counter_lvc163_1_p3, n4_bit_up_counter_lvc163_1_p7, pull_resistor_11_node, FRAME_BUFFER_A0_17[7:4], n4_bit_up_counter_lvc163_2_p7
  Pull_Resistor #(.pull(1)) pull_resistor_12 ();  // open: node
  Pull_Resistor #(.pull(1)) pull_resistor_13 (.node(pull_resistor_13_node));
  Pull_Resistor #(.pull(1)) pull_resistor_14 (.node(pull_resistor_14_node));
  // _4_bit_Up_Counter__LVC163 4_bit_up_counter_lvc163_3: pin names not known; wires that end beside it: and_1_out, pull_resistor_13_node, n4_bit_up_counter_lvc163_1_p3, n4_bit_up_counter_lvc163_2_p7, pull_resistor_14_node, FRAME_BUFFER_A0_17[11:8], n4_bit_up_counter_lvc163_3_p7
  Pull_Resistor #(.pull(1)) pull_resistor_15 ();  // open: node
  Pull_Resistor #(.pull(1)) pull_resistor_16 (.node(pull_resistor_16_node));
  Pull_Resistor #(.pull(1)) pull_resistor_17 (.node(pull_resistor_17_node));
  // _4_bit_Up_Counter__LVC163 4_bit_up_counter_lvc163_4: pin names not known; wires that end beside it: and_1_out, pull_resistor_16_node, n4_bit_up_counter_lvc163_1_p3, n4_bit_up_counter_lvc163_3_p7, pull_resistor_17_node, FRAME_BUFFER_A0_17[15:12], n4_bit_up_counter_lvc163_4_p7
  Pull_Resistor #(.pull(1)) pull_resistor_18 ();  // open: node
  Pull_Resistor #(.pull(1)) pull_resistor_19 (.node(pull_resistor_19_node));
  Pull_Resistor #(.pull(1)) pull_resistor_20 (.node(pull_resistor_20_node));
  // _4_bit_Up_Counter__LVC163 4_bit_up_counter_lvc163_5: pin names not known; wires that end beside it: and_1_out, pull_resistor_19_node, n4_bit_up_counter_lvc163_1_p3, n4_bit_up_counter_lvc163_4_p7, pull_resistor_20_node, {n4_bit_up_counter_lvc163_5_p6, FRAME_BUFFER_A0_17[17:16]}
  Pull_Resistor pull_resistor_21 ();  // open: node
  Pull_Resistor #(.pull(1)) pull_resistor_22 ();  // open: node
  Pull_Resistor #(.pull(1)) pull_resistor_23 (.node(pull_resistor_23_node));
  // _2_to_4_Decoder__LVC139 2_to_4_decoder_lvc139_1: pin names not known; wires that end beside it: n4_bit_up_counter_lvc163_5_p6, pull_resistor_23_node, {n2_to_4_decoder_lvc139_1_p3[3], FRAME_MEMORY_2_B, FRAME_MEMORY_1_B, FRAME_MEMORY_0_B}

  // Notes on the sheet:
  //   Source Address
endmodule

module Video_Frame_Buffer (
  input  [7:0] D_IN,
  input  MPU_ENABLE_B,
  input  VIDEO_BUFFER_ENABLE_B,
  input  [7:0] PALETTE_INDEX_IN,
  input  OEB,
  input  WEB,
  input  CEB_0,
  input  CEB_1,
  input  CEB_2,
  input  [17:0] Address_A0_17,
  output [7:0] D_OUT,
  output [7:0] PALETTE_OUT_D0_7,
  output [7:0] PIXEL_OUT_D0_7
);

  wire bidirectional_monsters_1_read, bidirectional_monsters_1_write;
  wire [7:0] n8_bit_bus_transceiver_lvc4245_1_p4;
  wire [15:0] ram_1_data;

  SRAM_Chipifier sram_chipifier_1 (.CEB(CEB_0), .OEB(OEB), .WEB(WEB));  // open: E, OE, WE
  SRAM_Chipifier sram_chipifier_2 (.CEB(CEB_1), .OEB(OEB), .WEB(WEB));  // open: E, OE, WE
  SRAM_Chipifier sram_chipifier_3 (.CEB(CEB_2), .OEB(OEB), .WEB(WEB));  // open: E, OE, WE
  RAM #(.enables("line"), .dataWidth(16), .databus("bidir"), .trigger("high"), .\type ("nonvolatile"), .addrWidth(18)) ram_1 (
    .addr(Address_A0_17), .data(ram_1_data));  // open: we, oe, clk
  RAM #(.\type ("nonvolatile"), .trigger("high"), .addrWidth(18), .dataWidth(16), .enables("line"), .databus("bidir")) ram_2 (
    .addr(Address_A0_17), .data(ram_1_data));  // open: we, oe, clk
  RAM #(.enables("line"), .dataWidth(16), .\type ("nonvolatile"), .trigger("high"), .databus("bidir"), .addrWidth(18)) ram_3 (
    .addr(Address_A0_17), .data(ram_1_data));  // open: we, oe, clk
  // _8_bit_Line_Driver__LVC541 8_bit_line_driver_lvc541_1: pin names not known; wires that end beside it: MPU_ENABLE_B, WEB, PALETTE_INDEX_IN, ram_1_data[15:8]
  // Probe on ram_1_data
  // _8_bit_Bus_Transceiver__LVC4245 8_bit_bus_transceiver_lvc4245_1: pin names not known; wires that end beside it: MPU_ENABLE_B, ram_1_data[7:0], OEB, n8_bit_bus_transceiver_lvc4245_1_p4
  // _16_bit_Line_Driver__LVC16244 16_bit_line_driver_lvc16244_1: pin names not known; wires that end beside it: VIDEO_BUFFER_ENABLE_B, VIDEO_BUFFER_ENABLE_B, VIDEO_BUFFER_ENABLE_B, VIDEO_BUFFER_ENABLE_B, ram_1_data[11:8], ram_1_data[15:12], ram_1_data[3:0], ram_1_data[7:4], PALETTE_OUT_D0_7[3:0], PALETTE_OUT_D0_7[7:4], PIXEL_OUT_D0_7[3:0], PIXEL_OUT_D0_7[7:4]
  // Probe on n8_bit_bus_transceiver_lvc4245_1_p4
  // Probe on PALETTE_OUT_D0_7
  // Probe on PIXEL_OUT_D0_7
  assign n8_bit_bus_transceiver_lvc4245_1_p4 = bidirectional_monsters_1_read ? D_IN : 8'bz;  // Controlled_Buffer controlled_buffer_1
  assign D_OUT = bidirectional_monsters_1_write ? n8_bit_bus_transceiver_lvc4245_1_p4 : 8'bz;  // Controlled_Buffer controlled_buffer_2
  Bidirectional_Monsters bidirectional_monsters_1 (
    .WRITE(bidirectional_monsters_1_write), .RWB(OEB), .READ(bidirectional_monsters_1_read),
    .ENABLE_B(MPU_ENABLE_B));
endmodule

module Video_Palette (
  input  [7:0] D_IN,
  input  [17:0] Address_A0_17,
  input  MPU_VALID_B,
  input  OEB,
  input  WEB,
  input  PIXEL_VALID_B,
  input  [7:0] VIDEO_PALETTE_INDEX,
  input  [7:0] VIDEO_PIXEL_INDEX,
  input  RGB_OEB,
  input  RGB_LE,
  output [7:0] D_OUT,
  output [7:0] RED,
  output [7:0] GREEN,
  output [7:0] BLUE
);

  wire and_1_out, and_2_out, and_3_out, bidirectional_monsters_1_read, bidirectional_monsters_1_write,
       not_1_out, pull_resistor_1_node, pull_resistor_2_node, pull_resistor_8_node;
  wire [3:0] n2_to_4_decoder_lvc139_1_p5, n4_bit_multiplexer_lvc257_1_p5, n16_bit_line_driver_lvc16244_1_p9,
       n16_bit_line_driver_lvc16244_1_p10, n16_bit_line_driver_lvc16244_1_p11,
       n16_bit_line_driver_lvc16244_1_p12;
  wire [3:1] pull_resistor_5_node;
  wire [3:2] pull_resistor_3_node;
  wire [7:0] n8_bit_bus_transceiver_lvc4245_1_p4, ram_1_data, ram_2_data, ram_3_data;
  wire [7:7] n8_bit_line_driver_lvc541_1_p4;

  Pull_Resistor #(.pull(1)) pull_resistor_1 (.node(pull_resistor_1_node));
  Pull_Resistor #(.pull(1)) pull_resistor_2 (.node(pull_resistor_2_node));
  not not_1 (not_1_out, MPU_VALID_B);
  Pull_Resistor pull_resistor_3 (.node(pull_resistor_3_node[2]));
  Pull_Resistor pull_resistor_4 (.node(pull_resistor_3_node[3]));
  Pull_Resistor #(.pull(1)) pull_resistor_5 (.node(pull_resistor_5_node[1]));
  Pull_Resistor pull_resistor_6 (.node(pull_resistor_5_node[2]));
  Pull_Resistor pull_resistor_7 (.node(pull_resistor_5_node[3]));
  // _2_to_4_Decoder__LVC139 2_to_4_decoder_lvc139_1: pin names not known; wires that end beside it: MPU_VALID_B, pull_resistor_1_node, Address_A0_17[17:16], pull_resistor_2_node, n2_to_4_decoder_lvc139_1_p5
  // _16_bit_Line_Driver__LVC16244 16_bit_line_driver_lvc16244_1: pin names not known; wires that end beside it: MPU_VALID_B, MPU_VALID_B, MPU_VALID_B, MPU_VALID_B, Address_A0_17[15:12], Address_A0_17[11:8], Address_A0_17[7:4], Address_A0_17[3:0], n16_bit_line_driver_lvc16244_1_p9, n16_bit_line_driver_lvc16244_1_p10, n16_bit_line_driver_lvc16244_1_p11, n16_bit_line_driver_lvc16244_1_p12
  Pull_Resistor pull_resistor_8 (.node(pull_resistor_8_node));
  // _8_bit_Line_Driver__LVC541 8_bit_line_driver_lvc541_1: pin names not known; wires that end beside it: PIXEL_VALID_B, not_1_out, VIDEO_PALETTE_INDEX, {n8_bit_line_driver_lvc541_1_p4[7], n16_bit_line_driver_lvc16244_1_p9[2:0], n16_bit_line_driver_lvc16244_1_p10}
  // _8_bit_Line_Driver__LVC541 8_bit_line_driver_lvc541_2: pin names not known; wires that end beside it: PIXEL_VALID_B, not_1_out, VIDEO_PIXEL_INDEX, {n16_bit_line_driver_lvc16244_1_p11, n16_bit_line_driver_lvc16244_1_p12}
  // _4_bit_Multiplexer__LVC257 4_bit_multiplexer_lvc257_1: pin names not known; wires that end beside it: pull_resistor_8_node, MPU_VALID_B, {pull_resistor_3_node, WEB, OEB}, {pull_resistor_5_node, PIXEL_VALID_B}, n4_bit_multiplexer_lvc257_1_p5
  // Probe on {n16_bit_line_driver_lvc16244_1_p9[2:0], n16_bit_line_driver_lvc16244_1_p10, n16_bit_line_driver_lvc16244_1_p11, n16_bit_line_driver_lvc16244_1_p12}
  and and_1 (and_1_out, n2_to_4_decoder_lvc139_1_p5[0], not_1_out);
  and and_2 (and_2_out, n2_to_4_decoder_lvc139_1_p5[1], not_1_out);
  and and_3 (and_3_out, n2_to_4_decoder_lvc139_1_p5[2], not_1_out);
  RAM #(.addrWidth(15), .\type ("nonvolatile"), .trigger("high"), .databus("bidir"), .enables("line")) ram_1 (
    .addr({n16_bit_line_driver_lvc16244_1_p9[2:0], n16_bit_line_driver_lvc16244_1_p10, n16_bit_line_driver_lvc16244_1_p11, n16_bit_line_driver_lvc16244_1_p12}),
    .data(ram_1_data));  // open: we, oe, clk
  SRAM_Chipifier sram_chipifier_1 (
    .CEB(and_1_out), .OEB(n4_bit_multiplexer_lvc257_1_p5[0]), .WEB(n4_bit_multiplexer_lvc257_1_p5[1]));  // open: E, OE, WE
  RAM #(.\type ("nonvolatile"), .enables("line"), .addrWidth(15), .trigger("high"), .databus("bidir")) ram_2 (
    .addr({n16_bit_line_driver_lvc16244_1_p9[2:0], n16_bit_line_driver_lvc16244_1_p10, n16_bit_line_driver_lvc16244_1_p11, n16_bit_line_driver_lvc16244_1_p12}),
    .data(ram_2_data));  // open: we, oe, clk
  SRAM_Chipifier sram_chipifier_2 (
    .CEB(and_2_out), .OEB(n4_bit_multiplexer_lvc257_1_p5[0]), .WEB(n4_bit_multiplexer_lvc257_1_p5[1]));  // open: E, OE, WE
  RAM #(.enables("line"), .addrWidth(15), .trigger("high"), .databus("bidir"), .\type ("nonvolatile")) ram_3 (
    .addr({n16_bit_line_driver_lvc16244_1_p9[2:0], n16_bit_line_driver_lvc16244_1_p10, n16_bit_line_driver_lvc16244_1_p11, n16_bit_line_driver_lvc16244_1_p12}),
    .data(ram_3_data));  // open: we, oe, clk
  SRAM_Chipifier sram_chipifier_3 (
    .CEB(and_3_out), .OEB(n4_bit_multiplexer_lvc257_1_p5[0]), .WEB(n4_bit_multiplexer_lvc257_1_p5[1]));  // open: E, OE, WE
  Pull_Resistor #(.pull(1)) pull_resistor_9 ();  // open: node
  // _8_bit_Bus_Transceiver__LVC4245 8_bit_bus_transceiver_lvc4245_1: pin names not known; wires that end beside it: n2_to_4_decoder_lvc139_1_p5[0], ram_1_data, OEB, n8_bit_bus_transceiver_lvc4245_1_p4
  // _8_bit_Bus_Transceiver__LVC4245 8_bit_bus_transceiver_lvc4245_2: pin names not known; wires that end beside it: n2_to_4_decoder_lvc139_1_p5[1], ram_2_data, OEB, n8_bit_bus_transceiver_lvc4245_1_p4
  // _8_bit_Bus_Transceiver__LVC4245 8_bit_bus_transceiver_lvc4245_3: pin names not known; wires that end beside it: n2_to_4_decoder_lvc139_1_p5[2], ram_3_data, OEB, n8_bit_bus_transceiver_lvc4245_1_p4
  // _8_bit_Bus_Transceiver__LVC4245 8_bit_bus_transceiver_lvc4245_4: pin names not known; wires that end beside it: n2_to_4_decoder_lvc139_1_p5[3], OEB, n8_bit_bus_transceiver_lvc4245_1_p4
  // Probe on n8_bit_bus_transceiver_lvc4245_1_p4
  // _16_bit_Latch__LVC16373 16_bit_latch_lvc16373_1: pin names not known; wires that end beside it: RGB_OEB, RGB_OEB, ram_1_data, RGB_LE, ram_2_data, RGB_LE, RED, GREEN
  // _8_bit_Latch__LVC573 8_bit_latch_lvc573_1: pin names not known; wires that end beside it: RGB_OEB, ram_3_data, RGB_LE, BLUE
  assign D_OUT = bidirectional_monsters_1_write ? n8_bit_bus_transceiver_lvc4245_1_p4 : 8'bz;  // Controlled_Buffer controlled_buffer_1
  assign n8_bit_bus_transceiver_lvc4245_1_p4 = bidirectional_monsters_1_read ? D_IN : 8'bz;  // Controlled_Buffer controlled_buffer_2
  Bidirectional_Monsters bidirectional_monsters_1 (
    .WRITE(bidirectional_monsters_1_write), .RWB(OEB), .READ(bidirectional_monsters_1_read),
    .ENABLE_B(MPU_VALID_B));
endmodule

module Timing_Circuit (
  input  RESET,
  input  CLOCK_IN,
  output [7:0] SELECTOR_B,
  output RESET_0_B,
  output RESET_1_B,
  output SLOW_SELECTOR,
  output CLK,
  output CLK_B,
  output HCLK,
  output HCLK_B,
  output [3:0] MULTIPLEXER,
  output [3:0] COUNTER
);

  wire clock_1_out, digital_oscilloscope_1_p1, not_1_out, not_2_out, not_3_out, not_4_out,
       pull_resistor_1_node, pull_resistor_2_node, pull_resistor_3_node, pull_resistor_4_node,
       pull_resistor_5_node, pull_resistor_6_node, pull_resistor_8_node, pull_resistor_9_node,
       SLOW_SELECTOR_t;
  wire [3:0] pull_resistor_7_node;
  wire [7:2] n8_bit_serial_in_shift_lvc595_1_p6;
  wire [7:4] n8_bit_latch_lvc574_1_p4, n8_bit_latch_lvc574_2_p4;

  not not_1 (not_1_out, RESET);
  Clock clock_1 (.out(clock_1_out));
  // Digital_Oscilloscope #(.nState(32)) digital_oscilloscope_1: pin names not known; wires that end beside it: digital_oscilloscope_1_p1, SELECTOR_B[0], SELECTOR_B[1], SELECTOR_B[2], SELECTOR_B[3], SELECTOR_B[4], SELECTOR_B[5], SELECTOR_B[6], SELECTOR_B[7], RESET_0_B, RESET_1_B
  Clock clock_2 (.out(digital_oscilloscope_1_p1));
  // EconoReset__DS1813 econoreset_ds1813_1: pin names not known; wires that end beside it: not_1_out, clock_1_out, SLOW_SELECTOR
  Pull_Resistor pull_resistor_1 (.node(pull_resistor_1_node));
  D_Flip_Flop d_ff_1 (.clk(CLOCK_IN), .D(CLK_B), .Q(CLK), .Qn(CLK_B), .reset(not_2_out));  // open: preset
  not not_2 (not_2_out, SLOW_SELECTOR);
  D_Flip_Flop d_ff_2 (.clk(CLK_B), .D(HCLK_B), .Q(HCLK), .Qn(HCLK_B), .reset(not_3_out));  // open: preset
  not not_3 (not_3_out, SLOW_SELECTOR);
  // _8_bit_serial_in_shift__LVC595 8_bit_serial_in_shift_lvc595_1: pin names not known; wires that end beside it: pull_resistor_1_node, SLOW_SELECTOR, SLOW_SELECTOR, CLK, CLK, {n8_bit_serial_in_shift_lvc595_1_p6, RESET_1_B, RESET_0_B}
  Pull_Resistor #(.pull(1)) pull_resistor_2 (.node(pull_resistor_2_node));
  Pull_Resistor #(.pull(1)) pull_resistor_3 (.node(pull_resistor_3_node));
  Pull_Resistor #(.pull(1)) pull_resistor_4 (.node(pull_resistor_4_node));
  not not_4 (not_4_out, RESET_1_B);
  // _4_bit_Up_Counter__LVC163 4_bit_up_counter_lvc163_1: pin names not known; wires that end beside it: RESET_1_B, pull_resistor_2_node, pull_resistor_3_node, CLK, pull_resistor_4_node, RESET_1_B, COUNTER, SLOW_SELECTOR_t
  Pull_Resistor #(.pull(1)) pull_resistor_5 (.node(pull_resistor_5_node));
  Pull_Resistor #(.pull(1)) pull_resistor_6 (.node(pull_resistor_6_node));
  // _2_to_4_Decoder__LVC139 2_to_4_decoder_lvc139_1: pin names not known; wires that end beside it: pull_resistor_5_node, not_4_out, pull_resistor_6_node, COUNTER[1:0], MULTIPLEXER
  Pull_Resistor #(.pull(1)) pull_resistor_7 (.node(pull_resistor_7_node));
  Pull_Resistor pull_resistor_8 (.node(pull_resistor_8_node));
  Pull_Resistor pull_resistor_9 (.node(pull_resistor_9_node));
  // _8_bit_Latch__LVC574 8_bit_latch_lvc574_1: pin names not known; wires that end beside it: pull_resistor_8_node, {pull_resistor_7_node, MULTIPLEXER}, CLK_B, {n8_bit_latch_lvc574_1_p4, SELECTOR_B[6], SELECTOR_B[4], SELECTOR_B[2], SELECTOR_B[0]}
  // _8_bit_Latch__LVC574 8_bit_latch_lvc574_2: pin names not known; wires that end beside it: pull_resistor_9_node, {n8_bit_latch_lvc574_1_p4, SELECTOR_B[6], SELECTOR_B[4], SELECTOR_B[2], SELECTOR_B[0]}, CLK, {n8_bit_latch_lvc574_2_p4, SELECTOR_B[7], SELECTOR_B[5], SELECTOR_B[3], SELECTOR_B[1]}

  // Other names for the same wires on the sheet: RESET_0 = RESET_0_B; RESET_1 = RESET_1_B; CLOCK_B = CLK_B;
  //   HALF_CLOCK = HCLK; HALF_CLOCK_B = HCLK_B; RSTB = SLOW_SELECTOR; SEL0 = SELECTOR_B[0]; SEL1 = SELECTOR_B[1];
  //   SEL2 = SELECTOR_B[2]; SEL3 = SELECTOR_B[3]; SEL4 = SELECTOR_B[4]; SEL5 = SELECTOR_B[5]; SEL6 = SELECTOR_B[6];
  //   SEL7 = SELECTOR_B[7]

  // Notes on the sheet:
  //   Debug Outputs
endmodule

module Quick_Timing_Circuit (
  input  RESET,
  input  CLOCK_IN,
  output [7:0] SELECTOR_B,
  output RESET_0_B,
  output RESET_1_B,
  output SLOW_SELECTOR,
  output CLK,
  output CLK_B,
  output HCLK,
  output HCLK_B,
  output [3:0] MULTIPLEXER,
  output [3:0] COUNTER
);

  wire digital_oscilloscope_1_p1, not_1_out, not_3_out, not_4_out, pull_resistor_1_node,
       pull_resistor_2_node, pull_resistor_3_node, pull_resistor_4_node, pull_resistor_5_node,
       pull_resistor_6_node, pull_resistor_8_node, pull_resistor_9_node, SLOW_SELECTOR_t;
  wire [3:0] pull_resistor_7_node;
  wire [7:0] n8_bit_serial_in_shift_lvc595_1_p6;
  wire [7:4] n8_bit_latch_lvc574_1_p4, n8_bit_latch_lvc574_2_p4;

  not not_1 (not_1_out, RESET);
  D_Flip_Flop d_ff_1 (.clk(CLOCK_IN), .D(not_1_out), .Q(SLOW_SELECTOR));  // open: Qn, preset, reset
  // Digital_Oscilloscope #(.nState(32)) digital_oscilloscope_1: pin names not known; wires that end beside it: digital_oscilloscope_1_p1, SELECTOR_B[0], SELECTOR_B[1], SELECTOR_B[2], SELECTOR_B[3], SELECTOR_B[4], SELECTOR_B[5], SELECTOR_B[6], SELECTOR_B[7], RESET_0_B, RESET_1_B
  Clock clock_1 (.out(digital_oscilloscope_1_p1));
  Pull_Resistor pull_resistor_1 (.node(pull_resistor_1_node));
  not not_2 (CLK_B, CLOCK_IN);
  D_Flip_Flop d_ff_2 (.clk(CLOCK_IN), .D(HCLK_B), .Q(HCLK), .Qn(HCLK_B), .reset(not_3_out));  // open: preset
  not not_3 (not_3_out, SLOW_SELECTOR);
  // _8_bit_serial_in_shift__LVC595 8_bit_serial_in_shift_lvc595_1: pin names not known; wires that end beside it: pull_resistor_1_node, SLOW_SELECTOR, SLOW_SELECTOR, CLOCK_IN, CLOCK_IN, {n8_bit_serial_in_shift_lvc595_1_p6[7:4], RESET_1_B, n8_bit_serial_in_shift_lvc595_1_p6[2], RESET_0_B, n8_bit_serial_in_shift_lvc595_1_p6[0]}
  Pull_Resistor #(.pull(1)) pull_resistor_2 (.node(pull_resistor_2_node));
  Pull_Resistor #(.pull(1)) pull_resistor_3 (.node(pull_resistor_3_node));
  Pull_Resistor #(.pull(1)) pull_resistor_4 (.node(pull_resistor_4_node));
  not not_4 (not_4_out, RESET_1_B);
  // _4_bit_Up_Counter__LVC163 4_bit_up_counter_lvc163_1: pin names not known; wires that end beside it: RESET_1_B, pull_resistor_2_node, pull_resistor_3_node, CLOCK_IN, pull_resistor_4_node, RESET_1_B, COUNTER, SLOW_SELECTOR_t
  Pull_Resistor #(.pull(1)) pull_resistor_5 (.node(pull_resistor_5_node));
  Pull_Resistor #(.pull(1)) pull_resistor_6 (.node(pull_resistor_6_node));
  // _2_to_4_Decoder__LVC139 2_to_4_decoder_lvc139_1: pin names not known; wires that end beside it: pull_resistor_5_node, not_4_out, pull_resistor_6_node, COUNTER[1:0], MULTIPLEXER
  Pull_Resistor #(.pull(1)) pull_resistor_7 (.node(pull_resistor_7_node));
  Pull_Resistor pull_resistor_8 (.node(pull_resistor_8_node));
  Pull_Resistor pull_resistor_9 (.node(pull_resistor_9_node));
  // _8_bit_Latch__LVC574 8_bit_latch_lvc574_1: pin names not known; wires that end beside it: pull_resistor_8_node, {pull_resistor_7_node, MULTIPLEXER}, CLK_B, {n8_bit_latch_lvc574_1_p4, SELECTOR_B[6], SELECTOR_B[4], SELECTOR_B[2], SELECTOR_B[0]}
  // _8_bit_Latch__LVC574 8_bit_latch_lvc574_2: pin names not known; wires that end beside it: pull_resistor_9_node, {n8_bit_latch_lvc574_1_p4, SELECTOR_B[6], SELECTOR_B[4], SELECTOR_B[2], SELECTOR_B[0]}, CLOCK_IN, {n8_bit_latch_lvc574_2_p4, SELECTOR_B[7], SELECTOR_B[5], SELECTOR_B[3], SELECTOR_B[1]}

  assign CLK = CLOCK_IN;

  // Other names for the same wires on the sheet: RESET_0 = RESET_0_B; RESET_1 = RESET_1_B; CLOCK_B = CLK_B;
  //   HALF_CLOCK = HCLK; HALF_CLOCK_B = HCLK_B; RSTB = SLOW_SELECTOR; SEL0 = SELECTOR_B[0]; SEL1 = SELECTOR_B[1];
  //   SEL2 = SELECTOR_B[2]; SEL3 = SELECTOR_B[3]; SEL4 = SELECTOR_B[4]; SEL5 = SELECTOR_B[5]; SEL6 = SELECTOR_B[6];
  //   SEL7 = SELECTOR_B[7]

  // Notes on the sheet:
  //   Debug Outputs
endmodule

module Clock_Generator (
  input  [3:0] SELECT_HIGH_SPEED_S0_3,
  input  [3:0] SELECT_LOW_SPEED_S0_3,
  input  CLOCK_IN,
  input  RESET,
  output CLOCK_OUT
);

  wire d_ff_1_qn, d_ff_2_qn, not_1_out, not_2_out, not_3_out, pull_resistor_1_node, pull_resistor_2_node,
       pull_resistor_3_node, pull_resistor_4_node, pull_resistor_7_node;
  wire [3:0] n4_bit_multiplexer_lvc157_1_p5, n4_bit_multiplexer_lvc157_2_p5;
  wire [7:1] d_ff_1_q;
  wire [7:6] pull_resistor_5_node;
  wire [11:0] n12_bit_up_counter_hc4040_2_p3;
  wire [11:1] n12_bit_up_counter_hc4040_1_p3;

  Pull_Resistor pull_resistor_1 (.node(pull_resistor_1_node));
  Pull_Resistor pull_resistor_2 (.node(pull_resistor_2_node));
  Pull_Resistor #(.pull(1)) pull_resistor_3 (.node(pull_resistor_3_node));
  // _4_bit_Multiplexer__LVC157 4_bit_multiplexer_lvc157_1: pin names not known; wires that end beside it: pull_resistor_1_node, pull_resistor_3_node, 4'b0111, SELECT_HIGH_SPEED_S0_3, n4_bit_multiplexer_lvc157_1_p5
  // _4_bit_Multiplexer__LVC157 4_bit_multiplexer_lvc157_2: pin names not known; wires that end beside it: pull_resistor_2_node, pull_resistor_3_node, 4'b0111, SELECT_LOW_SPEED_S0_3, n4_bit_multiplexer_lvc157_2_p5
  not not_1 (not_1_out, RESET);
  D_Flip_Flop d_ff_1 (
    .clk(CLOCK_IN), .D(d_ff_1_qn), .Q(d_ff_1_q[1]), .Qn(d_ff_1_qn), .reset(not_2_out));  // open: preset
  not not_2 (not_2_out, RESET);
  D_Flip_Flop d_ff_2 (
    .clk(d_ff_1_qn), .D(d_ff_2_qn), .Q(d_ff_1_q[2]), .Qn(d_ff_2_qn), .reset(not_3_out));  // open: preset
  not not_3 (not_3_out, RESET);
  // _12_bit_Up_Counter__HC4040 12_bit_up_counter_hc4040_1: pin names not known; wires that end beside it: not_1_out, d_ff_2_qn, {n12_bit_up_counter_hc4040_1_p3[11:8], d_ff_1_q[6], n12_bit_up_counter_hc4040_1_p3[6:5], d_ff_1_q[5], n12_bit_up_counter_hc4040_1_p3[3], d_ff_1_q[4], n12_bit_up_counter_hc4040_1_p3[1], d_ff_1_q[3]}
  // _12_bit_Up_Counter__HC4040 12_bit_up_counter_hc4040_2: pin names not known; wires that end beside it: not_1_out, n12_bit_up_counter_hc4040_1_p3[11], n12_bit_up_counter_hc4040_2_p3
  Pull_Resistor pull_resistor_4 (.node(pull_resistor_4_node));
  Pull_Resistor pull_resistor_5 (.node(pull_resistor_5_node[6]));
  Pull_Resistor #(.pull(1)) pull_resistor_6 (.node(pull_resistor_5_node[7]));
  // _8_to_1_Multiplexer__B3251 8_to_1_multiplexer_b3251_1: pin names not known; wires that end beside it: pull_resistor_4_node, n4_bit_multiplexer_lvc157_2_p5[2:0], {pull_resistor_5_node, n12_bit_up_counter_hc4040_2_p3[11], n12_bit_up_counter_hc4040_2_p3[9], n12_bit_up_counter_hc4040_2_p3[7], n12_bit_up_counter_hc4040_2_p3[4], n12_bit_up_counter_hc4040_2_p3[1], n12_bit_up_counter_hc4040_1_p3[10]}, d_ff_1_q[7]
  Pull_Resistor pull_resistor_7 (.node(pull_resistor_7_node));
  // _8_to_1_Multiplexer__B3251 8_to_1_multiplexer_b3251_2: pin names not known; wires that end beside it: pull_resistor_7_node, n4_bit_multiplexer_lvc157_1_p5[2:0], {d_ff_1_q, CLOCK_IN}, CLOCK_OUT
endmodule

module User_Mode_Memory_Glue (
  input  [7:0] USER_BANK,
  input  [23:0] ADDRESS_IN_A0_23,
  input  INTERNAL_MEMORY_VALID,
  input  READ_ENABLE,
  input  READ_BANK_REMAP_B,
  input  WRITE_ENABLE,
  output [16:0] ADDRESS_OUT_A0_16,
  output OEB,
  output WEB,
  output CEB
);

  wire and_1_out, and_2_out, not_1_out, not_2_out, pull_resistor_1_node;

  Pull_Resistor #(.pull(1)) pull_resistor_1 (.node(pull_resistor_1_node));
  not not_1 (not_1_out, READ_BANK_REMAP_B);
  and and_1 (and_1_out, INTERNAL_MEMORY_VALID, READ_ENABLE);
  and and_2 (and_2_out, INTERNAL_MEMORY_VALID, WRITE_ENABLE);
  // _4_bit_Line_Driver__LVC125 4_bit_line_driver_lvc125_1: pin names not known; wires that end beside it: READ_BANK_REMAP_B, not_1_out, pull_resistor_1_node, pull_resistor_1_node, 1'b1, ADDRESS_IN_A0_23[16], ADDRESS_OUT_A0_16[16], ADDRESS_OUT_A0_16[16]
  // _16_bit_Line_Driver__LVC16244 16_bit_line_driver_lvc16244_1: pin names not known; wires that end beside it: READ_BANK_REMAP_B, READ_BANK_REMAP_B, READ_BANK_REMAP_B, READ_BANK_REMAP_B, USER_BANK[7:4], USER_BANK[3:0], ADDRESS_IN_A0_23[23:20], ADDRESS_IN_A0_23[19:16], ADDRESS_OUT_A0_16[15:12], ADDRESS_OUT_A0_16[11:8], ADDRESS_OUT_A0_16[7:4], ADDRESS_OUT_A0_16[3:0]
  // _16_bit_Line_Driver__LVC16244 16_bit_line_driver_lvc16244_2: pin names not known; wires that end beside it: not_1_out, not_1_out, not_1_out, not_1_out, ADDRESS_IN_A0_23[15:12], ADDRESS_IN_A0_23[11:8], ADDRESS_IN_A0_23[7:4], ADDRESS_IN_A0_23[3:0], ADDRESS_OUT_A0_16[15:12], ADDRESS_OUT_A0_16[11:8], ADDRESS_OUT_A0_16[7:4], ADDRESS_OUT_A0_16[3:0]
  not not_2 (not_2_out, READ_BANK_REMAP_B);
  nor nor_1 (OEB, and_1_out, not_2_out);
  nand nand_1 (WEB, READ_BANK_REMAP_B, and_2_out);
  Pull_Resistor pull_resistor_2 (.node(CEB));
endmodule
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module Microcontroller_Testing (
  input  RESET
);

  wire BANK_LATCH, CLOCK_ENABLE_B, DATA_TRANSMIT_B, DEVICE_STROBE_B, DEVICE_VALID_B, ENTER_INTERRUPT,
       EXIT_INTERRUPT, FST, INTERNAL_MEMORY_VALID, IRQ_B, KERNAL_MODE, KERNAL_MODE_B, KERNAL_ROM_B,
       main_memory_gateway_1_memory_oeb_out, main_memory_gateway_1_memory_web_out, MAIN_MEMORY_VALID_B,
       MEMORY_LOCKOUT_CHANNEL_0, memory_transceiver_1_oe_b, memory_transceiver_1_we_b,
       microprocessor_w65c816_1_p6, microprocessor_w65c816_1_p13, microprocessor_w65c816_1_p14,
       microprocessor_w65c816_1_p15, MPU_LOCK_IN, n8_bit_bi_latch_lvc543_1_p5, n8_bit_bi_latch_lvc543_2_p5,
       n8_bit_comparator_f521_1_p4, n16_bit_latch_lvc16373_1_p7, n16_bit_latch_lvc16373_1_p8, NATIVE_MODE,
       NMI_B, NMIB_LOCKOUT_CHANNEL_0, nor_1_out, not_1_out, not_2_out, not_3_out, not_4_out, not_5_out,
       not_6_out, not_7_out, not_8_out, OPCODE_ADDRESS, or_1_out, or_2_out, or_3_out, or_4_out, or_5_out,
       or_6_out, PHI2, pull_resistor_5_node, pull_resistor_6_node, pull_resistor_10_node,
       pull_resistor_13_node, pull_resistor_14_node, pull_resistor_16_node, pull_resistor_17_node,
       pull_resistor_20_node, pull_resistor_21_node, pull_resistor_24_node, pull_resistor_25_node,
       pull_resistor_27_node, pull_resistor_28_node, quick_timing_circuit_1_clk,
       quick_timing_circuit_1_reset_1_b, RDY, READ_BANK_REMAP_B, READ_ENABLE, READ_ENABLE_B, READ_SELECTOR,
       RESET_t, ROM_ADDRESS_VALID, RWB, RWB_B, SA_FLAG_REGISTER_B, SA_INSTRUCTION_COUNTER_0,
       SA_INSTRUCTION_COUNTER_1, SA_INSTRUCTION_COUNTER_2, SA_INSTRUCTION_COUNTER_3,
       SA_INTERRUPTS_IN_DEPTH_B, SA_USER_PROGRAM_ID_B, SEL0, SEL2, SEL4, SEL6, selector_state_1_sel0,
       selector_state_1_sel1, selector_state_1_sel2, selector_state_1_sel3, selector_state_1_sel4,
       selector_state_1_sel5, selector_state_1_sel6, selector_state_1_sel7, SLW, SPECIAL_ADDRESS_VALID_B,
       STOP_SELECTOR, user_mode_memory_glue_1_ceb, user_mode_memory_glue_1_oeb, user_mode_memory_glue_1_web,
       VPB, WRITE_ENABLE, WRITE_ENABLE_B, WRITE_SELECTOR;
  wire [1:0] DEVICE_CHANNEL, n16_bit_line_driver_lvc16244_1_p8, pull_resistor_7_node;
  wire [3:0] DEVICE_ADDRESS, n2_to_4_decoder_lvc139_1_p4, n16_bit_line_driver_lvc16244_1_p10,
       pull_resistor_2_node, pull_resistor_8_node;
  wire [5:0] DEVICE_IDENTIFIER, n16_bit_line_driver_lvc16244_1_p9;
  wire [7:0] A0_7, A8_15, BA0_7, D, interrupt_detection_1_opcode, IRAM_A0_7, KERNAL_ROM_data,
       kernal_user_mode_1_interrupt_depth, main_memory_gateway_1_d_out_right,
       memory_transceiver_1_main_memory_d_out, microprocessor_w65c816_1_p10, MRAM_A16_23,
       n3_to_8_decoder_lvc138_1_p5, n8_bit_bus_transceiver_lvc4245_2_p4, pull_resistor_18_node,
       pull_resistor_22_node, pull_resistor_26_node, USER_PROGRAM_ID;
  wire [7:1] quick_timing_circuit_1_selector_b;
  wire [7:2] flags_register_1_flag_register;
  wire [8:0] pull_resistor_1_node;
  wire [11:3] address_decode_1_special_memory_selector_b;
  wire [16:0] user_mode_memory_glue_1_address_out_a0_16;
  wire [23:0] main_memory_gateway_1_maddress_out_a0_23, memory_transceiver_1_address_out_a0_23,
       pull_resistor_15_node, pull_resistor_19_node, pull_resistor_23_node;
  wire [31:0] instruction_counter_1_count;
  wire [39:0] T1, T2;

  Quick_Timing_Circuit quick_timing_circuit_1 (
    .SELECTOR_B({quick_timing_circuit_1_selector_b[7], SEL6, quick_timing_circuit_1_selector_b[5], SEL4, quick_timing_circuit_1_selector_b[3], SEL2, quick_timing_circuit_1_selector_b[1], SEL0}),
    .CLK(quick_timing_circuit_1_clk), .RESET_1_B(quick_timing_circuit_1_reset_1_b), .SLOW_SELECTOR(SLW),
    .RESET(RESET));  // open: MULTIPLEXER, COUNTER, CLK_B, HCLK, CLOCK_IN, RESET_0_B, HCLK_B
  // Probe on {BA0_7, A8_15, A0_7}
  not not_1 (not_1_out, PHI2);
  Pull_Resistor #(.pull(1)) pull_resistor_1 (.node(pull_resistor_1_node));
  Pull_Resistor #(.pull(1)) pull_resistor_2 (.node(pull_resistor_2_node));
  LED led_1 (.in(selector_state_1_sel0));
  // Probe on D
  LED led_2 (.in(selector_state_1_sel4));
  LED led_3 (.in(selector_state_1_sel2));
  LED led_4 (.in(selector_state_1_sel3));
  LED led_5 (.in(selector_state_1_sel1));
  Selector_State selector_state_1 (
    .RESET(quick_timing_circuit_1_reset_1_b), .PHI2(PHI2), .SEL1(selector_state_1_sel1),
    .SEL0(selector_state_1_sel0), .BOARD_RESET(RESET_t), .WRITE_SELECTOR(WRITE_SELECTOR),
    .DEVICE_STROBE_B(DEVICE_STROBE_B), .SEL3(selector_state_1_sel3), .BANK_LATCH(BANK_LATCH),
    .READ_SELECTOR(READ_SELECTOR), .CLOCK_ENABLE_B(CLOCK_ENABLE_B), .SEL2(selector_state_1_sel2),
    .READ_BANK_REMAP_B(READ_BANK_REMAP_B), .DATA_TRANSMIT_B(DATA_TRANSMIT_B), .SEL7(selector_state_1_sel7),
    .MPU_LOCK_IN(MPU_LOCK_IN), .SEL4(selector_state_1_sel4),
    .SELECTOR({quick_timing_circuit_1_selector_b[7], SEL6, quick_timing_circuit_1_selector_b[5], SEL4, quick_timing_circuit_1_selector_b[3], SEL2, quick_timing_circuit_1_selector_b[1], SEL0}),
    .SEL6(selector_state_1_sel6), .STOP_SELECTOR_B(STOP_SELECTOR), .SEL5(selector_state_1_sel5));
  Address_Decode address_decode_1 (
    .SPECIAL_VALID_B(SPECIAL_ADDRESS_VALID_B), .MAIN_MEMORY_VALID_B(MAIN_MEMORY_VALID_B),
    .DEVICE_VALID_B(DEVICE_VALID_B), .INTERNAL_MEMORY_VALID(INTERNAL_MEMORY_VALID),
    .DEVICE_CHANNEL(DEVICE_CHANNEL), .KERNAL_ROM_B(KERNAL_ROM_B), .ADDRESS_IN_A0_24({BA0_7, A8_15, A0_7}),
    .DEVICE_ADDRESS(DEVICE_ADDRESS), .RWB(RWB),
    .SPECIAL_MEMORY_SELECTOR_B({SA_INSTRUCTION_COUNTER_3, SA_INSTRUCTION_COUNTER_2, SA_INSTRUCTION_COUNTER_1, SA_INSTRUCTION_COUNTER_0, address_decode_1_special_memory_selector_b, SA_FLAG_REGISTER_B, SA_INTERRUPTS_IN_DEPTH_B, SA_USER_PROGRAM_ID_B}),
    .MPU_LOCK_IN(MPU_LOCK_IN), .ROM_VALID(ROM_ADDRESS_VALID), .KERNAL_MODE(KERNAL_MODE),
    .KERNAL_MODE_B(KERNAL_MODE_B), .DEVICE_IDENTIFIER(DEVICE_IDENTIFIER));
  Interrupt_Detection interrupt_detection_1 (
    .RESET_B(RESET_t), .LATCH_D(WRITE_SELECTOR), .RETURN_FROM_INTERRUPT(EXIT_INTERRUPT),
    .OPCODE(interrupt_detection_1_opcode), .ENTER_INTERRUPT(ENTER_INTERRUPT), .D(D),
    .OPCODE_ADDRESS(OPCODE_ADDRESS), .NATIVE_MODE(NATIVE_MODE), .ADDRESS_IN_A0(A0_7[0]), .PHI2_B(not_1_out));
  Interrupt_Vectoring interrupt_vectoring_1 (
    .ADDRESS_OUT_A0_7(IRAM_A0_7), .IRQ_4_B(pull_resistor_1_node[4]), .IRQ_1_B(pull_resistor_1_node[1]),
    .IRQ_B(IRQ_B), .NMI_2_B(pull_resistor_2_node[2]), .ADDRESS_IN_A0_7(A0_7),
    .NMI_0_B(pull_resistor_2_node[0]), .NMI_1_B(pull_resistor_2_node[1]), .IRQ_7_B(pull_resistor_1_node[7]),
    .IRQ_0_B(pull_resistor_1_node[0]), .IRQ_8_B(pull_resistor_1_node[8]), .NMI_3_B(pull_resistor_2_node[3]),
    .IRQ_5_B(pull_resistor_1_node[5]), .IRQ_6_B(pull_resistor_1_node[6]), .VPB(VPB),
    .IRQ_3_B(pull_resistor_1_node[3]), .NMI_B(NMI_B), .IRQ_2_B(pull_resistor_1_node[2]));
  LED led_6 (.in(selector_state_1_sel6));
  LED led_7 (.in(selector_state_1_sel5));
  LED led_8 (.in(selector_state_1_sel7));
  not not_2 (not_2_out, CLOCK_ENABLE_B);
  and and_1 (FST, not_2_out, quick_timing_circuit_1_clk);
  Counter #(.max('hffffffff), .width(32)) counter_1 (.clk(FST));  // open: load, D, count, Q, carry, up, clr
  // Probe on interrupt_detection_1_opcode
  or or_1 (or_1_out, RWB_B, SEL4);
  // Probe on D
  Pull_Resistor #(.pull(1)) pull_resistor_3 ();  // open: node
  or or_2 (or_2_out, DEVICE_VALID_B, SEL4);
  Pull_Resistor #(.pull(1)) pull_resistor_4 ();  // open: node
  Pull_Resistor #(.pull(1)) pull_resistor_5 (.node(pull_resistor_5_node));
  // _8_bit_Bi_latch__LVC543 8_bit_bi_latch_lvc543_1: pin names not known; wires that end beside it: RWB, RWB, SEL4, D, n8_bit_bi_latch_lvc543_1_p5, or_1_out, RWB_B, DEVICE_VALID_B
  // _16_bit_Line_Driver__LVC16244 16_bit_line_driver_lvc16244_1: pin names not known; wires that end beside it: SEL4, SEL4, SEL4, SEL4, {DEVICE_IDENTIFIER[5:4], WRITE_ENABLE_B, READ_ENABLE_B}, DEVICE_IDENTIFIER[3:0], DEVICE_ADDRESS, {n16_bit_line_driver_lvc16244_1_p9[5:4], n16_bit_line_driver_lvc16244_1_p8}, n16_bit_line_driver_lvc16244_1_p9[3:0], n16_bit_line_driver_lvc16244_1_p10
  // _2_to_4_Decoder__LVC139 2_to_4_decoder_lvc139_1: pin names not known; wires that end beside it: or_2_out, DEVICE_CHANNEL, pull_resistor_5_node, n2_to_4_decoder_lvc139_1_p4
  LED led_9 (.in(INTERNAL_MEMORY_VALID));
  LED led_10 (.in(SPECIAL_ADDRESS_VALID_B));
  LED led_11 (.in(DEVICE_VALID_B));
  LED led_12 (.in(ROM_ADDRESS_VALID));
  LED led_13 (.in(MAIN_MEMORY_VALID_B));
  Pull_Resistor #(.pull(1)) pull_resistor_6 (.node(pull_resistor_6_node));
  // Probe on n8_bit_bi_latch_lvc543_1_p5
  // Microprocessor__W65C816 microprocessor_w65c816_1: pin names not known; wires that end beside it: pull_resistor_6_node, IRQ_B, NMI_B, RESET_t, PHI2, microprocessor_w65c816_1_p6, T1, T2, {A8_15, A0_7}, microprocessor_w65c816_1_p10, RWB, RDY, microprocessor_w65c816_1_p13, microprocessor_w65c816_1_p14, microprocessor_w65c816_1_p15, FST, VPB
  Clock_Control clock_control_1 (
    .CLOCK_ENABLE_B(CLOCK_ENABLE_B), .RESET(RESET_t), .ROM_ADDRESS_VALID(ROM_ADDRESS_VALID), .RWB_B(RWB_B),
    .DEVICE_ADDRESS_VALID_B(DEVICE_VALID_B), .UNSTOPPABLE_CLOCK(STOP_SELECTOR));
  Flags_Register flags_register_1 (
    .SA_FLAG_REGISTER_B(SA_FLAG_REGISTER_B), .RESET(RESET_t), .WRITE_ENABLE_B(WRITE_ENABLE_B), .D_OUT(D),
    .FLAG_REGISTER({flags_register_1_flag_register, KERNAL_ROM_B, MPU_LOCK_IN}),
    .READ_ENABLE_B(READ_ENABLE_B), .D_IN(D));
  Pull_Resistor pull_resistor_7 (.node(pull_resistor_7_node));
  Pull_Resistor pull_resistor_8 (.node(pull_resistor_8_node));
  // Probe on {A8_15, A0_7}
  Pull_Resistor #(.pull(1)) pull_resistor_9 (.node(microprocessor_w65c816_1_p15));
  Pull_Resistor pull_resistor_10 (.node(pull_resistor_10_node));
  not not_3 (not_3_out, n2_to_4_decoder_lvc139_1_p4[0]);
  // Probe on microprocessor_w65c816_1_p10
  // Probe on {BA0_7, A8_15, IRAM_A0_7}
  // _8_bit_Bi_latch__LVC543 8_bit_bi_latch_lvc543_2: pin names not known; wires that end beside it: n16_bit_line_driver_lvc16244_1_p8[1], n16_bit_line_driver_lvc16244_1_p8[1], n2_to_4_decoder_lvc139_1_p4[0], n8_bit_bi_latch_lvc543_1_p5, n8_bit_bi_latch_lvc543_2_p5, n16_bit_line_driver_lvc16244_1_p8[0], n16_bit_line_driver_lvc16244_1_p8[0], n2_to_4_decoder_lvc139_1_p4[0]
  // _16_bit_Latch__LVC16373 16_bit_latch_lvc16373_1: pin names not known; wires that end beside it: pull_resistor_10_node, pull_resistor_10_node, {pull_resistor_7_node, n16_bit_line_driver_lvc16244_1_p9}, not_3_out, {pull_resistor_8_node, n16_bit_line_driver_lvc16244_1_p10}, not_3_out, n16_bit_latch_lvc16373_1_p7, n16_bit_latch_lvc16373_1_p8
  Signals signals_1 (
    .BA0_7(BA0_7), .VPA(microprocessor_w65c816_1_p14), .READ_SELECTOR(READ_SELECTOR),
    .CLOCK_ENABLE_B(CLOCK_ENABLE_B), .BANK_LATCH(BANK_LATCH), .OPCODE_ADDRESS(OPCODE_ADDRESS),
    .D(microprocessor_w65c816_1_p10), .RWB(RWB), .READ_ENABLE_B(READ_ENABLE_B),
    .WRITE_ENABLE_B(WRITE_ENABLE_B), .NATIVE_MODE(NATIVE_MODE), .READ_ENABLE(READ_ENABLE),
    .WRITE_SELECTOR(WRITE_SELECTOR), .RWB_B(RWB_B), .VDA(microprocessor_w65c816_1_p13),
    .E(microprocessor_w65c816_1_p6), .WRITE_ENABLE(WRITE_ENABLE));
  User_Mode_Memory_Glue user_mode_memory_glue_1 (
    .WRITE_ENABLE(WRITE_ENABLE), .OEB(user_mode_memory_glue_1_oeb), .READ_BANK_REMAP_B(READ_BANK_REMAP_B),
    .ADDRESS_OUT_A0_16(user_mode_memory_glue_1_address_out_a0_16), .USER_BANK(USER_PROGRAM_ID),
    .READ_ENABLE(READ_ENABLE), .ADDRESS_IN_A0_23({BA0_7, A8_15, IRAM_A0_7}),
    .WEB(user_mode_memory_glue_1_web), .CEB(user_mode_memory_glue_1_ceb),
    .INTERNAL_MEMORY_VALID(INTERNAL_MEMORY_VALID));
  // _8_bit_Bus_Transceiver__LVC4245 8_bit_bus_transceiver_lvc4245_1: pin names not known; wires that end beside it: DATA_TRANSMIT_B, microprocessor_w65c816_1_p10, RWB, D
  Pull_Resistor pull_resistor_11 (.node({A8_15, A0_7}));
  not not_4 (not_4_out, ROM_ADDRESS_VALID);
  or or_3 (or_3_out, not_4_out, READ_ENABLE_B);
  Pull_Resistor pull_resistor_12 (.node(D));
  // Probe on user_mode_memory_glue_1_address_out_a0_16
  RAM #(.enables("line"), .databus("bidir"), .\type ("nonvolatile"), .trigger("high"), .addrWidth(17)) INTERNAL_MEMORY (
    .addr(user_mode_memory_glue_1_address_out_a0_16), .data(D));  // open: we, oe, clk
  LED led_14 (.in(user_mode_memory_glue_1_oeb));
  SRAM_Chipifier sram_chipifier_1 (
    .CEB(user_mode_memory_glue_1_ceb), .OEB(user_mode_memory_glue_1_oeb), .WEB(user_mode_memory_glue_1_web));  // open: E, OE, WE
  LED led_15 (.in(user_mode_memory_glue_1_web));
  LED led_16 (.in(user_mode_memory_glue_1_ceb));
  // Probe on {A8_15[6:0], IRAM_A0_7}
  ROM #(.addrWidth(16)) KERNAL_ROM (.addr({1'b1, A8_15[6:0], IRAM_A0_7}), .data(KERNAL_ROM_data));
  not not_5 (not_5_out, or_3_out);
  LED led_17 (.in(or_3_out));
  // Probe on n8_bit_bi_latch_lvc543_2_p5
  // Probe on {BA0_7, A8_15, A0_7}
  // Probe on D
  Kernal_User_Mode kernal_user_mode_1 (
    .D_IN(D), .D_OUT(D), .RESET(RESET_t), .INTERRUPT_DEPTH(kernal_user_mode_1_interrupt_depth),
    .ENTER_INTERRUPT(ENTER_INTERRUPT), .KERNAL_MODE(KERNAL_MODE),
    .SA_INTERRUPTS_IN_DEPTH_B(SA_INTERRUPTS_IN_DEPTH_B), .USER(USER_PROGRAM_ID),
    .READ_ENABLE_B(READ_ENABLE_B), .KERNAL_MODE_B(KERNAL_MODE_B), .MAIN_MEMORY_BA0_7(MRAM_A16_23),
    .EXIT_INTERRUPT(EXIT_INTERRUPT), .BA0_7(BA0_7), .WRITE_ENABLE_B(WRITE_ENABLE_B),
    .SA_USER_PROGRAM_ID_B(SA_USER_PROGRAM_ID_B), .READ_BANK_REMAP_B(READ_BANK_REMAP_B));  // open: USER_MODE_ABILITY
  // Probe on n16_bit_latch_lvc16373_1_p7
  // Probe on n16_bit_latch_lvc16373_1_p8
  not not_6 (not_6_out, READ_BANK_REMAP_B);
  // Probe on D
  // Probe on D
  assign D = not_5_out ? KERNAL_ROM_data : 8'bz;  // Controlled_Buffer controlled_buffer_1
  // Probe on USER_PROGRAM_ID
  // Probe on MRAM_A16_23
  // Probe on kernal_user_mode_1_interrupt_depth
  or or_4 (or_4_out, READ_ENABLE_B, n8_bit_comparator_f521_1_p4);
  nor nor_1 (nor_1_out, WRITE_ENABLE_B, n8_bit_comparator_f521_1_p4);
  or or_5 (or_5_out, MAIN_MEMORY_VALID_B, not_6_out, DATA_TRANSMIT_B);
  // _8_bit_Comparator__F521 8_bit_comparator_f521_1: pin names not known; wires that end beside it: DEVICE_VALID_B, n16_bit_latch_lvc16373_1_p7, 8'h1, n8_bit_comparator_f521_1_p4
  // _8_bit_Bus_Transceiver__LVC4245 8_bit_bus_transceiver_lvc4245_2: pin names not known; wires that end beside it: or_5_out, D, RWB, n8_bit_bus_transceiver_lvc4245_2_p4
  // _8_bit_Latch__LVC573 8_bit_latch_lvc573_1: pin names not known; wires that end beside it: or_4_out, n8_bit_bi_latch_lvc543_2_p5, nor_1_out, n8_bit_bi_latch_lvc543_2_p5
  // Probe on n8_bit_bus_transceiver_lvc4245_2_p4
  Pull_Resistor #(.pull(1)) pull_resistor_13 (.node(pull_resistor_13_node));
  Pull_Resistor #(.pull(1)) pull_resistor_14 (.node(pull_resistor_14_node));
  // Probe on {MRAM_A16_23, A8_15, A0_7}
  not not_7 (not_7_out, PHI2);
  Memory_Transceiver memory_transceiver_1 (
    .MPU_D_IN(n8_bit_bus_transceiver_lvc4245_2_p4), .WE_B(memory_transceiver_1_we_b),
    .MAIN_MEMORY_D_OUT(memory_transceiver_1_main_memory_d_out), .RWB(RWB),
    .MEMORY_LOCKOUT(MEMORY_LOCKOUT_CHANNEL_0), .RWB_B(RWB_B),
    .ADDRESS_OUT_A0_23(memory_transceiver_1_address_out_a0_23),
    .ADDRESS_IN_A0_23({MRAM_A16_23, A8_15, A0_7}), .MAIN_MEMORY_VALID_B(MAIN_MEMORY_VALID_B),
    .MAIN_MEMORY_D_IN(memory_transceiver_1_main_memory_d_out), .OE_B(memory_transceiver_1_oe_b),
    .MPU_D_OUT(n8_bit_bus_transceiver_lvc4245_2_p4));
  Memory_Lockout_And_Generator memory_lockout_and_generator_1 (
    .SLOW_SELECTOR(SLW), .LOCKOUT(MEMORY_LOCKOUT_CHANNEL_0), .NMI_B(NMIB_LOCKOUT_CHANNEL_0),
    .WE_B(memory_transceiver_1_oe_b), .MAIN_MEMORY_VALID_3_B(pull_resistor_14_node), .GATEWAY_ENABLE_B(SEL0),
    .MAIN_MEMORY_VALID_2_B(pull_resistor_13_node),
    .ADDRESS_OUT_A0_23(memory_transceiver_1_address_out_a0_23), .MAIN_MEMORY_VALID_1_B(MAIN_MEMORY_VALID_B),
    .OE_B(memory_transceiver_1_we_b), .ADDRESS_IN_A0_23(24'h4aaaaa), .RESET(RESET_t));
  Instruction_Counter instruction_counter_1 (
    .RESET(RESET_t), .READ_ENABLE_B(READ_ENABLE_B), .A0(A0_7[0]), .OEB_C8_15(SA_INSTRUCTION_COUNTER_1),
    .PHI2_B(not_7_out), .D_OUT(D), .OEB_C0_7(SA_INSTRUCTION_COUNTER_0),
    .OEB_C24_31(SA_INSTRUCTION_COUNTER_3), .OEB_C16_23(SA_INSTRUCTION_COUNTER_2),
    .COUNT(instruction_counter_1_count), .OPCODE_ADDRESS(OPCODE_ADDRESS));
  // Probe on instruction_counter_1_count
  // Probe on memory_transceiver_1_address_out_a0_23
  // Probe on memory_transceiver_1_main_memory_d_out
  Pull_Resistor pull_resistor_15 (.node(pull_resistor_15_node));
  Pull_Resistor pull_resistor_16 (.node(pull_resistor_16_node));
  Pull_Resistor #(.pull(1)) pull_resistor_17 (.node(pull_resistor_17_node));
  Pull_Resistor pull_resistor_18 (.node(pull_resistor_18_node));
  Pull_Resistor pull_resistor_19 (.node(pull_resistor_19_node));
  Pull_Resistor pull_resistor_20 (.node(pull_resistor_20_node));
  Pull_Resistor #(.pull(1)) pull_resistor_21 (.node(pull_resistor_21_node));
  Pull_Resistor pull_resistor_22 (.node(pull_resistor_22_node));
  Pull_Resistor pull_resistor_23 (.node(pull_resistor_23_node));
  Pull_Resistor pull_resistor_24 (.node(pull_resistor_24_node));
  Pull_Resistor #(.pull(1)) pull_resistor_25 (.node(pull_resistor_25_node));
  Pull_Resistor pull_resistor_26 (.node(pull_resistor_26_node));
  Main_Memory_Gateway main_memory_gateway_1 (
    .MEMORY_OEB_IN(memory_transceiver_1_oe_b), .MEMORY_OEB_OUT(main_memory_gateway_1_memory_oeb_out),
    .D_IN_LEFT(memory_transceiver_1_main_memory_d_out), .MEMORY_WEB_IN(memory_transceiver_1_we_b),
    .GATEWAY_ENABLE_B(SEL6), .D_IN_RIGHT(main_memory_gateway_1_d_out_right),
    .MADDRESS_OUT_A0_23(main_memory_gateway_1_maddress_out_a0_23),
    .D_OUT_RIGHT(main_memory_gateway_1_d_out_right),
    .ADDRESS_IN_A0_23(memory_transceiver_1_address_out_a0_23),
    .D_OUT_LEFT(memory_transceiver_1_main_memory_d_out), .MEMORY_WEB_OUT(main_memory_gateway_1_memory_web_out));
  Main_Memory_Gateway main_memory_gateway_2 (
    .MEMORY_OEB_IN(pull_resistor_16_node), .MEMORY_OEB_OUT(main_memory_gateway_1_memory_oeb_out),
    .D_IN_LEFT(pull_resistor_18_node), .MEMORY_WEB_IN(pull_resistor_17_node), .GATEWAY_ENABLE_B(SEL0),
    .D_IN_RIGHT(main_memory_gateway_1_d_out_right),
    .MADDRESS_OUT_A0_23(main_memory_gateway_1_maddress_out_a0_23),
    .D_OUT_RIGHT(main_memory_gateway_1_d_out_right), .ADDRESS_IN_A0_23(pull_resistor_15_node),
    .D_OUT_LEFT(pull_resistor_18_node), .MEMORY_WEB_OUT(main_memory_gateway_1_memory_web_out));
  Main_Memory_Gateway main_memory_gateway_3 (
    .MEMORY_OEB_IN(pull_resistor_20_node), .MEMORY_OEB_OUT(main_memory_gateway_1_memory_oeb_out),
    .D_IN_LEFT(pull_resistor_22_node), .MEMORY_WEB_IN(pull_resistor_21_node), .GATEWAY_ENABLE_B(SEL2),
    .D_IN_RIGHT(main_memory_gateway_1_d_out_right),
    .MADDRESS_OUT_A0_23(main_memory_gateway_1_maddress_out_a0_23),
    .D_OUT_RIGHT(main_memory_gateway_1_d_out_right), .ADDRESS_IN_A0_23(pull_resistor_19_node),
    .D_OUT_LEFT(pull_resistor_22_node), .MEMORY_WEB_OUT(main_memory_gateway_1_memory_web_out));
  Main_Memory_Gateway main_memory_gateway_4 (
    .MEMORY_OEB_IN(pull_resistor_24_node), .MEMORY_OEB_OUT(main_memory_gateway_1_memory_oeb_out),
    .D_IN_LEFT(pull_resistor_26_node), .MEMORY_WEB_IN(pull_resistor_25_node), .GATEWAY_ENABLE_B(SEL4),
    .D_IN_RIGHT(main_memory_gateway_1_d_out_right),
    .MADDRESS_OUT_A0_23(main_memory_gateway_1_maddress_out_a0_23),
    .D_OUT_RIGHT(main_memory_gateway_1_d_out_right), .ADDRESS_IN_A0_23(pull_resistor_23_node),
    .D_OUT_LEFT(pull_resistor_26_node), .MEMORY_WEB_OUT(main_memory_gateway_1_memory_web_out));
  // Probe on main_memory_gateway_1_maddress_out_a0_23
  // Probe on main_memory_gateway_1_d_out_right
  Pull_Resistor pull_resistor_27 (.node(pull_resistor_27_node));
  Pull_Resistor #(.pull(1)) pull_resistor_28 (.node(pull_resistor_28_node));
  // _3_to_8_Decoder__LVC138 3_to_8_decoder_lvc138_1: pin names not known; wires that end beside it: pull_resistor_27_node, pull_resistor_27_node, main_memory_gateway_1_maddress_out_a0_23[23:21], pull_resistor_28_node, n3_to_8_decoder_lvc138_1_p5
  not not_8 (not_8_out, FST);
  or or_6 (or_6_out, main_memory_gateway_1_memory_web_out, not_8_out);
  // Probe on main_memory_gateway_1_maddress_out_a0_23[20:0]
  LED led_18 (.in(main_memory_gateway_1_memory_oeb_out));
  LED led_19 (.in(or_6_out));
  LED led_20 (.in(n3_to_8_decoder_lvc138_1_p5[2]));
  LED led_21 (.in(or_6_out));
  LED led_22 (.in(main_memory_gateway_1_memory_oeb_out));
  LED led_23 (.in(n3_to_8_decoder_lvc138_1_p5[3]));
  LED led_24 (.in(or_6_out));
  LED led_25 (.in(main_memory_gateway_1_memory_oeb_out));
  LED led_26 (.in(n3_to_8_decoder_lvc138_1_p5[4]));
  LED led_27 (.in(or_6_out));
  LED led_28 (.in(main_memory_gateway_1_memory_oeb_out));
  LED led_29 (.in(n3_to_8_decoder_lvc138_1_p5[5]));
  LED led_30 (.in(or_6_out));
  LED led_31 (.in(main_memory_gateway_1_memory_oeb_out));
  LED led_32 (.in(n3_to_8_decoder_lvc138_1_p5[6]));
  LED led_33 (.in(or_6_out));
  LED led_34 (.in(main_memory_gateway_1_memory_oeb_out));
  LED led_35 (.in(n3_to_8_decoder_lvc138_1_p5[7]));
  RAM #(.enables("line"), .databus("bidir"), .addrWidth(21), .\type ("nonvolatile"), .trigger("high")) ram_1 (
    .addr(main_memory_gateway_1_maddress_out_a0_23[20:0]), .data(main_memory_gateway_1_d_out_right));  // open: we, oe, clk
  SRAM_Chipifier sram_chipifier_2 (
    .CEB(n3_to_8_decoder_lvc138_1_p5[2]), .OEB(main_memory_gateway_1_memory_oeb_out), .WEB(or_6_out));  // open: E, OE, WE
  RAM #(.trigger("high"), .enables("line"), .addrWidth(21), .\type ("nonvolatile"), .databus("bidir")) ram_2 (
    .addr(main_memory_gateway_1_maddress_out_a0_23[20:0]), .data(main_memory_gateway_1_d_out_right));  // open: we, oe, clk
  SRAM_Chipifier sram_chipifier_3 (
    .CEB(n3_to_8_decoder_lvc138_1_p5[3]), .OEB(or_6_out), .WEB(main_memory_gateway_1_memory_oeb_out));  // open: E, OE, WE
  RAM #(.addrWidth(21), .trigger("high"), .enables("line"), .\type ("nonvolatile"), .databus("bidir")) ram_3 (
    .addr(main_memory_gateway_1_maddress_out_a0_23[20:0]), .data(main_memory_gateway_1_d_out_right));  // open: we, oe, clk
  SRAM_Chipifier sram_chipifier_4 (
    .CEB(n3_to_8_decoder_lvc138_1_p5[4]), .OEB(or_6_out), .WEB(main_memory_gateway_1_memory_oeb_out));  // open: E, OE, WE
  RAM #(.addrWidth(21), .databus("bidir"), .trigger("high"), .enables("line"), .\type ("nonvolatile")) ram_4 (
    .addr(main_memory_gateway_1_maddress_out_a0_23[20:0]), .data(main_memory_gateway_1_d_out_right));  // open: we, oe, clk
  SRAM_Chipifier sram_chipifier_5 (
    .CEB(n3_to_8_decoder_lvc138_1_p5[5]), .OEB(or_6_out), .WEB(main_memory_gateway_1_memory_oeb_out));  // open: E, OE, WE
  RAM #(.\type ("nonvolatile"), .enables("line"), .databus("bidir"), .addrWidth(21), .trigger("high")) ram_5 (
    .addr(main_memory_gateway_1_maddress_out_a0_23[20:0]), .data(main_memory_gateway_1_d_out_right));  // open: we, oe, clk
  SRAM_Chipifier sram_chipifier_6 (
    .CEB(n3_to_8_decoder_lvc138_1_p5[6]), .OEB(or_6_out), .WEB(main_memory_gateway_1_memory_oeb_out));  // open: E, OE, WE
  RAM #(.\type ("nonvolatile"), .trigger("high"), .enables("line"), .addrWidth(21), .databus("bidir")) ram_6 (
    .addr(main_memory_gateway_1_maddress_out_a0_23[20:0]), .data(main_memory_gateway_1_d_out_right));  // open: we, oe, clk
  SRAM_Chipifier sram_chipifier_7 (
    .CEB(n3_to_8_decoder_lvc138_1_p5[7]), .OEB(or_6_out), .WEB(main_memory_gateway_1_memory_oeb_out));  // open: E, OE, WE
  // Probe on main_memory_gateway_1_d_out_right
  // Probe on main_memory_gateway_1_d_out_right
  // Helper__W65C816_Timing helper_w65c816_timing_1: pin names not known; wires that end beside it: PHI2, 4'b0110, 4'b0001, 4'b0110, 4'b0100, 4'b0001, 4'b0101, 4'b0001, 4'b0110, 4'b0010, 4'b0110, FST, T1, 4'b0100, 4'b0000, 4'b0111, 4'b0000, 4'b0011, 4'b0111, 4'b0111, 4'b0000, 4'b0011, 4'b0000, T2

  // Notes on the sheet:
  //   Device Channel 0
  //   contents of KERNAL_ROM (hex, n*v repeats v):
  //   16384*0 ad fc ff c9 2b e1 f0 2 0 0 e2 20 a9 a4 8d 12 70 a9 cc ad 12 70 1a 8d 12 70 a9 cc ad 12 70 c9
  //   a5 f0 2 0 0 a2 ef cd 9b ae c 6f ac e 6f a9 ff 8d 0 6f a9 42 8f 0 ff 1 a9 43 8f 1 ff 1 a9 0 48 a9 4
  //   48 a9 1c 48 8 40 41184*ff 18 fb c2 30 a9 ff 1 1b e2 20 a9 0 48 ab c2 20 5c 0 40 0 8b b c2 30 48 da
  //   5a 80 39 8b b c2 30 48 da 5a 80 30 8b b c2 30 48 da 5a 80 27 8b b c2 30 48 da 5a e2 20 a9 0 48 ab ae
  //   c 6f ac e 6f 80 12 8b b c2 30 48 da 5a 80 9 8b b c2 30 48 da 5a 80 0 c2 30 7a fa 68 2b ab 40 7771*ff
  //   5a e1 6f e1 51 e1 48 e1 0 0 3f e1 4*ff 78 e1 0 0 78 e1 78 e1 2b e1 78 e1
  //   32KB_ROM
endmodule

module Device_Bus_Testing (
  input  RESET,
  input  [1:0] MPU_0_DEVICE_CHANNEL,
  input  MPU_0_DEVICE_VALID_B,
  input  [5:0] MPU_0_DEVICE_IDENTIFIER,
  input  [3:0] MPU_0_DEVICE_ADDRESS,
  input  MPU_0_RWB,
  input  [7:0] MPU_0_D_IN,
  input  [7:0] CH_0_D_IN,
  input  [1:0] MPU_1_DEVICE_CHANNEL,
  input  MPU_1_DEVICE_VALID_B,
  input  [5:0] MPU_1_DEVICE_IDENTIFIER,
  input  [3:0] MPU_1_DEVICE_ADDRESS,
  input  MPU_1_RWB,
  input  [7:0] MPU_1_D_IN,
  input  [7:0] CH_1_D_IN,
  input  [1:0] MPU_2_DEVICE_CHANNEL,
  input  MPU_2_DEVICE_VALID,
  input  [5:0] MPU_2_DEVICE_IDENTIFIER,
  input  [3:0] MPU_2_DEVICE_ADDRESS,
  input  FST,
  input  MPU_2_RWB,
  input  SEL_4,
  input  SEL_6,
  input  [7:0] MPU_2_D_IN,
  input  [7:0] CH_2_D_IN,
  input  SEL_0,
  input  SEL_2,
  input  [1:0] MPU_3_DEVICE_CHANNEL,
  input  MPU_3_DEVICE_VALID,
  input  [5:0] MPU_3_DEVICE_IDENTIFIER,
  input  [3:0] MPU_3_DEVICE_ADDRESS,
  input  MPU_3_RWB,
  input  [7:0] MPU_3_D_IN,
  input  [7:0] CH_3_D_IN,
  output [5:0] CH_0_DEVICE_IDENTIFIER,
  output [3:0] CH_0_DEVICE_ADDRESS,
  output CH_0_RWB_B,
  output CH_0_RWB,
  output [7:0] CH_0_D_OUT,
  output [7:0] MPU_0_D_OUT,
  output [5:0] CH_1_DEVICE_IDENTIFIER,
  output [3:0] CH_1_DEVICE_ADDRESS,
  output CH_1_RWB,
  output CH_1_RWB_B,
  output [7:0] CH_1_D_OUT,
  output [7:0] MPU_1_D_OUT,
  output [5:0] CH_2_DEVICE_IDENTIFIER,
  output [3:0] CH_2_DEVICE_ADDRESS,
  output CH_2_RWB,
  output CH_2_RWB_B,
  output [7:0] CH_2_D_OUT,
  output [7:0] MPU_2_D_OUT,
  output [5:0] CH_3_DEVICE_IDENTIFIER,
  output [3:0] CH_3_DEVICE_ADDRESS,
  output CH_3_RWB,
  output CH_3_RWB_B,
  output [7:0] CH_3_D_OUT,
  output [7:0] MPU_3_D_OUT
);

  wire decoder_1_out0, decoder_1_out1, decoder_1_out2, decoder_1_out3,
       device_mpu_gateway_1_channel_device_valid_b, device_mpu_gateway_1_channel_rwb,
       device_strobe_1_channel_0_b, device_strobe_1_channel_1_b, device_strobe_1_channel_2_b,
       device_strobe_1_channel_3_b, FST_t, SEL0, SEL2, SEL4, SEL6;
  wire [1:0] counter_1_q;
  wire [3:0] device_mpu_gateway_1_channel_device_address;
  wire [5:0] device_mpu_gateway_1_channel_device_identifier;
  wire [7:0] device_mpu_gateway_1_channel_d_out;

  Counter #(.max('h3), .width(2)) counter_1 (.Q(counter_1_q), .clk(FST_t));  // open: load, D, count, carry, up, clr
  Clock clock_1 (.out(FST_t));
  not not_1 (SEL4, decoder_1_out0);
  not not_2 (SEL6, decoder_1_out1);
  not not_3 (SEL0, decoder_1_out2);
  not not_4 (SEL2, decoder_1_out3);
  Decoder #(.select(2)) decoder_1 (
    .out0(decoder_1_out0), .out1(decoder_1_out1), .out2(decoder_1_out2), .out3(decoder_1_out3),
    .sel(counter_1_q));  // open: en
  LED led_1 (.in(MPU_0_DEVICE_VALID_B));
  LED led_2 (.in(MPU_1_DEVICE_VALID_B));
  LED led_3 (.in(MPU_2_DEVICE_VALID));
  LED led_4 (.in(MPU_3_DEVICE_VALID));
  Device_MPU_Gateway device_mpu_gateway_1 (
    .MPU_DEVICE_VALID_B(MPU_0_DEVICE_VALID_B), .CHANNEL_RWB(device_mpu_gateway_1_channel_rwb),
    .MPU_D_OUT(MPU_0_D_OUT), .MPU_D_IN(MPU_0_D_IN), .CHANNEL_D_IN(device_mpu_gateway_1_channel_d_out),
    .CHANNEL_DEVICE_VALID_B(device_mpu_gateway_1_channel_device_valid_b),
    .CHANNEL_DEVICE_IDENTIFIER(device_mpu_gateway_1_channel_device_identifier),
    .MPU_0_DEVICE_IDENTIFIER(MPU_0_DEVICE_IDENTIFIER),
    .CHANNEL_DEVICE_ADDRESS(device_mpu_gateway_1_channel_device_address), .SELECTOR_B(SEL4),
    .MPU_0_DEVICE_ADDRESS(MPU_0_DEVICE_ADDRESS), .MPU_RWB(MPU_0_RWB),
    .CHANNEL_D_OUT(device_mpu_gateway_1_channel_d_out));
  Device_MPU_Gateway device_mpu_gateway_2 (
    .MPU_DEVICE_VALID_B(MPU_1_DEVICE_VALID_B), .CHANNEL_RWB(device_mpu_gateway_1_channel_rwb),
    .MPU_D_OUT(MPU_1_D_OUT), .MPU_D_IN(MPU_1_D_IN), .CHANNEL_D_IN(device_mpu_gateway_1_channel_d_out),
    .CHANNEL_DEVICE_VALID_B(device_mpu_gateway_1_channel_device_valid_b),
    .CHANNEL_DEVICE_IDENTIFIER(device_mpu_gateway_1_channel_device_identifier),
    .MPU_0_DEVICE_IDENTIFIER(MPU_1_DEVICE_IDENTIFIER),
    .CHANNEL_DEVICE_ADDRESS(device_mpu_gateway_1_channel_device_address), .SELECTOR_B(SEL6),
    .MPU_0_DEVICE_ADDRESS(MPU_1_DEVICE_ADDRESS), .MPU_RWB(MPU_1_RWB),
    .CHANNEL_D_OUT(device_mpu_gateway_1_channel_d_out));
  Device_MPU_Gateway device_mpu_gateway_3 (
    .MPU_DEVICE_VALID_B(MPU_2_DEVICE_VALID), .CHANNEL_RWB(device_mpu_gateway_1_channel_rwb),
    .MPU_D_OUT(MPU_2_D_OUT), .MPU_D_IN(MPU_2_D_IN), .CHANNEL_D_IN(device_mpu_gateway_1_channel_d_out),
    .CHANNEL_DEVICE_VALID_B(device_mpu_gateway_1_channel_device_valid_b),
    .CHANNEL_DEVICE_IDENTIFIER(device_mpu_gateway_1_channel_device_identifier),
    .MPU_0_DEVICE_IDENTIFIER(MPU_2_DEVICE_IDENTIFIER),
    .CHANNEL_DEVICE_ADDRESS(device_mpu_gateway_1_channel_device_address), .SELECTOR_B(SEL0),
    .MPU_0_DEVICE_ADDRESS(MPU_2_DEVICE_ADDRESS), .MPU_RWB(MPU_2_RWB),
    .CHANNEL_D_OUT(device_mpu_gateway_1_channel_d_out));
  Device_MPU_Gateway device_mpu_gateway_4 (
    .MPU_DEVICE_VALID_B(MPU_3_DEVICE_VALID), .CHANNEL_RWB(device_mpu_gateway_1_channel_rwb),
    .MPU_D_OUT(MPU_3_D_OUT), .MPU_D_IN(MPU_3_D_IN), .CHANNEL_D_IN(device_mpu_gateway_1_channel_d_out),
    .CHANNEL_DEVICE_VALID_B(device_mpu_gateway_1_channel_device_valid_b),
    .CHANNEL_DEVICE_IDENTIFIER(device_mpu_gateway_1_channel_device_identifier),
    .MPU_0_DEVICE_IDENTIFIER(MPU_3_DEVICE_IDENTIFIER),
    .CHANNEL_DEVICE_ADDRESS(device_mpu_gateway_1_channel_device_address), .SELECTOR_B(SEL2),
    .MPU_0_DEVICE_ADDRESS(MPU_3_DEVICE_ADDRESS), .MPU_RWB(MPU_3_RWB),
    .CHANNEL_D_OUT(device_mpu_gateway_1_channel_d_out));
  Device_Strobe device_strobe_1 (
    .Channel_2_B(device_strobe_1_channel_2_b), .DEVICE_0_VALID_B(MPU_0_DEVICE_VALID_B),
    .Channel_3_B(device_strobe_1_channel_3_b), .CHANNEL_1_NUMBER(MPU_1_DEVICE_CHANNEL),
    .Channel_0_B(device_strobe_1_channel_0_b), .CHANNEL_0_NUMBER(MPU_0_DEVICE_CHANNEL),
    .DEVICE_1_VALID_B(MPU_1_DEVICE_VALID_B), .SELECTOR_0_B(SEL4), .Channel_1_B(device_strobe_1_channel_1_b),
    .RESET(RESET), .SELECTOR_1_B(SEL6));
  Device_Strobe device_strobe_2 (
    .Channel_2_B(device_strobe_1_channel_2_b), .DEVICE_0_VALID_B(MPU_2_DEVICE_VALID),
    .Channel_3_B(device_strobe_1_channel_3_b), .CHANNEL_1_NUMBER(MPU_3_DEVICE_CHANNEL),
    .Channel_0_B(device_strobe_1_channel_0_b), .CHANNEL_0_NUMBER(MPU_2_DEVICE_CHANNEL),
    .DEVICE_1_VALID_B(MPU_3_DEVICE_VALID), .SELECTOR_0_B(SEL0), .Channel_1_B(device_strobe_1_channel_1_b),
    .RESET(RESET), .SELECTOR_1_B(SEL2));
  // Probe on device_mpu_gateway_1_channel_d_out
  // Probe on device_mpu_gateway_1_channel_d_out
  // Probe on device_mpu_gateway_1_channel_d_out
  // Probe on device_mpu_gateway_1_channel_d_out
  Device_Channel_Gateway device_channel_gateway_1 (
    .MPU_DEVICE_ADDRESS(device_mpu_gateway_1_channel_device_address), .CHANNEL_RWB(CH_0_RWB_B),
    .CHANNEL_RWB_B(CH_0_RWB), .MPU_DEVICE_IDENTIFIER(device_mpu_gateway_1_channel_device_identifier),
    .CHANNEL_DEVICE_ADDRESS(CH_0_DEVICE_ADDRESS), .FST(FST_t), .CHANNEL_D_OUT(CH_0_D_OUT),
    .MPU_RWB(device_mpu_gateway_1_channel_rwb), .CHANNEL_DEVICE_IDENTIFIER(CH_0_DEVICE_IDENTIFIER),
    .MPU_D_IN(device_mpu_gateway_1_channel_d_out), .SELECTOR_B(device_strobe_1_channel_0_b),
    .MPU_DEVICE_VALID_B(device_mpu_gateway_1_channel_device_valid_b), .CHANNEL_D_IN(CH_0_D_IN),
    .MPU_D_OUT(device_mpu_gateway_1_channel_d_out));
  Device_Channel_Gateway device_channel_gateway_2 (
    .MPU_DEVICE_ADDRESS(device_mpu_gateway_1_channel_device_address), .CHANNEL_RWB(CH_1_RWB),
    .CHANNEL_RWB_B(CH_1_RWB_B), .MPU_DEVICE_IDENTIFIER(device_mpu_gateway_1_channel_device_identifier),
    .CHANNEL_DEVICE_ADDRESS(CH_1_DEVICE_ADDRESS), .FST(FST_t), .CHANNEL_D_OUT(CH_1_D_OUT),
    .MPU_RWB(device_mpu_gateway_1_channel_rwb), .CHANNEL_DEVICE_IDENTIFIER(CH_1_DEVICE_IDENTIFIER),
    .MPU_D_IN(device_mpu_gateway_1_channel_d_out), .SELECTOR_B(device_strobe_1_channel_1_b),
    .MPU_DEVICE_VALID_B(device_mpu_gateway_1_channel_device_valid_b), .CHANNEL_D_IN(CH_1_D_IN),
    .MPU_D_OUT(device_mpu_gateway_1_channel_d_out));
  Device_Channel_Gateway device_channel_gateway_3 (
    .MPU_DEVICE_ADDRESS(device_mpu_gateway_1_channel_device_address), .CHANNEL_RWB(CH_2_RWB),
    .CHANNEL_RWB_B(CH_2_RWB_B), .MPU_DEVICE_IDENTIFIER(device_mpu_gateway_1_channel_device_identifier),
    .CHANNEL_DEVICE_ADDRESS(CH_2_DEVICE_ADDRESS), .FST(FST_t), .CHANNEL_D_OUT(CH_2_D_OUT),
    .MPU_RWB(device_mpu_gateway_1_channel_rwb), .CHANNEL_DEVICE_IDENTIFIER(CH_2_DEVICE_IDENTIFIER),
    .MPU_D_IN(device_mpu_gateway_1_channel_d_out), .SELECTOR_B(device_strobe_1_channel_2_b),
    .MPU_DEVICE_VALID_B(device_mpu_gateway_1_channel_device_valid_b), .CHANNEL_D_IN(CH_2_D_IN),
    .MPU_D_OUT(device_mpu_gateway_1_channel_d_out));
  Device_Channel_Gateway device_channel_gateway_4 (
    .MPU_DEVICE_ADDRESS(device_mpu_gateway_1_channel_device_address), .CHANNEL_RWB(CH_3_RWB),
    .CHANNEL_RWB_B(CH_3_RWB_B), .MPU_DEVICE_IDENTIFIER(device_mpu_gateway_1_channel_device_identifier),
    .CHANNEL_DEVICE_ADDRESS(CH_3_DEVICE_ADDRESS), .FST(FST_t), .CHANNEL_D_OUT(CH_3_D_OUT),
    .MPU_RWB(device_mpu_gateway_1_channel_rwb), .CHANNEL_DEVICE_IDENTIFIER(CH_3_DEVICE_IDENTIFIER),
    .MPU_D_IN(device_mpu_gateway_1_channel_d_out), .SELECTOR_B(device_strobe_1_channel_3_b),
    .MPU_DEVICE_VALID_B(device_mpu_gateway_1_channel_device_valid_b), .CHANNEL_D_IN(CH_3_D_IN),
    .MPU_D_OUT(device_mpu_gateway_1_channel_d_out));
endmodule

module SRAM_Chipifier (
  input  OEB,
  input  WEB,
  input  CEB,
  output OE,
  output WE,
  output E
);

  nor nor_1 (OE, OEB, CEB);
  nor nor_2 (WE, WEB, CEB);
  Pull_Resistor #(.pull(1)) pull_resistor_1 (.node(E));
endmodule

module Bidirectional_Monsters (
  input  RWB,
  input  ENABLE_B,
  output READ,
  output WRITE
);

  wire not_1_out, not_2_out;

  and and_1 (READ, RWB, not_1_out);
  not not_1 (not_1_out, ENABLE_B);
  and and_2 (WRITE, not_2_out, not_1_out);
  not not_2 (not_2_out, RWB);
endmodule

module Parallel_To_SPI (
  input  CLK,
  input  LOAD_HIGH_B,
  input  LOAD_LOW_B,
  input  [7:0] D
);

  wire d_ff_1_qn, n8_bit_down_counter_hct40103_1_p7, n8_bit_line_driver_lvc541_1_p4,
       n8_bit_parallel_in_shift_lv165_1_p1, n8_bit_parallel_in_shift_lv165_1_p6,
       n8_bit_parallel_in_shift_lv165_2_p6, not_1_out, not_2_out, not_3_out, or_1_out, pull_resistor_1_node,
       pull_resistor_2_node, pull_resistor_3_node;

  Pull_Resistor #(.pull(1)) pull_resistor_1 (.node(pull_resistor_1_node));
  Pull_Resistor #(.pull(1)) pull_resistor_2 (.node(pull_resistor_2_node));
  not not_1 (not_1_out, CLK);
  Pull_Resistor pull_resistor_3 (.node(pull_resistor_3_node));
  D_Flip_Flop d_ff_1 (.Qn(d_ff_1_qn), .preset(not_2_out), .reset(not_3_out));  // open: clk, D, Q
  not not_2 (not_2_out, LOAD_HIGH_B);
  not not_3 (not_3_out, n8_bit_down_counter_hct40103_1_p7);
  // _8_bit_Line_Driver__LVC541 8_bit_line_driver_lvc541_1: pin names not known; wires that end beside it: LOAD_HIGH_B, LOAD_HIGH_B, 8'h10, n8_bit_line_driver_lvc541_1_p4
  // _8_bit_Down_Counter__HCT40103 8_bit_down_counter_hct40103_1: pin names not known; wires that end beside it: pull_resistor_1_node, pull_resistor_2_node, LOAD_HIGH_B, d_ff_1_qn, CLK, n8_bit_line_driver_lvc541_1_p4, n8_bit_down_counter_hct40103_1_p7
  // _8_bit_parallel_in_shift__LV165 8_bit_parallel_in_shift_lv165_1: pin names not known; wires that end beside it: n8_bit_parallel_in_shift_lv165_1_p1, LOAD_HIGH_B, not_1_out, D, pull_resistor_3_node, n8_bit_parallel_in_shift_lv165_1_p6
  // _8_bit_parallel_in_shift__LV165 8_bit_parallel_in_shift_lv165_2: pin names not known; wires that end beside it: n8_bit_parallel_in_shift_lv165_1_p1, LOAD_LOW_B, not_1_out, D, n8_bit_parallel_in_shift_lv165_1_p6, n8_bit_parallel_in_shift_lv165_2_p6
  // Probe on n8_bit_line_driver_lvc541_1_p4
  not not_4 (n8_bit_parallel_in_shift_lv165_1_p1, n8_bit_down_counter_hct40103_1_p7);
  // Probe on or_1_out
  or or_1 (or_1_out, n8_bit_down_counter_hct40103_1_p7, n8_bit_parallel_in_shift_lv165_2_p6);
endmodule
